// Logisim project pre1.circ as structural Verilog: 1 circuit, main circuit main
module main (
);

  wire button_1_out, button_2_out, button_3_out, button_4_out, clock_1_out, d_ff_1_q, d_ff_1_qn, d_ff_2_q,
       d_ff_2_qn, d_ff_3_q, d_ff_3_qn, nand_1_out;

  Button button_1 (.out(button_1_out));
  Button button_2 (.out(button_2_out));
  Button button_3 (.out(button_3_out));
  Button button_4 (.out(button_4_out));
  D_Flip_Flop d_ff_1 (
    .clk(nand_1_out), .D(button_1_out), .Q(d_ff_1_q), .Qn(d_ff_1_qn), .reset(button_4_out));  // open: preset, en
  D_Flip_Flop d_ff_2 (
    .clk(nand_1_out), .D(button_2_out), .Q(d_ff_2_q), .Qn(d_ff_2_qn), .reset(button_4_out));  // open: preset, en
  D_Flip_Flop d_ff_3 (
    .clk(nand_1_out), .D(button_3_out), .Q(d_ff_3_q), .Qn(d_ff_3_qn), .reset(button_4_out));  // open: preset, en
  LED led_1 (.in(d_ff_1_q));
  LED led_2 (.in(d_ff_2_q));
  LED led_3 (.in(d_ff_3_q));
  Clock clock_1 (.out(clock_1_out));
  nand nand_1 (nand_1_out, d_ff_1_qn, d_ff_2_qn, d_ff_3_qn, clock_1_out);
endmodule
