// Logisim project test1.circ as structural Verilog: 1 circuit, main circuit test1
module test1 (
  input  A,
  input  B,
  input  C,
  input  D,
  output out_5
);

  wire and_1_out, and_2_out, not_1_out;

  not not_1 (not_1_out, A);
  and and_1 (and_1_out, not_1_out, B);
  and and_2 (and_2_out, A, D);
  or or_1 (out_5, and_1_out, C, and_2_out);
endmodule
