// Logisim project test3version1.circ as structural Verilog: 3 circuits, main circuit 2nmod5
module _2nmod5 (
  input  In,
  output [2:0] out_2
);

  wire clock_1_out;
  wire [2:0] input_out_3, register_1_q;

  // Probe on input_out_3
  \input  \input  (.in_1(register_1_q), .\input (In), .out_3(input_out_3));
  Clock #(.highDuration(5), .lowDuration(5)) clock_1 (.out(clock_1_out));
  // Probe on register_1_q
  Register #(.width(3)) register_1 (.D(input_out_3), .Q(register_1_q), .clk(clock_1_out));  // open: en, clr
  \output  \output  (.in_1(register_1_q), .in_2(In), .out_3(out_2));
endmodule

module \input  (
  input  [2:0] in_1,
  input  \input ,
  output [2:0] out_3
);

  wire and_2_out, and_3_out, and_4_out, and_5_out, not_1_out, not_2_out, not_3_out, not_4_out, not_5_out;

  not not_1 (not_1_out, in_1[0]);
  not not_2 (not_2_out, \input );
  not not_3 (not_3_out, in_1[1]);
  not not_4 (not_4_out, in_1[1]);
  not not_5 (not_5_out, \input );
  and and_1 (out_3[2], in_1[1], not_1_out, not_2_out);
  and and_2 (and_2_out, not_3_out, in_1[0]);
  and and_3 (and_3_out, in_1[0], \input );
  and and_4 (and_4_out, not_4_out, \input );
  and and_5 (and_5_out, in_1[1], in_1[0], not_5_out);
  or or_1 (out_3[1], and_2_out, and_3_out);
  or or_2 (out_3[0], and_4_out, and_5_out);
endmodule

module \output  (
  input  [2:0] in_1,
  input  in_2,
  output [2:0] out_3
);

  wire [2:0] undriven;

  Multiplexer #(.select(3), .width(3)) multiplexer_1 (
    .in0(3'b001), .in1(3'b010), .in2(3'b100), .in3(3'b011), .in4(3'b001), .out(out_3), .sel(undriven));  // open: in5, in6, in7, en
endmodule
