// Logisim project test4.circ as structural Verilog: 1 circuit, main circuit check
module check (
  input  [8:0] in_1,
  output [7:0] out_2
);

  wire adder_1_out, adder_2_out, adder_3_out, adder_4_out, adder_5_out, adder_6_out, adder_7_out, xor_1_out;

  Adder #(.width(1)) adder_1 (.a(in_1[1]), .b(in_1[2]), .out(adder_1_out));  // open: cin, cout
  Adder #(.width(1)) adder_2 (.a(adder_1_out), .b(in_1[3]), .out(adder_2_out));  // open: cin, cout
  Adder #(.width(1)) adder_3 (.a(adder_2_out), .b(in_1[4]), .out(adder_3_out));  // open: cin, cout
  Adder #(.width(1)) adder_4 (.a(adder_3_out), .b(in_1[5]), .out(adder_4_out));  // open: cin, cout
  Adder #(.width(1)) adder_5 (.a(adder_4_out), .b(in_1[6]), .out(adder_5_out));  // open: cin, cout
  Adder #(.width(1)) adder_6 (.a(adder_5_out), .b(in_1[7]), .out(adder_6_out));  // open: cin, cout
  Adder #(.width(1)) adder_7 (.a(adder_6_out), .b(in_1[8]), .out(adder_7_out));  // open: cin, cout
  xor xor_1 (xor_1_out, in_1[0], adder_7_out);
  Multiplexer #(.width(8)) multiplexer_1 (.in0(in_1[8:1]), .in1({8{1'b1}}), .out(out_2), .sel(xor_1_out));  // open: en
endmodule
