// Logisim project test5.circ as structural Verilog: 2 circuits, main circuit sort
module sort (
  input  [3:0] in_1,
  input  [3:0] in_2,
  input  [3:0] in_3,
  input  [3:0] in_4,
  output [3:0] out_5,
  output [3:0] out_6,
  output [3:0] out_7,
  output [3:0] out_8
);

  wire [3:0] swap_1_o1, swap_1_o2, swap_2_o1, swap_2_o2, swap_3_o2, swap_4_o1;

  swap swap_1 (.i1(in_1), .i2(in_2), .o1(swap_1_o1), .o2(swap_1_o2));
  swap swap_2 (.i1(in_3), .i2(in_4), .o1(swap_2_o1), .o2(swap_2_o2));
  swap swap_3 (.i1(swap_1_o1), .i2(swap_2_o1), .o1(out_5), .o2(swap_3_o2));
  swap swap_4 (.i1(swap_1_o2), .i2(swap_2_o2), .o1(swap_4_o1), .o2(out_8));
  swap swap_5 (.i1(swap_3_o2), .i2(swap_4_o1), .o1(out_6), .o2(out_7));
endmodule

module swap (
  input  [3:0] i1,
  input  [3:0] i2,
  output [3:0] o1,
  output [3:0] o2
);

  wire comparator_1_lt, multiplexer_1_out;
  wire [3:0] and_1_out, and_2_out, and_3_out, and_4_out, bit_extender_1_out, not_1_out, not_2_out;

  Comparator #(.width(4), .mode("unsigned")) comparator_1 (.a(i1), .b(i2), .lt(comparator_1_lt));  // open: gt, eq
  Multiplexer multiplexer_1 (.in0(1'b0), .in1(1'b1), .out(multiplexer_1_out), .sel(comparator_1_lt));  // open: en
  assign bit_extender_1_out = {{3{multiplexer_1_out}}, comparator_1_lt};  // Bit_Extender bit_extender_1
  assign not_1_out = ~bit_extender_1_out;  // NOT_Gate not_1, 4 bits wide
  assign not_2_out = ~bit_extender_1_out;  // NOT_Gate not_2, 4 bits wide
  assign and_1_out = not_1_out & i1;  // AND_Gate and_1, 4 bits wide
  assign and_2_out = bit_extender_1_out & i2;  // AND_Gate and_2, 4 bits wide
  assign and_3_out = not_2_out & i2;  // AND_Gate and_3, 4 bits wide
  assign and_4_out = bit_extender_1_out & i1;  // AND_Gate and_4, 4 bits wide
  assign o1 = and_1_out | and_2_out;  // OR_Gate or_1, 4 bits wide
  assign o2 = and_3_out | and_4_out;  // OR_Gate or_2, 4 bits wide

  // Notes on the sheet:
  //   比较大小的转换
  //   swap电路
endmodule
