// Logisim project CPU12.circ as structural Verilog: 8 circuits, main circuit main
module main (
  input  in_1,
  output [31:0] out_2,
  output out_3,
  output [4:0] out_4,
  output [31:0] out_5,
  output out_6,
  output [4:0] out_7,
  output [31:0] out_8
);

  wire ALU_zero, ALUSrc, branch, clk, MemRead, MemtoReg, PCSel, PCSrc_out, RegDst;
  wire [1:0] ALUop, EXTop;
  wire [3:0] high4;
  wire [4:0] splitter_out_4, splitter_out_5, splitter_out_6;
  wire [5:0] Func, Op;
  wire [15:0] splitter_out_8;
  wire [25:0] splitter_out_9;
  wire [27:0] adder_1_out, bit_extender_1_out, jumpAddr;
  wire [31:0] adder_2_out, ALU_out_5, ext_1_out_3, GRF_rd1, multiplexer_2_out, multiplexer_3_out,
       multiplexer_4_out, ram_1_data, register_1_q, shifter_2_out;

  Register #(.width(32)) register_1 (.D(multiplexer_4_out), .Q(register_1_q), .clk(clk), .clr(in_1));  // open: en
  Clock clock_1 (.out(clk));
  Adder #(.width(32)) adder_1 (.a(register_1_q), .b(32'h4), .out({high4, adder_1_out}));  // open: cin, cout
  ROM #(.addrWidth(5), .dataWidth(32)) rom_1 (.addr(register_1_q[6:2]), .data(out_2));  // open: sel
  splitter splitter (
    .in_1(out_2), .out_2(Func), .out_4(splitter_out_4), .out_5(splitter_out_5), .out_6(splitter_out_6),
    .out_7(Op), .out_8(splitter_out_8), .out_9(splitter_out_9));  // open: out_3
  assign bit_extender_1_out = {{2{1'b0}}, splitter_out_9};  // Bit_Extender bit_extender_1
  Controller controller_1 (
    .Op(Op), .func(Func), .RegDst(RegDst), .ALUSrc(ALUSrc), .MemtoReg(MemtoReg), .RegWrite(out_3),
    .MemRead(MemRead), .MemWrite(out_6), .branch(branch), .PCSel(PCSel), .ALUop(ALUop), .EXTop(EXTop));
  Multiplexer #(.width(5), .enable("false")) multiplexer_1 (
    .in0(splitter_out_5), .in1(splitter_out_4), .out(out_4), .sel(RegDst));
  EXT ext_1 (.in_1(splitter_out_8), .out_3(ext_1_out_3), .in_2(EXTop));
  Shifter #(.width(28)) shifter_1 (.in(bit_extender_1_out), .\dist (5'b00010), .out(jumpAddr));
  GRF GRF (
    .A1(splitter_out_6), .A2(splitter_out_5), .A3(out_4), .WD(out_5), .RD1(GRF_rd1), .RD2(out_8), .clk(clk),
    .reset(in_1), .we(out_3));
  ALU ALU (
    .in_1(GRF_rd1), .in_2(multiplexer_2_out), .ALUOP(ALUop), .Zero(ALU_zero),
    .out_5({ALU_out_5[31:7], out_7, ALU_out_5[1:0]}));
  Multiplexer #(.width(32), .enable("false")) multiplexer_2 (
    .in0(out_8), .in1(ext_1_out_3), .out(multiplexer_2_out), .sel(ALUSrc));
  Adder #(.width(32)) adder_2 (.a({high4, adder_1_out}), .b(shifter_2_out), .out(adder_2_out));  // open: cin, cout
  Shifter #(.width(32)) shifter_2 (.in(ext_1_out_3), .\dist (5'b00010), .out(shifter_2_out));
  Multiplexer #(.width(32), .enable("false")) multiplexer_3 (
    .in0({high4, adder_1_out}), .in1(adder_2_out), .out(multiplexer_3_out), .sel(PCSrc_out));
  and PCSrc (PCSrc_out, branch, ALU_zero);
  Multiplexer #(.width(32), .enable("false")) multiplexer_4 (
    .in0(multiplexer_3_out), .in1({high4, jumpAddr}), .out(multiplexer_4_out), .sel(PCSel));
  RAM #(.addrWidth(5), .dataWidth(32), .bus("separate")) ram_1 (
    .addr(out_7), .din(out_8), .data(ram_1_data), .str(out_6), .clk(clk), .ld(MemRead), .clr(in_1));  // open: sel
  Multiplexer #(.width(32), .enable("false")) multiplexer_5 (
    .in0(ram_1_data), .in1({ALU_out_5[31:7], out_7, ALU_out_5[1:0]}), .out(out_5), .sel(MemtoReg));

  // Other names for the same wires on the sheet: MemAddr[4:0] = out_7; instr[31:0] = out_2; jumpAddr[31:28] = high4;
  //   MemData[31:0] = out_8; MemWrite = out_6; RegAddr[4:0] = out_4; RegData[31:0] = out_5; RegWrite = out_3;
  //   reset = in_1

  // Notes on the sheet:
  //   源地址
  //   分支地址 16immm
  //   (PC+4)+EXT
  //   跳转地址26位
endmodule

module splitter (
  input  [31:0] in_1,
  output [5:0] out_2,
  output [4:0] out_3,
  output [4:0] out_4,
  output [4:0] out_5,
  output [4:0] out_6,
  output [5:0] out_7,
  output [15:0] out_8,
  output [25:0] out_9
);


  assign out_2 = in_1[5:0];
  assign out_3 = in_1[10:6];
  assign out_4 = in_1[15:11];
  assign out_5 = in_1[20:16];
  assign out_6 = in_1[25:21];
  assign out_7 = in_1[31:26];
  assign out_8 = in_1[15:0];
  assign out_9 = in_1[25:0];

  // Notes on the sheet:
  //   Func 0-6
  //   Shamt 6-10
  //   Rt 16-20
  //   Rd 11-15
  //   Rs 21-25
  //   Op 26-31
  //   16bit Immediate
  //   26 bir address for jump
endmodule

module IFU (
  input  clk,
  input  reset,
  input  [31:0] beq_imm,
  input  branch_op,
  input  [31:0] j_jal_imm,
  input  jump_op,
  output [31:0] PC_4,
  output [31:0] out_8
);

  wire [31:0] adder_2_out, multiplexer_1_out, multiplexer_2_out, register_1_q;

  Register #(.width(32)) register_1 (.D(multiplexer_2_out), .Q(register_1_q), .clk(clk), .clr(reset));  // open: en
  ROM #(.addrWidth(5), .dataWidth(32)) rom_1 (.addr(register_1_q[4:0]), .data(out_8));  // open: sel
  Adder #(.width(32)) adder_1 (.a(register_1_q), .b(32'h4), .out(PC_4));  // open: cin, cout
  Adder #(.width(32)) adder_2 (.a(PC_4), .b(beq_imm), .out(adder_2_out));  // open: cin, cout
  Multiplexer #(.width(32)) multiplexer_1 (
    .in0(PC_4), .in1(adder_2_out), .out(multiplexer_1_out), .sel(branch_op));  // open: en
  Multiplexer #(.width(32)) multiplexer_2 (
    .in0(multiplexer_1_out), .in1(j_jal_imm), .out(multiplexer_2_out), .sel(jump_op));  // open: en
endmodule

module ALU (
  input  [31:0] in_1,
  input  [31:0] in_2,
  input  [1:0] ALUOP,
  output Zero,
  output [31:0] out_5
);

  wire comparator_1_gt, comparator_2_eq, comparator_3_eq;
  wire [31:0] adder_1_out, bit_extender_1_out, or_1_out, subtractor_1_out;

  Adder #(.width(32)) adder_1 (.a(in_1), .b(in_2), .out(adder_1_out));  // open: cin, cout
  Subtractor #(.width(32)) subtractor_1 (.a(in_1), .b(in_2), .out(subtractor_1_out));  // open: bin, bout
  assign or_1_out = in_1 | in_2;  // OR_Gate or_1, 32 bits wide
  Multiplexer #(.select(2), .width(32), .enable("false")) multiplexer_1 (
    .in0(adder_1_out), .in1(subtractor_1_out), .in2(or_1_out), .in3(bit_extender_1_out), .out(out_5),
    .sel(ALUOP));
  Comparator #(.width(32)) comparator_1 (.a(in_1), .b(in_2), .gt(comparator_1_gt));  // open: eq, lt
  assign bit_extender_1_out = {{31{1'b0}}, comparator_1_gt};  // Bit_Extender bit_extender_1
  Comparator #(.width(32)) comparator_2 (.a(out_5), .b({32{1'b0}}), .eq(comparator_2_eq));  // open: gt, lt
  Comparator #(.width(32)) comparator_3 (.a(out_5), .b(32'h1), .eq(comparator_3_eq));  // open: gt, lt
  Multiplexer #(.select(2), .enable("false")) multiplexer_2 (
    .in0(1'b0), .in1(comparator_2_eq), .in2(1'b0), .in3(comparator_3_eq), .out(Zero), .sel(ALUOP));
endmodule

module Controller (
  input  [5:0] Op,
  input  [5:0] func,
  output [1:0] EXTop,
  output RegDst,
  output ALUSrc,
  output MemtoReg,
  output RegWrite,
  output MemRead,
  output MemWrite,
  output branch,
  output PCSel,
  output [1:0] ALUop
);

  wire addiu, addu, beq, bgtz, not_1_out, not_2_out, not_3_out, not_4_out, not_5_out, not_6_out, not_7_out,
       not_8_out, not_9_out, not_10_out, not_11_out, not_12_out, ori, subu;

  not not_1 (not_1_out, Op[5]);
  not not_2 (not_2_out, Op[4]);
  not not_3 (not_3_out, Op[3]);
  not not_4 (not_4_out, Op[1]);
  not not_5 (not_5_out, Op[2]);
  not not_6 (not_6_out, Op[0]);
  and LW (MemRead, Op[5], not_2_out, not_3_out, not_5_out, Op[1], Op[0]);
  and SW (MemWrite, Op[5], not_2_out, Op[3], not_5_out, Op[1], Op[0]);
  and R (RegDst, not_1_out, not_2_out, not_3_out, not_5_out, not_4_out, not_6_out);
  and u_ORI (ori, not_1_out, not_2_out, Op[3], Op[2], not_4_out, Op[0]);
  and J (PCSel, not_1_out, not_2_out, not_3_out, not_5_out, Op[1], not_6_out);
  and u_BEQ (beq, not_1_out, not_2_out, not_3_out, Op[2], not_4_out, not_6_out);
  and u_ADDIU (addiu, not_1_out, not_2_out, Op[3], not_5_out, not_4_out, Op[0]);
  and u_BGTZ (bgtz, not_1_out, not_2_out, not_3_out, Op[2], Op[1], Op[0]);
  not not_7 (not_7_out, func[5]);
  not not_8 (not_8_out, func[3]);
  not not_9 (not_9_out, func[4]);
  not not_10 (not_10_out, func[2]);
  not not_11 (not_11_out, func[1]);
  not not_12 (not_12_out, func[0]);
  and u_ADDU (addu, RegDst, func[5], not_9_out, not_8_out, not_10_out, not_11_out, func[0]);
  and u_SUBU (subu, RegDst, func[5], not_9_out, not_8_out, not_10_out, func[1], func[0]);
  or or_1 (ALUop[0], subu, bgtz, beq);
  or or_2 (ALUop[1], bgtz, ori);
  or or_3 (EXTop[0], MemRead, addiu, MemWrite);
  buf or_4 (EXTop[1], 1'b0);  // OR_Gate
  or or_5 (ALUSrc, addiu, MemRead, ori, MemWrite);
  or or_6 (MemtoReg, addiu, RegDst, ori, beq, PCSel, bgtz);
  or or_7 (RegWrite, RegDst, ori, MemRead);
  or or_8 (branch, bgtz, beq);

  // Other names for the same wires on the sheet: j = PCSel; lw = MemRead; r = RegDst; sw = MemWrite

  // Notes on the sheet:
  //   用于拓展lui
endmodule

module GRF (
  input  [4:0] A1,
  input  clk,
  input  reset,
  input  we,
  input  [4:0] A2,
  input  [4:0] A3,
  input  [31:0] WD,
  output [31:0] RD1,
  output [31:0] RD2
);

  wire [31:0] I0, I1, I2, I3, I4, I5, I6, I7, I8, I9, I10, I11, I12, I13, I14, I15, I16, I17, I18, I19, I20,
       I21, I22, I23, I24, I25, I26, I27, I28, I29, I30, I31, O0, O1, O2, O3, O4, O5, O6, O7, O8, O9, O10,
       O11, O12, O13, O14, O15, O16, O17, O18, O19, O20, O21, O22, O23, O24, O25, O26, O27, O28, O29, O30,
       O31;

  Demultiplexer #(.select(5), .width(32), .tristate("true")) demultiplexer_1 (
    .out0(I0), .out1(I1), .out2(I2), .out3(I3), .out4(I4), .out5(I5), .out6(I6), .out7(I7), .out8(I8),
    .out9(I9), .out10(I10), .out11(I11), .out12(I12), .out13(I13), .out14(I14), .out15(I15), .out16(I16),
    .out17(I17), .out18(I18), .out19(I19), .out20(I20), .out21(I21), .out22(I22), .out23(I23), .out24(I24),
    .out25(I25), .out26(I26), .out27(I27), .out28(I28), .out29(I29), .out30(I30), .out31(I31), .in(WD),
    .sel(A3));  // open: en
  Multiplexer #(.select(5), .width(32)) multiplexer_1 (
    .in0(O0), .in1(O1), .in2(O2), .in3(O3), .in4(O4), .in5(O5), .in6(O6), .in7(O7), .in8(O8), .in9(O9),
    .in10(O10), .in11(O11), .in12(O12), .in13(O13), .in14(O14), .in15(O15), .in16(O16), .in17(O17),
    .in18(O18), .in19(O19), .in20(O20), .in21(O21), .in22(O22), .in23(O23), .in24(O24), .in25(O25),
    .in26(O26), .in27(O27), .in28(O28), .in29(O29), .in30(O30), .in31(O31), .out(RD2), .sel(A2));  // open: en
  Multiplexer #(.select(5), .width(32)) multiplexer_2 (
    .in0(O0), .in1(O1), .in2(O2), .in3(O3), .in4(O4), .in5(O5), .in6(O6), .in7(O7), .in8(O8), .in9(O9),
    .in10(O10), .in11(O11), .in12(O12), .in13(O13), .in14(O14), .in15(O15), .in16(O16), .in17(O17),
    .in18(O18), .in19(O19), .in20(O20), .in21(O21), .in22(O22), .in23(O23), .in24(O24), .in25(O25),
    .in26(O26), .in27(O27), .in28(O28), .in29(O29), .in30(O30), .in31(O31), .out(RD1), .sel(A1));  // open: en
  Register #(.width(32)) register_1 (.D({32{1'b0}}), .en(we), .Q(O0), .clk(clk), .clr(reset));
  Register #(.width(32)) register_2 (.D(I8), .en(we), .Q(O8), .clk(clk), .clr(reset));
  Register #(.width(32)) register_3 (.D(I16), .en(we), .Q(O16), .clk(clk), .clr(reset));
  Register #(.width(32)) register_4 (.D(I24), .en(we), .Q(O24), .clk(clk), .clr(reset));
  Register #(.width(32)) register_5 (.D(I1), .en(we), .Q(O1), .clk(clk), .clr(reset));
  Register #(.width(32)) register_6 (.D(I9), .en(we), .Q(O9), .clk(clk), .clr(reset));
  Register #(.width(32)) register_7 (.D(I17), .en(we), .Q(O17), .clk(clk), .clr(reset));
  Register #(.width(32)) register_8 (.D(I25), .en(we), .Q(O25), .clk(clk), .clr(reset));
  Register #(.width(32)) register_9 (.D(I2), .en(we), .Q(O2), .clk(clk), .clr(reset));
  Register #(.width(32)) register_10 (.D(I10), .en(we), .Q(O10), .clk(clk), .clr(reset));
  Register #(.width(32)) register_11 (.D(I18), .en(we), .Q(O18), .clk(clk), .clr(reset));
  Register #(.width(32)) register_12 (.D(I26), .en(we), .Q(O26), .clk(clk), .clr(reset));
  Register #(.width(32)) register_13 (.D(I3), .en(we), .Q(O3), .clk(clk), .clr(reset));
  Register #(.width(32)) register_14 (.D(I11), .en(we), .Q(O11), .clk(clk), .clr(reset));
  Register #(.width(32)) register_15 (.D(I19), .en(we), .Q(O19), .clk(clk), .clr(reset));
  Register #(.width(32)) register_16 (.D(I27), .en(we), .Q(O27), .clk(clk), .clr(reset));
  Register #(.width(32)) register_17 (.D(I4), .en(we), .Q(O4), .clk(clk), .clr(reset));
  Register #(.width(32)) register_18 (.D(I12), .en(we), .Q(O12), .clk(clk), .clr(reset));
  Register #(.width(32)) register_19 (.D(I20), .en(we), .Q(O20), .clk(clk), .clr(reset));
  Register #(.width(32)) register_20 (.D(I28), .en(we), .Q(O28), .clk(clk), .clr(reset));
  Register #(.width(32)) register_21 (.D(I5), .en(we), .Q(O5), .clk(clk), .clr(reset));
  Register #(.width(32)) register_22 (.D(I13), .en(we), .Q(O13), .clk(clk), .clr(reset));
  Register #(.width(32)) register_23 (.D(I21), .en(we), .Q(O21), .clk(clk), .clr(reset));
  Register #(.width(32)) register_24 (.D(I29), .en(we), .Q(O29), .clk(clk), .clr(reset));
  Register #(.width(32)) register_25 (.D(I6), .en(we), .Q(O6), .clk(clk), .clr(reset));
  Register #(.width(32)) register_26 (.D(I14), .en(we), .Q(O14), .clk(clk), .clr(reset));
  Register #(.width(32)) register_27 (.D(I22), .en(we), .Q(O22), .clk(clk), .clr(reset));
  Register #(.width(32)) register_28 (.D(I30), .en(we), .Q(O30), .clk(clk), .clr(reset));
  Register #(.width(32)) register_29 (.D(I7), .en(we), .Q(O7), .clk(clk), .clr(reset));
  Register #(.width(32)) register_30 (.D(I15), .en(we), .Q(O15), .clk(clk), .clr(reset));
  Register #(.width(32)) register_31 (.D(I23), .en(we), .Q(O23), .clk(clk), .clr(reset));
  Register #(.width(32)) register_32 (.D(I31), .en(we), .Q(O31), .clk(clk), .clr(reset));
endmodule

module EXT (
  input  [15:0] in_1,
  input  [1:0] in_2,
  output [31:0] out_3
);

  wire [31:0] bit_extender_1_out, bit_extender_2_out;

  assign bit_extender_1_out = {{16{1'b0}}, in_1};  // Bit_Extender bit_extender_1
  assign bit_extender_2_out = {{16{in_1[15]}}, in_1};  // Bit_Extender bit_extender_2
  Multiplexer #(.select(2), .width(32), .enable("false")) multiplexer_1 (
    .in0(bit_extender_1_out), .in1(bit_extender_2_out), .in2({{16{1'b0}}, in_1}), .out(out_3), .sel(in_2));  // open: in3
endmodule

module DataMemory (
  input  [1:0] SSel,
  input  [1:0] Lsel,
  input  [31:0] Addr,
  input  in_4,
  input  in_5,
  input  in_6,
  input  in_7,
  input  [31:0] WriteData,
  output [31:0] RD
);

  wire decoder_1_out0, decoder_1_out1, decoder_1_out2, decoder_1_out3, decoder_2_out0, decoder_2_out1;
  wire [7:0] _7_0, _15_8, _23_16, _24_31, multiplexer_1_out, multiplexer_2_out, multiplexer_3_out,
       multiplexer_4_out, multiplexer_8_out;
  wire [15:0] multiplexer_5_out, multiplexer_6_out, multiplexer_9_out;
  wire [31:0] bit_extender_1_out, bit_extender_2_out, multiplexer_7_out;

  Decoder #(.select(2)) decoder_1 (
    .out0(decoder_1_out0), .out1(decoder_1_out1), .out2(decoder_1_out2), .out3(decoder_1_out3),
    .sel(Addr[1:0]));  // open: en
  Decoder decoder_2 (.out0(decoder_2_out0), .out1(decoder_2_out1), .sel(Addr[1]));  // open: en
  Multiplexer #(.width(8), .enable("false")) multiplexer_1 (
    .in0(_7_0), .in1(WriteData[7:0]), .out(multiplexer_1_out), .sel(decoder_1_out0));
  Multiplexer #(.width(8), .enable("false")) multiplexer_2 (
    .in0(_15_8), .in1(WriteData[7:0]), .out(multiplexer_2_out), .sel(decoder_1_out1));
  Multiplexer #(.width(8), .enable("false")) multiplexer_3 (
    .in0(_23_16), .in1(WriteData[7:0]), .out(multiplexer_3_out), .sel(decoder_1_out2));
  Multiplexer #(.width(8), .enable("false")) multiplexer_4 (
    .in0(_24_31), .in1(WriteData[7:0]), .out(multiplexer_4_out), .sel(decoder_1_out3));
  Multiplexer #(.width(16), .enable("false")) multiplexer_5 (
    .in0({_15_8, _7_0}), .in1(WriteData[15:0]), .out(multiplexer_5_out), .sel(decoder_2_out0));
  Multiplexer #(.width(16), .enable("false")) multiplexer_6 (
    .in0({_24_31, _23_16}), .in1(WriteData[15:0]), .out(multiplexer_6_out), .sel(decoder_2_out1));
  Multiplexer #(.select(2), .width(32), .enable("false")) multiplexer_7 (
    .in0(WriteData), .in1({multiplexer_4_out, multiplexer_3_out, multiplexer_2_out, multiplexer_1_out}),
    .in2({multiplexer_6_out, multiplexer_5_out}), .out(multiplexer_7_out), .sel(SSel));  // open: in3
  RAM #(.addrWidth(5), .dataWidth(32), .bus("separate")) ram_1 (
    .addr(Addr[6:2]), .din(multiplexer_7_out), .data({_24_31, _23_16, _15_8, _7_0}), .str(in_4), .clk(in_5),
    .ld(in_6), .clr(in_7));  // open: sel
  Multiplexer #(.select(2), .width(8), .enable("false")) multiplexer_8 (
    .in0(_7_0), .in1(_15_8), .in2(_23_16), .in3(_24_31), .out(multiplexer_8_out), .sel(Addr[1:0]));
  Multiplexer #(.width(16), .enable("false")) multiplexer_9 (
    .in0({_15_8, _7_0}), .in1({_24_31, _23_16}), .out(multiplexer_9_out), .sel(Addr[1]));
  assign bit_extender_1_out = {{24{multiplexer_8_out[7]}}, multiplexer_8_out};  // Bit_Extender bit_extender_1
  assign bit_extender_2_out = {{16{multiplexer_9_out[15]}}, multiplexer_9_out};  // Bit_Extender bit_extender_2
  Multiplexer #(.select(2), .width(32), .enable("false")) multiplexer_10 (
    .in0({_24_31, _23_16, _15_8, _7_0}), .in1(bit_extender_1_out), .in2(bit_extender_2_out), .out(RD),
    .sel(Lsel));  // open: in3
endmodule
