// Logisim project CPU_xyf.circ as structural Verilog: 7 circuits, main circuit main
module register (
  input  [4:0] Rreg1,
  input  clk,
  input  [4:0] Wreg,
  input  RegWrite,
  input  [31:0] Wdata,
  input  [4:0] Rreg2,
  output [31:0] Rdata1,
  output [31:0] Rdata2
);

  wire and_1_out, and_2_out, and_3_out, and_4_out, and_5_out, and_6_out, and_7_out, and_8_out, and_9_out,
       and_10_out, and_11_out, and_12_out, and_13_out, and_14_out, and_15_out, and_16_out, and_17_out,
       and_18_out, and_19_out, and_20_out, and_21_out, and_22_out, and_23_out, and_24_out, and_25_out,
       and_26_out, and_27_out, and_28_out, and_29_out, and_30_out, and_31_out, and_32_out, decoder_1_out0,
       decoder_1_out1, decoder_1_out2, decoder_1_out3, decoder_1_out4, decoder_1_out5, decoder_1_out6,
       decoder_1_out7, decoder_1_out8, decoder_1_out9, decoder_1_out10, decoder_1_out11, decoder_1_out12,
       decoder_1_out13, decoder_1_out14, decoder_1_out15, decoder_1_out16, decoder_1_out17, decoder_1_out18,
       decoder_1_out19, decoder_1_out20, decoder_1_out21, decoder_1_out22, decoder_1_out23, decoder_1_out24,
       decoder_1_out25, decoder_1_out26, decoder_1_out27, decoder_1_out28, decoder_1_out29, decoder_1_out30,
       decoder_1_out31;
  wire [31:0] register_1_q, register_2_q, register_3_q, register_4_q, register_5_q, register_6_q,
       register_7_q, register_8_q, register_9_q, register_10_q, register_11_q, register_12_q, register_13_q,
       register_14_q, register_15_q, register_16_q, register_17_q, register_18_q, register_19_q,
       register_20_q, register_21_q, register_22_q, register_23_q, register_24_q, register_25_q,
       register_26_q, register_27_q, register_28_q, register_29_q, register_30_q, register_31_q,
       register_32_q;

  Decoder #(.select(5)) decoder_1 (
    .out0(decoder_1_out0), .out1(decoder_1_out1), .out2(decoder_1_out2), .out3(decoder_1_out3),
    .out4(decoder_1_out4), .out5(decoder_1_out5), .out6(decoder_1_out6), .out7(decoder_1_out7),
    .out8(decoder_1_out8), .out9(decoder_1_out9), .out10(decoder_1_out10), .out11(decoder_1_out11),
    .out12(decoder_1_out12), .out13(decoder_1_out13), .out14(decoder_1_out14), .out15(decoder_1_out15),
    .out16(decoder_1_out16), .out17(decoder_1_out17), .out18(decoder_1_out18), .out19(decoder_1_out19),
    .out20(decoder_1_out20), .out21(decoder_1_out21), .out22(decoder_1_out22), .out23(decoder_1_out23),
    .out24(decoder_1_out24), .out25(decoder_1_out25), .out26(decoder_1_out26), .out27(decoder_1_out27),
    .out28(decoder_1_out28), .out29(decoder_1_out29), .out30(decoder_1_out30), .out31(decoder_1_out31),
    .sel(Wreg));  // open: en
  Register #(.width(32)) register_1 (.D(Wdata), .Q(register_1_q), .clk(and_1_out));  // open: en, clr
  and and_1 (and_1_out, RegWrite, clk, decoder_1_out0);
  Register #(.width(32)) register_2 (.D(Wdata), .Q(register_2_q), .clk(and_2_out));  // open: en, clr
  and and_2 (and_2_out, RegWrite, clk, decoder_1_out1);
  Register #(.width(32)) register_3 (.D(Wdata), .Q(register_3_q), .clk(and_3_out));  // open: en, clr
  and and_3 (and_3_out, RegWrite, clk, decoder_1_out2);
  Register #(.width(32)) register_4 (.D(Wdata), .Q(register_4_q), .clk(and_4_out));  // open: en, clr
  and and_4 (and_4_out, RegWrite, clk, decoder_1_out3);
  Register #(.width(32)) register_5 (.D(Wdata), .Q(register_5_q), .clk(and_5_out));  // open: en, clr
  and and_5 (and_5_out, RegWrite, clk, decoder_1_out4);
  Register #(.width(32)) register_6 (.D(Wdata), .Q(register_6_q), .clk(and_6_out));  // open: en, clr
  and and_6 (and_6_out, RegWrite, clk, decoder_1_out5);
  Register #(.width(32)) register_7 (.D(Wdata), .Q(register_7_q), .clk(and_7_out));  // open: en, clr
  and and_7 (and_7_out, RegWrite, clk, decoder_1_out6);
  Register #(.width(32)) register_8 (.D(Wdata), .Q(register_8_q), .clk(and_8_out));  // open: en, clr
  and and_8 (and_8_out, RegWrite, clk, decoder_1_out7);
  Register #(.width(32)) register_9 (.D(Wdata), .Q(register_9_q), .clk(and_9_out));  // open: en, clr
  and and_9 (and_9_out, RegWrite, clk, decoder_1_out8);
  Register #(.width(32)) register_10 (.D(Wdata), .Q(register_10_q), .clk(and_10_out));  // open: en, clr
  and and_10 (and_10_out, RegWrite, clk, decoder_1_out9);
  Register #(.width(32)) register_11 (.D(Wdata), .Q(register_11_q), .clk(and_11_out));  // open: en, clr
  and and_11 (and_11_out, RegWrite, clk, decoder_1_out10);
  Register #(.width(32)) register_12 (.D(Wdata), .Q(register_12_q), .clk(and_12_out));  // open: en, clr
  and and_12 (and_12_out, RegWrite, clk, decoder_1_out11);
  Register #(.width(32)) register_13 (.D(Wdata), .Q(register_13_q), .clk(and_13_out));  // open: en, clr
  and and_13 (and_13_out, RegWrite, clk, decoder_1_out12);
  Register #(.width(32)) register_14 (.D(Wdata), .Q(register_14_q), .clk(and_14_out));  // open: en, clr
  and and_14 (and_14_out, RegWrite, clk, decoder_1_out13);
  Register #(.width(32)) register_15 (.D(Wdata), .Q(register_15_q), .clk(and_15_out));  // open: en, clr
  and and_15 (and_15_out, RegWrite, clk, decoder_1_out14);
  Register #(.width(32)) register_16 (.D(Wdata), .Q(register_16_q), .clk(and_16_out));  // open: en, clr
  and and_16 (and_16_out, RegWrite, clk, decoder_1_out15);
  and and_17 (and_17_out, RegWrite, clk, decoder_1_out16);
  and and_18 (and_18_out, RegWrite, clk, decoder_1_out17);
  and and_19 (and_19_out, RegWrite, clk, decoder_1_out18);
  and and_20 (and_20_out, RegWrite, clk, decoder_1_out19);
  and and_21 (and_21_out, RegWrite, clk, decoder_1_out20);
  and and_22 (and_22_out, RegWrite, clk, decoder_1_out21);
  and and_23 (and_23_out, RegWrite, clk, decoder_1_out22);
  and and_24 (and_24_out, RegWrite, clk, decoder_1_out23);
  and and_25 (and_25_out, RegWrite, clk, decoder_1_out24);
  and and_26 (and_26_out, RegWrite, clk, decoder_1_out25);
  and and_27 (and_27_out, RegWrite, clk, decoder_1_out26);
  and and_28 (and_28_out, RegWrite, clk, decoder_1_out27);
  and and_29 (and_29_out, RegWrite, clk, decoder_1_out28);
  and and_30 (and_30_out, RegWrite, clk, decoder_1_out29);
  and and_31 (and_31_out, RegWrite, clk, decoder_1_out30);
  and and_32 (and_32_out, RegWrite, clk, decoder_1_out31);
  Register #(.width(32)) register_17 (.D(Wdata), .Q(register_17_q), .clk(and_17_out));  // open: en, clr
  Register #(.width(32)) register_18 (.D(Wdata), .Q(register_18_q), .clk(and_18_out));  // open: en, clr
  Register #(.width(32)) register_19 (.D(Wdata), .Q(register_19_q), .clk(and_19_out));  // open: en, clr
  Register #(.width(32)) register_20 (.D(Wdata), .Q(register_20_q), .clk(and_20_out));  // open: en, clr
  Register #(.width(32)) register_21 (.D(Wdata), .Q(register_21_q), .clk(and_21_out));  // open: en, clr
  Register #(.width(32)) register_22 (.D(Wdata), .Q(register_22_q), .clk(and_22_out));  // open: en, clr
  Register #(.width(32)) register_23 (.D(Wdata), .Q(register_23_q), .clk(and_23_out));  // open: en, clr
  Register #(.width(32)) register_24 (.D(Wdata), .Q(register_24_q), .clk(and_24_out));  // open: en, clr
  Register #(.width(32)) register_25 (.D(Wdata), .Q(register_25_q), .clk(and_25_out));  // open: en, clr
  Register #(.width(32)) register_26 (.D(Wdata), .Q(register_26_q), .clk(and_26_out));  // open: en, clr
  Register #(.width(32)) register_27 (.D(Wdata), .Q(register_27_q), .clk(and_27_out));  // open: en, clr
  Register #(.width(32)) register_28 (.D(Wdata), .Q(register_28_q), .clk(and_28_out));  // open: en, clr
  Register #(.width(32)) register_29 (.D(Wdata), .Q(register_29_q), .clk(and_29_out));  // open: en, clr
  Register #(.width(32)) register_30 (.D(Wdata), .Q(register_30_q), .clk(and_30_out));  // open: en, clr
  Register #(.width(32)) register_31 (.D(Wdata), .Q(register_31_q), .clk(and_31_out));  // open: en, clr
  Register #(.width(32)) register_32 (.D(Wdata), .Q(register_32_q), .clk(and_32_out));  // open: en, clr
  Multiplexer #(.select(5), .width(32)) multiplexer_1 (
    .in0(register_1_q), .in1(register_2_q), .in2(register_3_q), .in3(register_4_q), .in4(register_5_q),
    .in5(register_6_q), .in6(register_7_q), .in7(register_8_q), .in8(register_9_q), .in9(register_10_q),
    .in10(register_11_q), .in11(register_12_q), .in12(register_13_q), .in13(register_14_q),
    .in14(register_15_q), .in15(register_16_q), .in16(register_17_q), .in17(register_18_q),
    .in18(register_19_q), .in19(register_20_q), .in20(register_21_q), .in21(register_22_q),
    .in22(register_23_q), .in23(register_24_q), .in24(register_25_q), .in25(register_26_q),
    .in26(register_27_q), .in27(register_28_q), .in28(register_29_q), .in29(register_30_q),
    .in30(register_31_q), .in31(register_32_q), .out(Rdata1), .sel(Rreg1));  // open: en
  Multiplexer #(.select(5), .width(32)) multiplexer_2 (
    .in0(register_1_q), .in1(register_2_q), .in2(register_3_q), .in3(register_4_q), .in4(register_5_q),
    .in5(register_6_q), .in6(register_7_q), .in7(register_8_q), .in8(register_9_q), .in9(register_10_q),
    .in10(register_11_q), .in11(register_12_q), .in12(register_13_q), .in13(register_14_q),
    .in14(register_15_q), .in15(register_16_q), .in16(register_17_q), .in17(register_18_q),
    .in18(register_19_q), .in19(register_20_q), .in20(register_21_q), .in21(register_22_q),
    .in22(register_23_q), .in23(register_24_q), .in24(register_25_q), .in25(register_26_q),
    .in26(register_27_q), .in27(register_28_q), .in28(register_29_q), .in29(register_30_q),
    .in30(register_31_q), .in31(register_32_q), .out(Rdata2), .sel(Rreg2));  // open: en
endmodule

module main (
  input  in_1,
  output [31:0] out_2,
  output out_3,
  output [4:0] out_4,
  output [31:0] out_5,
  output out_6,
  output [4:0] out_7,
  output [31:0] out_8
);

  wire alu_1_zero, ALUSrc, Branch, CLK, EXTop, MemRead, MemtoReg, PCSel, PCSrc_out, RegDst;
  wire [4:0] bit_extender_1_out, instruction_splitter_1__15_11, instruction_splitter_1__20_16,
       instruction_splitter_1__25_21;
  wire [5:0] func, op;
  wire [15:0] instruction_splitter_1__15_0;
  wire [25:0] _25_0, shifter_3_out;
  wire [31:0] adder_1_out, adder_2_out, alu_1_rd, bit_extender_3_out, ext_1_out_3, grf_1_rd1,
       multiplexer_2_out, multiplexer_3_out, multiplexer_4_out, PC_4, ram_1_data, register_1_q,
       shifter_1_out, shifter_2_out;

  Register #(.width(32)) register_1 (.D(PC_4), .Q(register_1_q), .clk(CLK), .clr(in_1));  // open: en
  Shifter #(.width(32), .shift("lr")) shifter_1 (.in(register_1_q), .\dist (5'b00010), .out(shifter_1_out));
  Adder #(.width(32)) adder_1 (.a(register_1_q), .b(32'h4), .out(adder_1_out));  // open: cin, cout
  Bit_Extender #(.in_width(32), .out_width(5)) bit_extender_1 (.in(shifter_1_out), .out(bit_extender_1_out));
  Clock clock_1 (.out(CLK));
  ROM #(.addrWidth(5), .dataWidth(32)) rom_1 (.addr(bit_extender_1_out), .data(out_2));  // open: sel
  Instruction_splitter instruction_splitter_1 (
    .in_1(out_2), ._31_26(op), ._25_21(instruction_splitter_1__25_21),
    ._20_16(instruction_splitter_1__20_16), ._15_11(instruction_splitter_1__15_11),
    ._15_0(instruction_splitter_1__15_0), ._25_0(_25_0));
  // Probe on op
  controller controller_1 (
    .in_1(op), .RegDst(RegDst), .ALUSrc(ALUSrc), .MemToReg(MemtoReg), .RegWrite(out_3), .MemRead(MemRead),
    .MemWrite(out_6), .Branch(Branch), .PCSel(PCSel), .EXTop(EXTop));
  // Probe on instruction_splitter_1__25_21
  Multiplexer #(.width(5), .enable("false")) multiplexer_1 (
    .in0(instruction_splitter_1__20_16), .in1(instruction_splitter_1__15_11), .out(out_4), .sel(RegDst));
  // Probe on out_4
  EXT ext_1 (.in_1(instruction_splitter_1__15_0), .EXTop(EXTop), .out_3(ext_1_out_3));
  Bit_Extender #(.in_width(16), .out_width(6)) bit_extender_2 (.in(instruction_splitter_1__15_0), .out(func));
  GRF grf_1 (
    .A1(instruction_splitter_1__25_21), .A2(instruction_splitter_1__20_16), .A3(out_4), .WD(out_5),
    .RD1(grf_1_rd1), .RD2(out_8), .clk(CLK), .reset(in_1), .we(out_3));
  Multiplexer #(.width(32), .enable("false")) multiplexer_2 (
    .in0(out_8), .in1(ext_1_out_3), .out(multiplexer_2_out), .sel(ALUSrc));
  Shifter #(.width(32)) shifter_2 (.in(ext_1_out_3), .\dist (5'b00010), .out(shifter_2_out));
  ALU alu_1 (
    .Rs(grf_1_rd1), .Rt(multiplexer_2_out), .Rd({alu_1_rd[31:7], out_7, alu_1_rd[1:0]}), .op(op),
    .func(func), .zero(alu_1_zero));
  Adder #(.width(32)) adder_2 (.a(adder_1_out), .b(shifter_2_out), .out(adder_2_out));  // open: cin, cout
  and PCSrc (PCSrc_out, Branch, alu_1_zero);
  Multiplexer #(.width(32), .enable("false")) multiplexer_3 (
    .in0(adder_1_out), .in1(adder_2_out), .out(multiplexer_3_out), .sel(PCSrc_out));
  Shifter #(.width(26)) shifter_3 (.in(_25_0), .\dist (5'b00010), .out(shifter_3_out));
  Multiplexer #(.width(32), .enable("false")) multiplexer_4 (
    .in0(multiplexer_3_out), .in1(bit_extender_3_out), .out(multiplexer_4_out), .sel(PCSel));
  assign bit_extender_3_out = {{6{1'b0}}, shifter_3_out};  // Bit_Extender bit_extender_3
  RAM #(.addrWidth(5), .dataWidth(32), .bus("separate")) ram_1 (
    .addr(out_7), .din(out_8), .data(ram_1_data), .str(out_6), .clk(CLK), .ld(MemRead), .clr(in_1));  // open: sel
  Adder #(.width(32)) adder_3 (.a(multiplexer_4_out), .b(32'h3000), .out(PC_4));  // open: cin, cout
  Multiplexer #(.width(32), .enable("false")) multiplexer_5 (
    .in0(ram_1_data), .in1({alu_1_rd[31:7], out_7, alu_1_rd[1:0]}), .out(out_5), .sel(MemtoReg));

  // Other names for the same wires on the sheet: MemAddr[4:0] = out_7; Instr[31:0] = out_2; MemData[31:0] = out_8;
  //   MemWrite = out_6; RegAddr[4:0] = out_4; RegData[31:0] = out_5; RegWrite = out_3; Reset = in_1

  // Notes on the sheet:
  //   contents of rom_1 (hex, n*v repeats v):
  //   8c2b0000 942021 a42023 10a50000 8000c05 34420002
endmodule

module Instruction_splitter (
  input  [31:0] in_1,
  output [5:0] _31_26,
  output [4:0] _25_21,
  output [4:0] _20_16,
  output [4:0] _15_11,
  output [15:0] _15_0,
  output [25:0] _25_0
);


  assign _15_0 = in_1[15:0];
  assign _15_11 = in_1[15:11];
  assign _20_16 = in_1[20:16];
  assign _25_0 = in_1[25:0];
  assign _25_21 = in_1[25:21];
  assign _31_26 = in_1[31:26];
endmodule

module ALU (
  input  [5:0] op,
  input  [5:0] func,
  input  [31:0] Rs,
  input  [31:0] Rt,
  output zero,
  output [31:0] Rd
);

  wire addu, comparator_1_eq, j, lw, or_2_out, ori, R_out, subu, sw;
  wire [31:0] adder_1_out, adder_2_out, bit_extender_1_out, or_1_out, shifter_1_out, subtractor_1_out;

  Adder #(.width(32)) adder_1 (.a(Rs), .b(Rt), .out(adder_1_out));  // open: cin, cout
  Subtractor #(.width(32)) subtractor_1 (.a(Rs), .b(Rt), .out(subtractor_1_out));  // open: bin, bout
  assign or_1_out = Rs | Rt;  // OR_Gate or_1, 32 bits wide
  Comparator #(.width(32), .mode("unsigned")) comparator_1 (.a(Rs), .b(Rt), .eq(comparator_1_eq));  // open: gt, lt
  Shifter #(.width(32)) shifter_1 (.in(Rt), .\dist (5'b00010), .out(shifter_1_out));
  assign Rd = addu ? adder_1_out : 32'bz;  // Controlled_Buffer controlled_buffer_1
  assign Rd = subu ? subtractor_1_out : 32'bz;  // Controlled_Buffer controlled_buffer_2
  assign Rd = ori ? or_1_out : 32'bz;  // Controlled_Buffer controlled_buffer_3
  assign Rd = zero ? bit_extender_1_out : 32'bz;  // Controlled_Buffer controlled_buffer_4
  assign bit_extender_1_out = {{31{1'b0}}, comparator_1_eq};  // Bit_Extender bit_extender_1
  assign Rd = j ? {32{1'b0}} : 32'bz;  // Controlled_Buffer controlled_buffer_5
  or or_2 (or_2_out, lw, sw);
  Adder #(.width(32)) adder_2 (.a(Rs), .b(shifter_1_out), .out(adder_2_out));  // open: cin, cout
  assign Rd = or_2_out ? adder_2_out : 32'bz;  // Controlled_Buffer controlled_buffer_6
  and R (R_out, ~op[5], ~op[4], ~op[3], ~op[2], ~op[1], ~op[0]);  // AND_Gate
  and u_lw (lw, op[0], op[1], ~op[2], ~op[3], ~op[4], op[5]);  // AND_Gate
  and u_sw (sw, op[0], op[1], ~op[2], op[3], ~op[4], op[5]);  // AND_Gate
  and u_ori (ori, op[0], ~op[1], op[2], op[3], ~op[4], ~op[5]);  // AND_Gate
  and beq (zero, ~op[0], ~op[1], op[2], ~op[3], ~op[4], ~op[5]);  // AND_Gate
  and and_1 (j, ~op[0], op[1], ~op[2], ~op[3], ~op[4], ~op[5]);  // AND_Gate
  and and_2 (addu, R_out, func[5], ~func[4], ~func[3], ~func[2], ~func[1], func[0]);  // AND_Gate
  and and_3 (subu, R_out, func[0], func[1], ~func[2], ~func[3], ~func[4], func[5]);  // AND_Gate

  // Other names for the same wires on the sheet: beq = zero
endmodule

module controller (
  input  [5:0] in_1,
  output RegDst,
  output ALUSrc,
  output MemToReg,
  output RegWrite,
  output MemRead,
  output MemWrite,
  output Branch,
  output PCSel,
  output EXTop
);

  and R_format (RegDst, ~in_1[0], ~in_1[1], ~in_1[2], ~in_1[3], ~in_1[4], ~in_1[5]);  // AND_Gate
  and lw (MemRead, in_1[0], in_1[1], ~in_1[2], ~in_1[3], ~in_1[4], in_1[5]);  // AND_Gate
  and sw (MemWrite, in_1[0], in_1[1], ~in_1[2], in_1[3], ~in_1[4], in_1[5]);  // AND_Gate
  and beq (Branch, ~in_1[0], ~in_1[1], in_1[2], ~in_1[3], ~in_1[4], ~in_1[5]);  // AND_Gate
  and ori (EXTop, in_1[0], ~in_1[1], in_1[2], in_1[3], ~in_1[4], ~in_1[5]);  // AND_Gate
  and j (PCSel, ~in_1[0], in_1[1], ~in_1[2], ~in_1[3], ~in_1[4], ~in_1[5]);  // AND_Gate
  // AND_Gate jal has open pins: in0=in_1[0], in1=in_1[1], in2=in_1[2], in3=in_1[3], in4=in_1[4], in5=in_1[5], out=open
  or or_1 (ALUSrc, MemRead, MemWrite, EXTop);
  or or_2 (MemToReg, RegDst, EXTop, Branch, PCSel);
  or or_3 (RegWrite, RegDst, EXTop, MemRead);

  // Other names for the same wires on the sheet: beq = Branch; j = PCSel; lw = MemRead; ori = EXTop;
  //   R_format = RegDst; sw = MemWrite
endmodule

module GRF (
  input  [4:0] A1,
  input  clk,
  input  reset,
  input  we,
  input  [4:0] A2,
  input  [4:0] A3,
  input  [31:0] WD,
  output [31:0] RD1,
  output [31:0] RD2
);

  wire [31:0] I0, I1, I2, I3, I4, I5, I6, I7, I8, I9, I10, I11, I12, I13, I14, I15, I16, I17, I18, I19, I20,
       I21, I22, I23, I24, I25, I26, I27, I28, I29, I30, I31, O0, O1, O2, O3, O4, O5, O6, O7, O8, O9, O10,
       O11, O12, O13, O14, O15, O16, O17, O18, O19, O20, O21, O22, O23, O24, O25, O26, O27, O28, O29, O30,
       O31;

  Demultiplexer #(.select(5), .width(32), .tristate("true")) demultiplexer_1 (
    .out0(I0), .out1(I1), .out2(I2), .out3(I3), .out4(I4), .out5(I5), .out6(I6), .out7(I7), .out8(I8),
    .out9(I9), .out10(I10), .out11(I11), .out12(I12), .out13(I13), .out14(I14), .out15(I15), .out16(I16),
    .out17(I17), .out18(I18), .out19(I19), .out20(I20), .out21(I21), .out22(I22), .out23(I23), .out24(I24),
    .out25(I25), .out26(I26), .out27(I27), .out28(I28), .out29(I29), .out30(I30), .out31(I31), .in(WD),
    .sel(A3));  // open: en
  Multiplexer #(.select(5), .width(32)) multiplexer_1 (
    .in0(O0), .in1(O1), .in2(O2), .in3(O3), .in4(O4), .in5(O5), .in6(O6), .in7(O7), .in8(O8), .in9(O9),
    .in10(O10), .in11(O11), .in12(O12), .in13(O13), .in14(O14), .in15(O15), .in16(O16), .in17(O17),
    .in18(O18), .in19(O19), .in20(O20), .in21(O21), .in22(O22), .in23(O23), .in24(O24), .in25(O25),
    .in26(O26), .in27(O27), .in28(O28), .in29(O29), .in30(O30), .in31(O31), .out(RD2), .sel(A2));  // open: en
  Multiplexer #(.select(5), .width(32)) multiplexer_2 (
    .in0(O0), .in1(O1), .in2(O2), .in3(O3), .in4(O4), .in5(O5), .in6(O6), .in7(O7), .in8(O8), .in9(O9),
    .in10(O10), .in11(O11), .in12(O12), .in13(O13), .in14(O14), .in15(O15), .in16(O16), .in17(O17),
    .in18(O18), .in19(O19), .in20(O20), .in21(O21), .in22(O22), .in23(O23), .in24(O24), .in25(O25),
    .in26(O26), .in27(O27), .in28(O28), .in29(O29), .in30(O30), .in31(O31), .out(RD1), .sel(A1));  // open: en
  Register #(.width(32)) register_1 (.D({32{1'b0}}), .en(we), .Q(O0), .clk(clk), .clr(reset));
  Register #(.width(32)) register_2 (.D(I8), .en(we), .Q(O8), .clk(clk), .clr(reset));
  Register #(.width(32)) register_3 (.D(I16), .en(we), .Q(O16), .clk(clk), .clr(reset));
  Register #(.width(32)) register_4 (.D(I24), .en(we), .Q(O24), .clk(clk), .clr(reset));
  Register #(.width(32)) register_5 (.D(I1), .en(we), .Q(O1), .clk(clk), .clr(reset));
  Register #(.width(32)) register_6 (.D(I9), .en(we), .Q(O9), .clk(clk), .clr(reset));
  Register #(.width(32)) register_7 (.D(I17), .en(we), .Q(O17), .clk(clk), .clr(reset));
  Register #(.width(32)) register_8 (.D(I25), .en(we), .Q(O25), .clk(clk), .clr(reset));
  Register #(.width(32)) register_9 (.D(I2), .en(we), .Q(O2), .clk(clk), .clr(reset));
  Register #(.width(32)) register_10 (.D(I10), .en(we), .Q(O10), .clk(clk), .clr(reset));
  Register #(.width(32)) register_11 (.D(I18), .en(we), .Q(O18), .clk(clk), .clr(reset));
  Register #(.width(32)) register_12 (.D(I26), .en(we), .Q(O26), .clk(clk), .clr(reset));
  Register #(.width(32)) register_13 (.D(I3), .en(we), .Q(O3), .clk(clk), .clr(reset));
  Register #(.width(32)) register_14 (.D(I11), .en(we), .Q(O11), .clk(clk), .clr(reset));
  Register #(.width(32)) register_15 (.D(I19), .en(we), .Q(O19), .clk(clk), .clr(reset));
  Register #(.width(32)) register_16 (.D(I27), .en(we), .Q(O27), .clk(clk), .clr(reset));
  Register #(.width(32)) register_17 (.D(I4), .en(we), .Q(O4), .clk(clk), .clr(reset));
  Register #(.width(32)) register_18 (.D(I12), .en(we), .Q(O12), .clk(clk), .clr(reset));
  Register #(.width(32)) register_19 (.D(I20), .en(we), .Q(O20), .clk(clk), .clr(reset));
  Register #(.width(32)) register_20 (.D(I28), .en(we), .Q(O28), .clk(clk), .clr(reset));
  Register #(.width(32)) register_21 (.D(I5), .en(we), .Q(O5), .clk(clk), .clr(reset));
  Register #(.width(32)) register_22 (.D(I13), .en(we), .Q(O13), .clk(clk), .clr(reset));
  Register #(.width(32)) register_23 (.D(I21), .en(we), .Q(O21), .clk(clk), .clr(reset));
  Register #(.width(32)) register_24 (.D(I29), .en(we), .Q(O29), .clk(clk), .clr(reset));
  Register #(.width(32)) register_25 (.D(I6), .en(we), .Q(O6), .clk(clk), .clr(reset));
  Register #(.width(32)) register_26 (.D(I14), .en(we), .Q(O14), .clk(clk), .clr(reset));
  Register #(.width(32)) register_27 (.D(I22), .en(we), .Q(O22), .clk(clk), .clr(reset));
  Register #(.width(32)) register_28 (.D(I30), .en(we), .Q(O30), .clk(clk), .clr(reset));
  Register #(.width(32)) register_29 (.D(I7), .en(we), .Q(O7), .clk(clk), .clr(reset));
  Register #(.width(32)) register_30 (.D(I15), .en(we), .Q(O15), .clk(clk), .clr(reset));
  Register #(.width(32)) register_31 (.D(I23), .en(we), .Q(O23), .clk(clk), .clr(reset));
  Register #(.width(32)) register_32 (.D(I31), .en(we), .Q(O31), .clk(clk), .clr(reset));
endmodule

module EXT (
  input  [15:0] in_1,
  input  EXTop,
  output [31:0] out_3
);

  wire [31:0] bit_extender_1_out, bit_extender_2_out;

  assign bit_extender_1_out = {{16{1'b0}}, in_1};  // Bit_Extender bit_extender_1
  assign bit_extender_2_out = {{16{in_1[15]}}, in_1};  // Bit_Extender bit_extender_2
  // Probe on bit_extender_1_out
  Multiplexer #(.width(32), .enable("false")) multiplexer_1 (
    .in0(bit_extender_1_out), .in1(bit_extender_2_out), .out(out_3), .sel(EXTop));
  // Probe on bit_extender_2_out
endmodule
