// Logisim project singal_period_CPU.circ as structural Verilog: 7 circuits, main circuit PC
module main (
  input  Reset,
  output [31:0] Instr,
  output RegWrite,
  output [4:0] RegAddr,
  output [31:0] RegData,
  output MemWrite,
  output [4:0] MemAddr,
  output [31:0] MemData
);

  wire ALU_ZERO, ALUSrc, branch, brancher_1_output, clk, Exten_Sign, MemRead, MemtoReg, PCSrc, RegDst;
  wire [3:0] ALU_OP;
  wire [31:0] adder_1_out, ALU_result, DM_OUT, IM_in, input1, input2, multiplexer_4_out, NextPC, PC_4,
       PCBranch, shifter_1_out, SignedExt;

  Shifter #(.width(32)) shifter_1 (.in(SignedExt), .\dist (5'b00010), .out(shifter_1_out));
  Adder #(.width(32)) adder_1 (.a(shifter_1_out), .b(PC_4), .out(adder_1_out));  // open: cin, cout
  Multiplexer #(.width(32), .enable("false")) multiplexer_1 (
    .in0(PC_4), .in1(PCBranch), .out(NextPC), .sel(brancher_1_output));
  Brancher brancher_1 (.PCSrc(PCSrc), .branch(branch), .ALUZERO(ALU_ZERO), .\output (brancher_1_output));
  PC pc_1 (.rst(Reset), .clk(clk), .Q(IM_in), .init(32'h3000), .D(NextPC));  // open: en
  Multiplexer #(.width(32), .enable("false")) multiplexer_2 (
    .in0({Instr[31:28], Instr[25:0], 2'b00}), .in1(adder_1_out), .out(PCBranch), .sel(branch));
  Add4 add4_1 (.in(IM_in), .out(PC_4));
  assign SignedExt = {{16{Instr[15]}}, Instr[15:0]};  // Bit_Extender bit_extender_1
  ROM #(.addrWidth(5), .dataWidth(32)) rom_1 (.addr(IM_in[6:2]), .data(Instr));  // open: sel
  Controller Controller (
    .OP(Instr[31:26]), .FUNC(Instr[5:0]), .ALU_OP(ALU_OP), .RegDst(RegDst), .RegWrite(RegWrite),
    .ALUSrc(ALUSrc), .PCSrc(PCSrc), .MemRead(MemRead), .MemWrite(MemWrite), .MemtoReg(MemtoReg),
    .branch(branch), .Exten_Signal(Exten_Sign));
  Clock clock_1 (.out(clk));
  GRF grf_1 (
    .A1(Instr[25:21]), .A2(Instr[20:16]), .A3(RegAddr), .WD(RegData), .clk(clk), .reset(Reset),
    .we(RegWrite), .RD1(input1), .RD2(MemData));
  Multiplexer #(.width(5), .enable("false")) multiplexer_3 (
    .in0(Instr[20:16]), .in1(Instr[15:11]), .out(RegAddr), .sel(RegDst));
  Multiplexer #(.width(32), .enable("false")) multiplexer_4 (
    .in0(SignedExt), .in1(SignedExt), .out(multiplexer_4_out), .sel(Exten_Sign));
  Multiplexer #(.width(32), .enable("false")) multiplexer_5 (
    .in0(MemData), .in1(multiplexer_4_out), .out(input2), .sel(ALUSrc));
  ALU alu_1 (
    .input1(input1), .input2(input2), .ALU_OP(ALU_OP), .zero(ALU_ZERO),
    .result({ALU_result[31:7], MemAddr, ALU_result[1:0]}));
  Multiplexer #(.width(32), .enable("false")) multiplexer_6 (
    .in0({ALU_result[31:7], MemAddr, ALU_result[1:0]}), .in1(DM_OUT), .out(RegData), .sel(MemtoReg));
  RAM #(.addrWidth(5), .dataWidth(32), .bus("separate")) ram_1 (
    .addr(MemAddr), .din(MemData), .data(DM_OUT), .str(MemWrite), .clk(clk), .ld(MemRead), .clr(Reset));  // open: sel

  // Other names for the same wires on the sheet: func[5:0] = Instr[5:0]; IM_out[31:0] = Instr;
  //   imm16[15:0] = Instr[15:0]; instr_t[25:0] = Instr[25:0]; s[4:0] = Instr[10:6]; rd[4:0] = Instr[15:11];
  //   rt[4:0] = Instr[20:16]; rs[4:0] = Instr[25:21]; op[5:0] = Instr[31:26]; PC31_28[3:0] = Instr[31:28];
  //   RD1[31:0] = input1; MemAddr_t[31:0] = {ALU_result[31:7], MemAddr, ALU_result[1:0]}; ALU_result[6:2] = MemAddr;
  //   RD2[31:0] = MemData; ZeroExt[31:0] = SignedExt

  // Notes on the sheet:
  //   PC
  //   op
  //   rs
  //   rt
  //   rd
  //   s
  //   imm16
  //   func
  //   instr
  //   contents of rom_1 (hex, n*v repeats v):
  //   34090004 ac090008 8c0a0008 12a5821 1406023 8000c07 0 112a0001 0 16a5821 8000c07
  //   IM
endmodule

module PC (
  input  [31:0] init,
  input  [31:0] D,
  input  en,
  input  clk,
  input  rst,
  output [31:0] Q
);

  wire counter_1_carry;
  wire [31:0] multiplexer_1_out, register_1_q;

  Pull_Resistor #(.pull(1)) pull_resistor_1 (.node(en));
  Multiplexer #(.width(32), .enable("false")) multiplexer_1 (.in0(Q), .in1(D), .out(multiplexer_1_out), .sel(en));
  Register #(.width(32)) register_1 (.D(multiplexer_1_out), .Q(register_1_q), .clk(clk), .clr(rst));  // open: en
  Counter #(.width(1), .max('h1), .ongoal("stay")) counter_1 (
    .carry(counter_1_carry), .clk(clk), .clr(rst));  // open: load, D, count, Q
  Pull_Resistor pull_resistor_2 (.node(init));
  Multiplexer #(.width(32), .enable("false")) multiplexer_2 (
    .in0(init), .in1(register_1_q), .out(Q), .sel(counter_1_carry));
endmodule

// ADD4
module Add4 (
  input  [31:0] in,
  output [31:0] out
);

  Adder #(.width(32)) adder_1 (.a(in), .b(32'h4), .out(out));  // open: cin, cout
endmodule

module ALU (
  input  [31:0] input1,
  input  [31:0] input2,
  input  [3:0] ALU_OP,
  output zero,
  output [31:0] result
);

  wire adder_1_cout;
  wire [31:0] adder_1_out, or_1_out, subtractor_1_out;

  assign or_1_out = input1 | input2;  // OR_Gate or_1, 32 bits wide
  Adder #(.width(32)) adder_1 (.a(input1), .b(input2), .out(adder_1_out), .cout(adder_1_cout));  // open: cin
  Subtractor #(.width(32)) subtractor_1 (
    .a(input1), .b(input2), .out(subtractor_1_out), .bin(adder_1_cout));  // open: bout
  Multiplexer #(.select(4), .width(32), .enable("false")) multiplexer_1 (
    .in1(or_1_out), .in2(adder_1_out), .in6(subtractor_1_out), .out(result), .sel(ALU_OP));  // open: in0, in3, in4, in5, in7, in8, in9, in10, in11, in12, in13, in14, in15
  Comparator #(.width(32)) comparator_1 (.a({32{1'b0}}), .b(result), .eq(zero));  // open: gt, lt
endmodule

module Controller (
  input  [5:0] OP,
  input  [5:0] FUNC,
  output [3:0] ALU_OP,
  output Exten_Signal,
  output RegDst,
  output RegWrite,
  output ALUSrc,
  output PCSrc,
  output MemRead,
  output MemWrite,
  output MemtoReg,
  output branch
);

  wire addu, j, or_1_out, or_2_out, or_3_out, ori, subu;
  wire [3:0] add_op, or_op, sub_op;

  and R_type (RegDst, ~OP[0], ~OP[1], ~OP[2], ~OP[3], ~OP[4], ~OP[5]);  // AND_Gate
  and u_ADDU (addu, RegDst, FUNC[0], ~FUNC[1], ~FUNC[2], ~FUNC[3], ~FUNC[4], FUNC[5]);  // AND_Gate
  and lw (MemRead, OP[0], OP[1], ~OP[2], ~OP[3], ~OP[4], OP[5]);  // AND_Gate
  Multiplexer #(.width(4), .enable("false")) multiplexer_1 (.in0(4'b0000), .in1(4'b0010), .out(add_op), .sel(or_1_out));
  or or_1 (or_1_out, MemRead, MemWrite, addu);
  and u_SUBU (subu, RegDst, FUNC[0], FUNC[1], ~FUNC[2], ~FUNC[3], ~FUNC[4], FUNC[5]);  // AND_Gate
  and sw (MemWrite, OP[0], OP[1], ~OP[2], OP[3], ~OP[4], OP[5]);  // AND_Gate
  and u_ori (ori, OP[0], ~OP[1], OP[2], OP[3], ~OP[4], ~OP[5]);  // AND_Gate
  Multiplexer #(.width(4), .enable("false")) multiplexer_2 (.in0(4'b0000), .in1(4'b0110), .out(sub_op), .sel(or_2_out));
  or or_2 (or_2_out, subu, branch);
  and u_j (j, ~OP[0], OP[1], ~OP[2], ~OP[3], ~OP[4], ~OP[5]);  // AND_Gate
  and beq (branch, ~OP[0], ~OP[1], OP[2], ~OP[3], ~OP[4], ~OP[5]);  // AND_Gate
  Multiplexer #(.width(4), .enable("false")) multiplexer_3 (.in0(4'b0000), .in1(4'b0001), .out(or_op), .sel(or_3_out));
  buf or_3 (or_3_out, ori);  // OR_Gate
  assign ALU_OP = add_op | sub_op | or_op;  // OR_Gate or_4, 4 bits wide
  or or_5 (Exten_Signal, MemRead, MemWrite);
  or or_6 (RegWrite, MemRead, ori, addu, subu);
  or or_7 (PCSrc, j, branch);
  or or_8 (ALUSrc, MemRead, MemWrite, ori);

  assign MemtoReg = MemRead;

  // Other names for the same wires on the sheet: beq = branch; lw = MemRead; R = RegDst; sw = MemWrite
endmodule

// NPC
module Brancher (
  input  PCSrc,
  input  branch,
  input  ALUZERO,
  output \output 
);

  wire and_1_out, and_2_out, not_1_out;

  not not_1 (not_1_out, branch);
  and and_1 (and_1_out, PCSrc, not_1_out);
  and and_2 (and_2_out, PCSrc, ALUZERO);
  or or_1 (\output , and_1_out, and_2_out);
endmodule

module GRF (
  input  [4:0] A1,
  input  clk,
  input  reset,
  input  we,
  input  [4:0] A2,
  input  [4:0] A3,
  input  [31:0] WD,
  output [31:0] RD1,
  output [31:0] RD2
);

  wire [31:0] I0, I1, I2, I3, I4, I5, I6, I7, I8, I9, I10, I11, I12, I13, I14, I15, I16, I17, I18, I19, I20,
       I21, I22, I23, I24, I25, I26, I27, I28, I29, I30, I31, O0, O1, O2, O3, O4, O5, O6, O7, O8, O9, O10,
       O11, O12, O13, O14, O15, O16, O17, O18, O19, O20, O21, O22, O23, O24, O25, O26, O27, O28, O29, O30,
       O31;

  Demultiplexer #(.select(5), .width(32), .tristate("true")) demultiplexer_1 (
    .out0(I0), .out1(I1), .out2(I2), .out3(I3), .out4(I4), .out5(I5), .out6(I6), .out7(I7), .out8(I8),
    .out9(I9), .out10(I10), .out11(I11), .out12(I12), .out13(I13), .out14(I14), .out15(I15), .out16(I16),
    .out17(I17), .out18(I18), .out19(I19), .out20(I20), .out21(I21), .out22(I22), .out23(I23), .out24(I24),
    .out25(I25), .out26(I26), .out27(I27), .out28(I28), .out29(I29), .out30(I30), .out31(I31), .in(WD),
    .sel(A3));  // open: en
  Multiplexer #(.select(5), .width(32)) multiplexer_1 (
    .in0(O0), .in1(O1), .in2(O2), .in3(O3), .in4(O4), .in5(O5), .in6(O6), .in7(O7), .in8(O8), .in9(O9),
    .in10(O10), .in11(O11), .in12(O12), .in13(O13), .in14(O14), .in15(O15), .in16(O16), .in17(O17),
    .in18(O18), .in19(O19), .in20(O20), .in21(O21), .in22(O22), .in23(O23), .in24(O24), .in25(O25),
    .in26(O26), .in27(O27), .in28(O28), .in29(O29), .in30(O30), .in31(O31), .out(RD2), .sel(A2));  // open: en
  Multiplexer #(.select(5), .width(32)) multiplexer_2 (
    .in0(O0), .in1(O1), .in2(O2), .in3(O3), .in4(O4), .in5(O5), .in6(O6), .in7(O7), .in8(O8), .in9(O9),
    .in10(O10), .in11(O11), .in12(O12), .in13(O13), .in14(O14), .in15(O15), .in16(O16), .in17(O17),
    .in18(O18), .in19(O19), .in20(O20), .in21(O21), .in22(O22), .in23(O23), .in24(O24), .in25(O25),
    .in26(O26), .in27(O27), .in28(O28), .in29(O29), .in30(O30), .in31(O31), .out(RD1), .sel(A1));  // open: en
  Register #(.width(32)) register_1 (.D({32{1'b0}}), .en(we), .Q(O0), .clk(clk), .clr(reset));
  Register #(.width(32)) register_2 (.D(I8), .en(we), .Q(O8), .clk(clk), .clr(reset));
  Register #(.width(32)) register_3 (.D(I16), .en(we), .Q(O16), .clk(clk), .clr(reset));
  Register #(.width(32)) register_4 (.D(I24), .en(we), .Q(O24), .clk(clk), .clr(reset));
  Register #(.width(32)) register_5 (.D(I1), .en(we), .Q(O1), .clk(clk), .clr(reset));
  Register #(.width(32)) register_6 (.D(I9), .en(we), .Q(O9), .clk(clk), .clr(reset));
  Register #(.width(32)) register_7 (.D(I17), .en(we), .Q(O17), .clk(clk), .clr(reset));
  Register #(.width(32)) register_8 (.D(I25), .en(we), .Q(O25), .clk(clk), .clr(reset));
  Register #(.width(32)) register_9 (.D(I2), .en(we), .Q(O2), .clk(clk), .clr(reset));
  Register #(.width(32)) register_10 (.D(I10), .en(we), .Q(O10), .clk(clk), .clr(reset));
  Register #(.width(32)) register_11 (.D(I18), .en(we), .Q(O18), .clk(clk), .clr(reset));
  Register #(.width(32)) register_12 (.D(I26), .en(we), .Q(O26), .clk(clk), .clr(reset));
  Register #(.width(32)) register_13 (.D(I3), .en(we), .Q(O3), .clk(clk), .clr(reset));
  Register #(.width(32)) register_14 (.D(I11), .en(we), .Q(O11), .clk(clk), .clr(reset));
  Register #(.width(32)) register_15 (.D(I19), .en(we), .Q(O19), .clk(clk), .clr(reset));
  Register #(.width(32)) register_16 (.D(I27), .en(we), .Q(O27), .clk(clk), .clr(reset));
  Register #(.width(32)) register_17 (.D(I4), .en(we), .Q(O4), .clk(clk), .clr(reset));
  Register #(.width(32)) register_18 (.D(I12), .en(we), .Q(O12), .clk(clk), .clr(reset));
  Register #(.width(32)) register_19 (.D(I20), .en(we), .Q(O20), .clk(clk), .clr(reset));
  Register #(.width(32)) register_20 (.D(I28), .en(we), .Q(O28), .clk(clk), .clr(reset));
  Register #(.width(32)) register_21 (.D(I5), .en(we), .Q(O5), .clk(clk), .clr(reset));
  Register #(.width(32)) register_22 (.D(I13), .en(we), .Q(O13), .clk(clk), .clr(reset));
  Register #(.width(32)) register_23 (.D(I21), .en(we), .Q(O21), .clk(clk), .clr(reset));
  Register #(.width(32)) register_24 (.D(I29), .en(we), .Q(O29), .clk(clk), .clr(reset));
  Register #(.width(32)) register_25 (.D(I6), .en(we), .Q(O6), .clk(clk), .clr(reset));
  Register #(.width(32)) register_26 (.D(I14), .en(we), .Q(O14), .clk(clk), .clr(reset));
  Register #(.width(32)) register_27 (.D(I22), .en(we), .Q(O22), .clk(clk), .clr(reset));
  Register #(.width(32)) register_28 (.D(I30), .en(we), .Q(O30), .clk(clk), .clr(reset));
  Register #(.width(32)) register_29 (.D(I7), .en(we), .Q(O7), .clk(clk), .clr(reset));
  Register #(.width(32)) register_30 (.D(I15), .en(we), .Q(O15), .clk(clk), .clr(reset));
  Register #(.width(32)) register_31 (.D(I23), .en(we), .Q(O23), .clk(clk), .clr(reset));
  Register #(.width(32)) register_32 (.D(I31), .en(we), .Q(O31), .clk(clk), .clr(reset));
endmodule
