// Logisim project CPU_pipeline_perfect.circ as structural Verilog: 14 circuits, main circuit main
module main (
  input  in_1,
  output [31:0] out_2,
  output out_3,
  output [4:0] out_4,
  output [31:0] out_5,
  output out_6,
  output [4:0] out_7,
  output [31:0] out_8
);

  wire addu, ALUSrc, beq, branch_beq, branch_j_jal, branch_jr, clk, de_reg_1_alusrc_o, de_reg_1_memread_o,
       de_reg_1_memwrite_o, de_reg_1_regwrite_o, eql, j, jal, jr, lb, lh, lui, lw, Mem_MemRead, Mem_MemWrite,
       Mem_RegWrite, MemRead, MemWrite, nop, ori, RegWrite, s, sb, sh, subu, undriven, undriven_2;
  wire [1:0] ALUop, de_reg_1_aluop_o, de_reg_1_memtoreg_o, de_reg_1_regdst_o, EXTop, Lsel, Mem_MemtoReg,
       MemtoReg, mw_reg_1_out_17, RegDst, Ssel;
  wire [3:0] high4;
  wire [4:0] de_reg_1_rd_o, de_reg_1_rt_o, Mem_WriteReg, multiplexer_1_out, Shamt_shift, Splitter_out_4,
       Splitter_out_5, Splitter_out_6;
  wire [5:0] func, Op;
  wire [15:0] imm16;
  wire [23:0] pc_1_instraddr;
  wire [25:0] j_imm26;
  wire [27:0] adder_1_out, bit_extender_1_out, jumpAddr;
  wire [31:0] adder_2_out, ALU_out_5, de_reg_1_extresult_o, de_reg_1_instr_o, de_reg_1_pc_4_o,
       de_reg_1_pc_8_o, de_reg_1_pc_o, de_reg_1_rd1_o, de_reg_1_rd2_o, dm_1_rd, em_reg_1_out_20,
       em_reg_1_out_21, em_reg_1_out_26, em_reg_1_pc_4_o, em_reg_1_pc_8_o, em_reg_1_pc_o, EXTresult,
       fd_reg_1_instr_o, fd_reg_1_pc_4_o, fd_reg_1_pc_8_o, fd_reg_1_pc_o, grf_1_rd1, grf_1_rd2, MemAddr,
       multiplexer_2_out, mw_reg_1_out_18, mw_reg_1_out_20, mw_reg_1_pc_8_o, npc_1_out_10, pc_1_pc;

  Clock clock_1 (.out(clk));
  PC pc_1 (.NPC(npc_1_out_10), .InstrAddr(pc_1_instraddr), .PC(pc_1_pc), .StalIF(undriven), .CLK(clk), .reset(in_1));
  ROM #(.addrWidth(24), .dataWidth(32)) rom_1 (.addr(pc_1_instraddr), .data(out_2));  // open: sel
  Adder #(.width(32)) adder_1 (.a(pc_1_pc), .b(32'h4), .out({high4, adder_1_out}));  // open: cin, cout
  Adder #(.width(32)) adder_2 (.a(pc_1_pc), .b(32'h8), .out(adder_2_out));  // open: cin, cout
  UseFunc UseFunc (
    .Op(Op), .func(func), .out_3(lw), .out_4(s), .out_5(addu), .out_6(subu), .out_7(ori), .out_8(lui),
    .out_9(j), .out_10(jal), .out_11(jr), .out_12(beq), .out_13(nop), .out_14(lh), .out_15(sh), .out_16(lb),
    .out_17(sb));
  FD_Reg fd_reg_1 (
    .instr_i(out_2), .pc_i(pc_1_pc), .pc_4_i({high4, adder_1_out}), .pc_8_i(adder_2_out),
    .instr_o(fd_reg_1_instr_o), .pc_o(fd_reg_1_pc_o), .pc_4_o(fd_reg_1_pc_4_o), .pc_8_o(fd_reg_1_pc_8_o),
    .in_1(clk), .in_2(in_1), .in_7(undriven_2));
  NPC npc_1 (
    .PC_4({high4, adder_1_out}), .PC(pc_1_pc), .EXTresult_imm32(EXTresult), .j_jal_Addr({high4, jumpAddr}),
    .out_10(npc_1_out_10), .B_beq(branch_beq), .B_j_jal(branch_j_jal), .B_jr(branch_jr), .equal(eql));  // open: RegData
  splitter Splitter (
    .in_1(fd_reg_1_instr_o), .out_2(func), .out_3(Shamt_shift), .out_4(Splitter_out_4),
    .out_5(Splitter_out_5), .out_6(Splitter_out_6), .out_7(Op), .out_8(imm16), .out_9(j_imm26));
  assign bit_extender_1_out = {{2{1'b0}}, j_imm26};  // Bit_Extender bit_extender_1
  Controller Controller (
    .Op(Op), .func(func), .RegDst(RegDst), .MemWrite(MemWrite), .branch_beq(branch_beq),
    .branch_j_jal(branch_j_jal), .branch_jr(branch_jr), .EXTop(EXTop), .RegWrite(RegWrite), .ALUSrc(ALUSrc),
    .MemRead(MemRead), .MemtoReg(MemtoReg), .ALUop(ALUop), .Ssel(Ssel), .Lsel(Lsel));
  EXT EXT (.in_1(imm16), .out_3(EXTresult), .in_2(EXTop));
  Shifter #(.width(28)) shifter_1 (.in(bit_extender_1_out), .\dist (5'b00010), .out(jumpAddr));
  GRF grf_1 (
    .A1(Splitter_out_6), .A2(Splitter_out_5), .A3(out_4), .WD(out_5), .RD1(grf_1_rd1), .RD2(grf_1_rd2),
    .clk(clk), .reset(in_1), .we(out_3));
  DE_Reg de_reg_1 (
    .RegDst_i(RegDst), .MemWrite_i(MemWrite), .RegWrite_i(RegWrite), .ALUSrc_i(ALUSrc), .MemRead_i(MemRead),
    .MemToReg_i(MemtoReg), .ALUop_i(ALUop), .RD1_i(grf_1_rd1), .RD2_i(grf_1_rd2), .rs_i(Splitter_out_6),
    .rt_i(Splitter_out_5), .rd_i(Splitter_out_4), .pc_i(fd_reg_1_pc_o), .pc_4_i(fd_reg_1_pc_4_o),
    .pc_8_i(fd_reg_1_pc_8_o), .EXTresult_i(EXTresult), .instr_i(fd_reg_1_instr_o),
    .RegDst_o(de_reg_1_regdst_o), .MemWrite_o(de_reg_1_memwrite_o), .RegWrite_o(de_reg_1_regwrite_o),
    .ALUSrc_o(de_reg_1_alusrc_o), .MemRead_o(de_reg_1_memread_o), .MemToReg_o(de_reg_1_memtoreg_o),
    .ALUop_o(de_reg_1_aluop_o), .RD1_o(de_reg_1_rd1_o), .RD2_o(de_reg_1_rd2_o), .rt_o(de_reg_1_rt_o),
    .rd_o(de_reg_1_rd_o), .pc_o(de_reg_1_pc_o), .pc_4_o(de_reg_1_pc_4_o), .pc_8_o(de_reg_1_pc_8_o),
    .EXTresult_o(de_reg_1_extresult_o), .instr_o(de_reg_1_instr_o), .in_1(clk), .in_2(in_1), .in_12(1'b0));  // open: rs_o
  Multiplexer #(.select(2), .width(5), .enable("false")) multiplexer_1 (
    .in0(de_reg_1_rt_o), .in1(de_reg_1_rd_o), .in2({5{1'b1}}), .out(multiplexer_1_out),
    .sel(de_reg_1_regdst_o));  // open: in3
  Multiplexer #(.width(32), .enable("false")) multiplexer_2 (
    .in0(de_reg_1_rd2_o), .in1(de_reg_1_extresult_o), .out(multiplexer_2_out), .sel(de_reg_1_alusrc_o));
  ALU ALU (.in_1(de_reg_1_rd1_o), .in_2(multiplexer_2_out), .Zero(eql), .out_5(ALU_out_5), .ALUOP(de_reg_1_aluop_o));
  EM_Reg em_reg_1 (
    .MemWrite_i(de_reg_1_memwrite_o), .RegWrite_i(de_reg_1_regwrite_o), .MemRead_i(de_reg_1_memread_o),
    .MemToReg_i(de_reg_1_memtoreg_o), .aluresult_i(ALU_out_5), .writedata_i(de_reg_1_rd2_o),
    .writereg_i(multiplexer_1_out), .pc_i(de_reg_1_pc_o), .pc_4_i(de_reg_1_pc_4_o), .pc_8_i(de_reg_1_pc_8_o),
    .instr_i(de_reg_1_instr_o), .MemWrite_o(Mem_MemWrite), .RegWrite_o(Mem_RegWrite),
    .MemRead_o(Mem_MemRead), .MemToReg_o(Mem_MemtoReg), .out_20(em_reg_1_out_20), .out_21(em_reg_1_out_21),
    .out_22(Mem_WriteReg), .pc_o(em_reg_1_pc_o), .pc_4_o(em_reg_1_pc_4_o), .pc_8_o(em_reg_1_pc_8_o),
    .out_26(em_reg_1_out_26), .in_1(clk), .in_2(in_1));  // open: tnew_E, tnew_M
  DM dm_1 (
    .SSel(Ssel), .Lsel(Lsel), .Addr(em_reg_1_out_20), .WriteData(em_reg_1_out_21), .RD(dm_1_rd),
    .in_4(Mem_MemWrite), .in_5(clk), .in_6(Mem_MemRead), .in_7(in_1));
  MW_Reg mw_reg_1 (
    .aluresult_i(em_reg_1_out_20), .writedata_i(em_reg_1_out_21), .readdata_i(dm_1_rd), .pc_i(em_reg_1_pc_o),
    .pc_4_i(em_reg_1_pc_4_o), .pc_8_i(em_reg_1_pc_8_o), .instr_i(em_reg_1_out_26), .memaddr(em_reg_1_out_20),
    .memdata(em_reg_1_out_21), .memwrite(Mem_MemWrite), .out_18(mw_reg_1_out_18), .out_20(mw_reg_1_out_20),
    .pc_8_o(mw_reg_1_pc_8_o), .out_26({MemAddr[31:7], out_7, MemAddr[1:0]}), .out_27(out_8), .out_28(out_6),
    .in_1(clk), .in_2(in_1), .writereg_i(Mem_WriteReg), .out_25(out_4), .MemtoReg(Mem_MemtoReg),
    .out_17(mw_reg_1_out_17), .RegWrite(Mem_RegWrite), .out_16(out_3));  // open: out_19, pc_o, pc_4_o, out_24
  // Probe on mw_reg_1_out_17
  Multiplexer #(.select(2), .width(32), .enable("false")) multiplexer_3 (
    .in0(mw_reg_1_out_18), .in1(mw_reg_1_out_20), .in2(mw_reg_1_pc_8_o), .out(out_5), .sel(mw_reg_1_out_17));  // open: in3

  // Other names for the same wires on the sheet: instr[31:0] = out_2; jumpAddr[31:28] = high4; MemAddr[6:2] = out_7;
  //   MemData[31:0] = out_8; memWriteFinal = out_6; RegAddr[4:0] = out_4; RegData[31:0] = out_5;
  //   regWriteFinal = out_3; reset = in_1

  // Notes on the sheet:
  //   contents of rom_1 (hex, n*v repeats v):
  //   3c110001 3c120002 3c130003 3c140004 36310001 36520002 36730003 36940004 ac110000 ac120004 ac130008
  //   ac14000c 8c150000 8c160004 8c170008 8c18000c
endmodule

module PC (
  input  [31:0] NPC,
  input  StalIF,
  input  CLK,
  input  reset,
  output [23:0] InstrAddr,
  output [31:0] PC
);

  wire comparator_1_eq;
  wire [31:0] register_1_q, subtractor_1_out;

  Register #(.width(32)) register_1 (.D(NPC), .en(StalIF), .Q(register_1_q), .clk(CLK), .clr(reset));
  Comparator #(.width(32)) comparator_1 (.a(register_1_q), .b({32{1'b0}}), .eq(comparator_1_eq));  // open: gt, lt
  Multiplexer #(.width(32), .enable("false")) multiplexer_1 (
    .in0(register_1_q), .in1(32'h3000), .out(PC), .sel(comparator_1_eq));
  Subtractor #(.width(32)) subtractor_1 (
    .a(PC), .b(32'h3000), .out({subtractor_1_out[31:26], InstrAddr, subtractor_1_out[1:0]}));  // open: bin, bout
endmodule

module NPC (
  input  B_beq,
  input  B_j_jal,
  input  B_jr,
  input  equal,
  input  [31:0] PC_4,
  input  [31:0] PC,
  input  [31:0] EXTresult_imm32,
  input  [31:0] j_jal_Addr,
  input  [31:0] RegData,
  output [31:0] out_10
);

  wire and_1_out;
  wire [1:0] NPCop;
  wire [31:0] adder_1_out, shifter_1_out;

  and and_1 (and_1_out, equal, B_beq);
  Shifter #(.width(32)) shifter_1 (.in(EXTresult_imm32), .\dist (5'b00010), .out(shifter_1_out));
  or or_1 (NPCop[0], and_1_out, B_jr);
  or or_2 (NPCop[1], B_j_jal, B_jr);
  Adder #(.width(32)) adder_1 (.a(shifter_1_out), .b(PC_4), .out(adder_1_out));  // open: cin, cout
  Multiplexer #(.select(2), .width(32), .enable("false")) multiplexer_1 (
    .in0(PC_4), .in1(adder_1_out), .in2(j_jal_Addr), .in3(RegData), .out(out_10), .sel(NPCop));

  // Other names for the same wires on the sheet: eql = equal

  // Notes on the sheet:
  //   beq
endmodule

module splitter (
  input  [31:0] in_1,
  output [5:0] out_2,
  output [4:0] out_3,
  output [4:0] out_4,
  output [4:0] out_5,
  output [4:0] out_6,
  output [5:0] out_7,
  output [15:0] out_8,
  output [25:0] out_9
);


  assign out_2 = in_1[5:0];
  assign out_3 = in_1[10:6];
  assign out_4 = in_1[15:11];
  assign out_5 = in_1[20:16];
  assign out_6 = in_1[25:21];
  assign out_7 = in_1[31:26];
  assign out_8 = in_1[15:0];
  assign out_9 = in_1[25:0];

  // Notes on the sheet:
  //   Func 0-5
  //   Shamt 6-10
  //   Rt 16-20
  //   Rd 11-15
  //   Rs 21-25
  //   Op 26-31
  //   16bit Immediate
  //   26 bir address for jump
endmodule

module GRF (
  input  [4:0] A1,
  input  clk,
  input  reset,
  input  we,
  input  [4:0] A2,
  input  [4:0] A3,
  input  [31:0] WD,
  output [31:0] RD1,
  output [31:0] RD2
);

  wire [31:0] I0, I1, I2, I3, I4, I5, I6, I7, I8, I9, I10, I11, I12, I13, I14, I15, I16, I17, I18, I19, I20,
       I21, I22, I23, I24, I25, I26, I27, I28, I29, I30, I31, O0, O1, O2, O3, O4, O5, O6, O7, O8, O9, O10,
       O11, O12, O13, O14, O15, O16, O17, O18, O19, O20, O21, O22, O23, O24, O25, O26, O27, O28, O29, O30,
       O31;

  Demultiplexer #(.select(5), .width(32), .tristate("true")) demultiplexer_1 (
    .out0(I0), .out1(I1), .out2(I2), .out3(I3), .out4(I4), .out5(I5), .out6(I6), .out7(I7), .out8(I8),
    .out9(I9), .out10(I10), .out11(I11), .out12(I12), .out13(I13), .out14(I14), .out15(I15), .out16(I16),
    .out17(I17), .out18(I18), .out19(I19), .out20(I20), .out21(I21), .out22(I22), .out23(I23), .out24(I24),
    .out25(I25), .out26(I26), .out27(I27), .out28(I28), .out29(I29), .out30(I30), .out31(I31), .in(WD),
    .sel(A3));  // open: en
  Multiplexer #(.select(5), .width(32)) multiplexer_1 (
    .in0(O0), .in1(O1), .in2(O2), .in3(O3), .in4(O4), .in5(O5), .in6(O6), .in7(O7), .in8(O8), .in9(O9),
    .in10(O10), .in11(O11), .in12(O12), .in13(O13), .in14(O14), .in15(O15), .in16(O16), .in17(O17),
    .in18(O18), .in19(O19), .in20(O20), .in21(O21), .in22(O22), .in23(O23), .in24(O24), .in25(O25),
    .in26(O26), .in27(O27), .in28(O28), .in29(O29), .in30(O30), .in31(O31), .out(RD2), .sel(A2));  // open: en
  Multiplexer #(.select(5), .width(32)) multiplexer_2 (
    .in0(O0), .in1(O1), .in2(O2), .in3(O3), .in4(O4), .in5(O5), .in6(O6), .in7(O7), .in8(O8), .in9(O9),
    .in10(O10), .in11(O11), .in12(O12), .in13(O13), .in14(O14), .in15(O15), .in16(O16), .in17(O17),
    .in18(O18), .in19(O19), .in20(O20), .in21(O21), .in22(O22), .in23(O23), .in24(O24), .in25(O25),
    .in26(O26), .in27(O27), .in28(O28), .in29(O29), .in30(O30), .in31(O31), .out(RD1), .sel(A1));  // open: en
  Register #(.width(32)) register_1 (.D({32{1'b0}}), .en(we), .Q(O0), .clk(clk), .clr(reset));
  Register #(.width(32)) register_2 (.D(I8), .en(we), .Q(O8), .clk(clk), .clr(reset));
  Register #(.width(32)) register_3 (.D(I16), .en(we), .Q(O16), .clk(clk), .clr(reset));
  Register #(.width(32)) register_4 (.D(I24), .en(we), .Q(O24), .clk(clk), .clr(reset));
  Register #(.width(32)) register_5 (.D(I1), .en(we), .Q(O1), .clk(clk), .clr(reset));
  Register #(.width(32)) register_6 (.D(I9), .en(we), .Q(O9), .clk(clk), .clr(reset));
  Register #(.width(32)) register_7 (.D(I17), .en(we), .Q(O17), .clk(clk), .clr(reset));
  Register #(.width(32)) register_8 (.D(I25), .en(we), .Q(O25), .clk(clk), .clr(reset));
  Register #(.width(32)) register_9 (.D(I2), .en(we), .Q(O2), .clk(clk), .clr(reset));
  Register #(.width(32)) register_10 (.D(I10), .en(we), .Q(O10), .clk(clk), .clr(reset));
  Register #(.width(32)) register_11 (.D(I18), .en(we), .Q(O18), .clk(clk), .clr(reset));
  Register #(.width(32)) register_12 (.D(I26), .en(we), .Q(O26), .clk(clk), .clr(reset));
  Register #(.width(32)) register_13 (.D(I3), .en(we), .Q(O3), .clk(clk), .clr(reset));
  Register #(.width(32)) register_14 (.D(I11), .en(we), .Q(O11), .clk(clk), .clr(reset));
  Register #(.width(32)) register_15 (.D(I19), .en(we), .Q(O19), .clk(clk), .clr(reset));
  Register #(.width(32)) register_16 (.D(I27), .en(we), .Q(O27), .clk(clk), .clr(reset));
  Register #(.width(32)) register_17 (.D(I4), .en(we), .Q(O4), .clk(clk), .clr(reset));
  Register #(.width(32)) register_18 (.D(I12), .en(we), .Q(O12), .clk(clk), .clr(reset));
  Register #(.width(32)) register_19 (.D(I20), .en(we), .Q(O20), .clk(clk), .clr(reset));
  Register #(.width(32)) register_20 (.D(I28), .en(we), .Q(O28), .clk(clk), .clr(reset));
  Register #(.width(32)) register_21 (.D(I5), .en(we), .Q(O5), .clk(clk), .clr(reset));
  Register #(.width(32)) register_22 (.D(I13), .en(we), .Q(O13), .clk(clk), .clr(reset));
  Register #(.width(32)) register_23 (.D(I21), .en(we), .Q(O21), .clk(clk), .clr(reset));
  Register #(.width(32)) register_24 (.D(I29), .en(we), .Q(O29), .clk(clk), .clr(reset));
  Register #(.width(32)) register_25 (.D(I6), .en(we), .Q(O6), .clk(clk), .clr(reset));
  Register #(.width(32)) register_26 (.D(I14), .en(we), .Q(O14), .clk(clk), .clr(reset));
  Register #(.width(32)) register_27 (.D(I22), .en(we), .Q(O22), .clk(clk), .clr(reset));
  Register #(.width(32)) register_28 (.D(I30), .en(we), .Q(O30), .clk(clk), .clr(reset));
  Register #(.width(32)) register_29 (.D(I7), .en(we), .Q(O7), .clk(clk), .clr(reset));
  Register #(.width(32)) register_30 (.D(I15), .en(we), .Q(O15), .clk(clk), .clr(reset));
  Register #(.width(32)) register_31 (.D(I23), .en(we), .Q(O23), .clk(clk), .clr(reset));
  Register #(.width(32)) register_32 (.D(I31), .en(we), .Q(O31), .clk(clk), .clr(reset));
endmodule

module Controller (
  input  [5:0] Op,
  input  [5:0] func,
  output [1:0] RegDst,
  output MemWrite,
  output branch_beq,
  output branch_j_jal,
  output branch_jr,
  output [1:0] EXTop,
  output RegWrite,
  output ALUSrc,
  output MemRead,
  output [1:0] MemtoReg,
  output [1:0] ALUop,
  output [1:0] Ssel,
  output [1:0] Lsel
);

  wire addu, beq, j, jal, jr, lb, lh, lui, lw, nop, not_1_out, not_2_out, not_3_out, not_4_out, not_5_out,
       not_6_out, not_7_out, not_8_out, not_9_out, not_10_out, not_11_out, not_12_out, ori, r, sb, sh, subu,
       sw;

  not not_1 (not_1_out, Op[5]);
  not not_2 (not_2_out, Op[3]);
  not not_3 (not_3_out, Op[4]);
  not not_4 (not_4_out, Op[2]);
  not not_5 (not_5_out, Op[1]);
  not not_6 (not_6_out, Op[0]);
  and u_LW (lw, Op[5], not_3_out, not_2_out, not_4_out, Op[1], Op[0]);
  and u_SW (sw, Op[5], not_3_out, Op[3], not_4_out, Op[1], Op[0]);
  and u_R (r, not_1_out, not_3_out, not_2_out, not_4_out, not_5_out, not_6_out);
  and u_ORI (ori, not_1_out, not_3_out, Op[3], Op[2], not_5_out, Op[0]);
  and u_J (j, not_1_out, not_3_out, not_2_out, not_4_out, Op[1], not_6_out);
  and u_JAL (jal, not_1_out, not_3_out, not_2_out, not_4_out, Op[1], Op[0]);
  and u_BEQ (beq, not_1_out, not_3_out, not_2_out, Op[2], not_5_out, not_6_out);
  and u_LUI (lui, not_1_out, not_3_out, Op[3], Op[2], Op[1], Op[0]);
  and u_LH (lh, Op[5], not_3_out, not_2_out, not_4_out, not_5_out, Op[0]);
  and u_SH (sh, Op[5], not_3_out, Op[3], not_4_out, not_5_out, Op[0]);
  and u_LB (lb, Op[5], not_3_out, not_2_out, not_4_out, not_5_out, not_6_out);
  and u_SB (sb, Op[5], not_3_out, Op[3], not_4_out, not_5_out, not_6_out);
  not not_7 (not_7_out, func[5]);
  not not_8 (not_8_out, func[3]);
  not not_9 (not_9_out, func[4]);
  not not_10 (not_10_out, func[1]);
  not not_11 (not_11_out, func[2]);
  not not_12 (not_12_out, func[0]);
  and u_ADDU (addu, r, func[5], not_9_out, not_8_out, not_11_out, not_10_out, func[0]);
  and u_SUBU (subu, r, func[5], not_9_out, not_8_out, not_11_out, func[1], func[0]);
  and u_JR (jr, r, not_7_out, not_9_out, func[3], not_11_out, not_10_out, not_12_out);
  and u_NOP (nop, r, not_7_out, not_9_out, not_8_out, not_11_out, not_10_out, not_12_out);
  buf or_1 (RegDst[0], r);  // OR_Gate
  buf or_2 (RegDst[1], jal);  // OR_Gate
  or or_3 (MemWrite, sw, sh, sb);
  buf or_4 (branch_beq, beq);  // OR_Gate
  or or_5 (branch_j_jal, j, jal);
  buf or_6 (branch_jr, jr);  // OR_Gate
  or or_7 (EXTop[0], lw, sw);
  buf or_8 (EXTop[1], lui);  // OR_Gate
  or or_9 (RegWrite, lui, ori, r, lw);
  or or_10 (ALUSrc, lw, sw, ori, lui);
  or or_11 (MemRead, sh, lw, sb);
  or or_12 (MemtoReg[0], lw, lh, lb);
  buf or_13 (MemtoReg[1], jal);  // OR_Gate
  or or_14 (ALUop[0], subu, beq);
  buf or_15 (ALUop[1], ori);  // OR_Gate
  buf or_16 (Ssel[0], sb);  // OR_Gate
  buf or_17 (Ssel[1], sh);  // OR_Gate
  buf or_18 (Lsel[0], lb);  // OR_Gate
  buf or_19 (Lsel[1], lh);  // OR_Gate

  // Notes on the sheet:
  //   有EXT就为1
endmodule

module UseFunc (
  input  [5:0] Op,
  input  [5:0] func,
  output out_3,
  output out_4,
  output out_5,
  output out_6,
  output out_7,
  output out_8,
  output out_9,
  output out_10,
  output out_11,
  output out_12,
  output out_13,
  output out_14,
  output out_15,
  output out_16,
  output out_17
);

  wire not_1_out, not_2_out, not_3_out, not_4_out, not_5_out, not_6_out, not_7_out, not_8_out, not_9_out,
       not_10_out, not_11_out, not_12_out, r;

  not not_1 (not_1_out, Op[5]);
  not not_2 (not_2_out, Op[3]);
  not not_3 (not_3_out, Op[4]);
  not not_4 (not_4_out, Op[1]);
  not not_5 (not_5_out, Op[2]);
  not not_6 (not_6_out, Op[0]);
  and LW (out_3, Op[5], not_3_out, not_2_out, not_5_out, Op[1], Op[0]);
  and SW (out_4, Op[5], not_3_out, Op[3], not_5_out, Op[1], Op[0]);
  and u_R (r, not_1_out, not_3_out, not_2_out, not_5_out, not_4_out, not_6_out);
  and ORI (out_7, not_1_out, not_3_out, Op[3], Op[2], not_4_out, Op[0]);
  and J (out_9, not_1_out, not_3_out, not_2_out, not_5_out, Op[1], not_6_out);
  and JAL (out_10, not_1_out, not_3_out, not_2_out, not_5_out, Op[1], Op[0]);
  and BEQ (out_12, not_1_out, not_3_out, not_2_out, Op[2], not_4_out, not_6_out);
  and LUI (out_8, not_1_out, not_3_out, Op[3], Op[2], Op[1], Op[0]);
  and LH (out_14, Op[5], not_3_out, not_2_out, not_5_out, not_4_out, Op[0]);
  and SH (out_15, Op[5], not_3_out, Op[3], not_5_out, not_4_out, Op[0]);
  and LB (out_16, Op[5], not_3_out, not_2_out, not_5_out, not_4_out, not_6_out);
  and SB (out_17, Op[5], not_3_out, Op[3], not_5_out, not_4_out, not_6_out);
  not not_7 (not_7_out, func[5]);
  not not_8 (not_8_out, func[3]);
  not not_9 (not_9_out, func[4]);
  not not_10 (not_10_out, func[1]);
  not not_11 (not_11_out, func[2]);
  not not_12 (not_12_out, func[0]);
  and ADDU (out_5, r, func[5], not_9_out, not_8_out, not_11_out, not_10_out, func[0]);
  and SUBU (out_6, r, func[5], not_9_out, not_8_out, not_11_out, func[1], func[0]);
  and JR (out_11, r, not_7_out, not_9_out, func[3], not_11_out, not_10_out, not_12_out);
  and NOP (out_13, r, not_7_out, not_9_out, not_8_out, not_11_out, not_10_out, not_12_out);

  // Other names for the same wires on the sheet: addu = out_5; beq = out_12; j = out_9; jal = out_10; jr = out_11;
  //   lb = out_16; lh = out_14; lui = out_8; lw = out_3; nop = out_13; ori = out_7; sb = out_17; sh = out_15;
  //   subu = out_6; sw = out_4
endmodule

module EXT (
  input  [15:0] in_1,
  input  [1:0] in_2,
  output [31:0] out_3
);

  wire [31:0] bit_extender_1_out, bit_extender_2_out;

  assign bit_extender_1_out = {{16{1'b0}}, in_1};  // Bit_Extender bit_extender_1
  assign bit_extender_2_out = {{16{in_1[15]}}, in_1};  // Bit_Extender bit_extender_2
  Multiplexer #(.select(2), .width(32), .enable("false")) multiplexer_1 (
    .in0(bit_extender_1_out), .in1(bit_extender_2_out), .in2({in_1, {16{1'b0}}}), .out(out_3), .sel(in_2));  // open: in3
endmodule

module ALU (
  input  [31:0] in_1,
  input  [31:0] in_2,
  input  [1:0] ALUOP,
  output Zero,
  output [31:0] out_5
);

  wire comparator_1_eq;
  wire [31:0] adder_1_out, bit_extender_1_out, or_1_out, subtractor_1_out;

  Adder #(.width(32)) adder_1 (.a(in_1), .b(in_2), .out(adder_1_out));  // open: cin, cout
  Subtractor #(.width(32)) subtractor_1 (.a(in_1), .b(in_2), .out(subtractor_1_out));  // open: bin, bout
  assign or_1_out = in_1 | in_2;  // OR_Gate or_1, 32 bits wide
  Multiplexer #(.select(2), .width(32), .enable("false")) multiplexer_1 (
    .in0(adder_1_out), .in1(subtractor_1_out), .in2(or_1_out), .in3(bit_extender_1_out), .out(out_5),
    .sel(ALUOP));
  Comparator #(.width(32)) comparator_1 (.a(in_1), .b(in_2), .eq(comparator_1_eq));  // open: gt, lt
  assign bit_extender_1_out = {{31{1'b0}}, comparator_1_eq};  // Bit_Extender bit_extender_1
  Comparator #(.width(32)) comparator_2 (.a(out_5), .b({32{1'b0}}), .eq(Zero));  // open: gt, lt
endmodule

module DM (
  input  [1:0] SSel,
  input  [1:0] Lsel,
  input  [31:0] Addr,
  input  in_4,
  input  in_5,
  input  in_6,
  input  in_7,
  input  [31:0] WriteData,
  output [31:0] RD
);

  wire decoder_1_out0, decoder_1_out1, decoder_1_out2, decoder_1_out3, decoder_2_out0, decoder_2_out1;
  wire [7:0] _7_0, _15_8, _23_16, _24_31, multiplexer_1_out, multiplexer_2_out, multiplexer_3_out,
       multiplexer_4_out, multiplexer_8_out;
  wire [15:0] multiplexer_5_out, multiplexer_6_out, multiplexer_9_out;
  wire [31:0] bit_extender_1_out, bit_extender_2_out, multiplexer_7_out;

  Decoder #(.select(2)) decoder_1 (
    .out0(decoder_1_out0), .out1(decoder_1_out1), .out2(decoder_1_out2), .out3(decoder_1_out3),
    .sel(Addr[1:0]));  // open: en
  Decoder decoder_2 (.out0(decoder_2_out0), .out1(decoder_2_out1), .sel(Addr[1]));  // open: en
  Multiplexer #(.width(8), .enable("false")) multiplexer_1 (
    .in0(_7_0), .in1(WriteData[7:0]), .out(multiplexer_1_out), .sel(decoder_1_out0));
  Multiplexer #(.width(8), .enable("false")) multiplexer_2 (
    .in0(_15_8), .in1(WriteData[7:0]), .out(multiplexer_2_out), .sel(decoder_1_out1));
  Multiplexer #(.width(8), .enable("false")) multiplexer_3 (
    .in0(_23_16), .in1(WriteData[7:0]), .out(multiplexer_3_out), .sel(decoder_1_out2));
  Multiplexer #(.width(8), .enable("false")) multiplexer_4 (
    .in0(_24_31), .in1(WriteData[7:0]), .out(multiplexer_4_out), .sel(decoder_1_out3));
  Multiplexer #(.width(16), .enable("false")) multiplexer_5 (
    .in0({_15_8, _7_0}), .in1(WriteData[15:0]), .out(multiplexer_5_out), .sel(decoder_2_out0));
  Multiplexer #(.width(16), .enable("false")) multiplexer_6 (
    .in0({_24_31, _23_16}), .in1(WriteData[15:0]), .out(multiplexer_6_out), .sel(decoder_2_out1));
  Multiplexer #(.select(2), .width(32), .enable("false")) multiplexer_7 (
    .in0(WriteData), .in1({multiplexer_4_out, multiplexer_3_out, multiplexer_2_out, multiplexer_1_out}),
    .in2({multiplexer_6_out, multiplexer_5_out}), .out(multiplexer_7_out), .sel(SSel));  // open: in3
  RAM #(.addrWidth(5), .dataWidth(32), .bus("separate")) ram_1 (
    .addr(Addr[6:2]), .din(multiplexer_7_out), .data({_24_31, _23_16, _15_8, _7_0}), .str(in_4), .clk(in_5),
    .ld(in_6), .clr(in_7));  // open: sel
  Multiplexer #(.select(2), .width(8), .enable("false")) multiplexer_8 (
    .in0(_7_0), .in1(_15_8), .in2(_23_16), .in3(_24_31), .out(multiplexer_8_out), .sel(Addr[1:0]));
  Multiplexer #(.width(16), .enable("false")) multiplexer_9 (
    .in0({_15_8, _7_0}), .in1({_24_31, _23_16}), .out(multiplexer_9_out), .sel(Addr[1]));
  assign bit_extender_1_out = {{24{multiplexer_8_out[7]}}, multiplexer_8_out};  // Bit_Extender bit_extender_1
  assign bit_extender_2_out = {{16{multiplexer_9_out[15]}}, multiplexer_9_out};  // Bit_Extender bit_extender_2
  Multiplexer #(.select(2), .width(32), .enable("false")) multiplexer_10 (
    .in0({_24_31, _23_16, _15_8, _7_0}), .in1(bit_extender_1_out), .in2(bit_extender_2_out), .out(RD),
    .sel(Lsel));  // open: in3
endmodule

module FD_Reg (
  input  in_1,
  input  in_2,
  input  [31:0] instr_i,
  input  [31:0] pc_i,
  input  [31:0] pc_4_i,
  input  [31:0] pc_8_i,
  input  in_7,
  output [31:0] instr_o,
  output [31:0] pc_o,
  output [31:0] pc_4_o,
  output [31:0] pc_8_o
);

  wire clk_prime, not_1_out, not_2_out, not_3_out, not_4_out;

  buf and_1 (clk_prime, in_1);  // AND_Gate
  not not_1 (not_1_out, in_7);
  not not_2 (not_2_out, in_7);
  not not_3 (not_3_out, in_7);
  not not_4 (not_4_out, in_7);
  Register #(.width(32)) register_1 (.D(instr_i), .en(not_1_out), .Q(instr_o), .clk(clk_prime), .clr(in_2));
  Register #(.width(32)) register_2 (.D(pc_i), .en(not_2_out), .Q(pc_o), .clk(clk_prime), .clr(in_2));
  Register #(.width(32)) register_3 (.D(pc_4_i), .en(not_3_out), .Q(pc_4_o), .clk(clk_prime), .clr(in_2));
  Register #(.width(32)) register_4 (.D(pc_8_i), .en(not_4_out), .Q(pc_8_o), .clk(clk_prime), .clr(in_2));

  // Other names for the same wires on the sheet: clk = in_1; F_D_stall = in_7; reset = in_2
endmodule

module DE_Reg (
  input  in_1,
  input  in_2,
  input  [1:0] RegDst_i,
  input  MemWrite_i,
  input  RegWrite_i,
  input  ALUSrc_i,
  input  MemRead_i,
  input  [1:0] MemToReg_i,
  input  [1:0] ALUop_i,
  input  [31:0] RD1_i,
  input  [31:0] RD2_i,
  input  in_12,
  input  [4:0] rs_i,
  input  [4:0] rt_i,
  input  [4:0] rd_i,
  input  [31:0] pc_i,
  input  [31:0] pc_4_i,
  input  [31:0] pc_8_i,
  input  [31:0] EXTresult_i,
  input  [31:0] instr_i,
  output [1:0] RegDst_o,
  output MemWrite_o,
  output RegWrite_o,
  output ALUSrc_o,
  output MemRead_o,
  output [1:0] MemToReg_o,
  output [1:0] ALUop_o,
  output [31:0] RD1_o,
  output [31:0] RD2_o,
  output [4:0] rs_o,
  output [4:0] rt_o,
  output [4:0] rd_o,
  output [31:0] pc_o,
  output [31:0] pc_4_o,
  output [31:0] pc_8_o,
  output [31:0] EXTresult_o,
  output [31:0] instr_o
);

  wire multiplexer_2_out, multiplexer_3_out, multiplexer_4_out, multiplexer_5_out;
  wire [1:0] multiplexer_1_out, multiplexer_6_out, multiplexer_7_out;
  wire [4:0] multiplexer_10_out, multiplexer_11_out, multiplexer_12_out;
  wire [31:0] multiplexer_8_out, multiplexer_9_out, multiplexer_13_out, multiplexer_14_out,
       multiplexer_15_out, multiplexer_16_out, multiplexer_17_out, undriven;

  Multiplexer #(.width(2), .enable("false")) multiplexer_1 (
    .in0(RegDst_i), .in1(2'b00), .out(multiplexer_1_out), .sel(in_12));
  Multiplexer #(.enable("false")) multiplexer_2 (.in0(MemWrite_i), .in1(1'b0), .out(multiplexer_2_out), .sel(in_12));
  Multiplexer #(.enable("false")) multiplexer_3 (.in0(RegWrite_i), .in1(1'b0), .out(multiplexer_3_out), .sel(in_12));
  Multiplexer #(.enable("false")) multiplexer_4 (.in0(ALUSrc_i), .in1(1'b0), .out(multiplexer_4_out), .sel(in_12));
  Multiplexer #(.enable("false")) multiplexer_5 (.in0(MemRead_i), .in1(1'b0), .out(multiplexer_5_out), .sel(in_12));
  Multiplexer #(.width(2), .enable("false")) multiplexer_6 (
    .in0(MemToReg_i), .in1(2'b00), .out(multiplexer_6_out), .sel(in_12));
  Multiplexer #(.width(2), .enable("false")) multiplexer_7 (
    .in0(ALUop_i), .in1(2'b00), .out(multiplexer_7_out), .sel(in_12));
  Multiplexer #(.width(32), .enable("false")) multiplexer_8 (
    .in0(RD1_i), .in1({32{1'b0}}), .out(multiplexer_8_out), .sel(in_12));
  Multiplexer #(.width(32), .enable("false")) multiplexer_9 (
    .in0(RD2_i), .in1({32{1'b0}}), .out(multiplexer_9_out), .sel(in_12));
  Multiplexer #(.width(5), .enable("false")) multiplexer_10 (
    .in0(rs_i), .in1({5{1'b0}}), .out(multiplexer_10_out), .sel(in_12));
  Multiplexer #(.width(5), .enable("false")) multiplexer_11 (
    .in0(rt_i), .in1({5{1'b0}}), .out(multiplexer_11_out), .sel(in_12));
  Multiplexer #(.width(5), .enable("false")) multiplexer_12 (
    .in0(rd_i), .in1({5{1'b0}}), .out(multiplexer_12_out), .sel(in_12));
  Multiplexer #(.width(32), .enable("false")) multiplexer_13 (
    .in0(pc_i), .in1({32{1'b0}}), .out(multiplexer_13_out), .sel(in_12));
  Multiplexer #(.width(32), .enable("false")) multiplexer_14 (
    .in0(pc_4_i), .in1({32{1'b0}}), .out(multiplexer_14_out), .sel(in_12));
  Multiplexer #(.width(32), .enable("false")) multiplexer_15 (
    .in0(pc_8_i), .in1({32{1'b0}}), .out(multiplexer_15_out), .sel(in_12));
  Multiplexer #(.width(32), .enable("false")) multiplexer_16 (
    .in0(EXTresult_i), .in1({32{1'b0}}), .out(multiplexer_16_out), .sel(in_12));
  Multiplexer #(.width(32), .enable("false")) multiplexer_17 (
    .in0(instr_i), .in1(undriven), .out(multiplexer_17_out), .sel(in_12));
  Register #(.width(2)) register_1 (.D(multiplexer_1_out), .Q(RegDst_o), .clk(in_1), .clr(in_2));  // open: en
  Register #(.width(1)) register_2 (.D(multiplexer_2_out), .Q(MemWrite_o), .clk(in_1), .clr(in_2));  // open: en
  Register #(.width(1)) register_3 (.D(multiplexer_3_out), .Q(RegWrite_o), .clk(in_1), .clr(in_2));  // open: en
  Register #(.width(1)) register_4 (.D(multiplexer_4_out), .Q(ALUSrc_o), .clk(in_1), .clr(in_2));  // open: en
  Register #(.width(1)) register_5 (.D(multiplexer_5_out), .Q(MemRead_o), .clk(in_1), .clr(in_2));  // open: en
  Register #(.width(32)) register_6 (.D(multiplexer_8_out), .Q(RD1_o), .clk(in_1), .clr(in_2));  // open: en
  Register #(.width(32)) register_7 (.D(multiplexer_9_out), .Q(RD2_o), .clk(in_1), .clr(in_2));  // open: en
  Register #(.width(5)) register_8 (.D(multiplexer_10_out), .Q(rs_o), .clk(in_1), .clr(in_2));  // open: en
  Register #(.width(5)) register_9 (.D(multiplexer_11_out), .Q(rt_o), .clk(in_1), .clr(in_2));  // open: en
  Register #(.width(5)) register_10 (.D(multiplexer_12_out), .Q(rd_o), .clk(in_1), .clr(in_2));  // open: en
  Register #(.width(32)) register_11 (.D(multiplexer_13_out), .Q(pc_o), .clk(in_1), .clr(in_2));  // open: en
  Register #(.width(32)) register_12 (.D(multiplexer_14_out), .Q(pc_4_o), .clk(in_1), .clr(in_2));  // open: en
  Register #(.width(32)) register_13 (.D(multiplexer_15_out), .Q(pc_8_o), .clk(in_1), .clr(in_2));  // open: en
  Register #(.width(32)) register_14 (.D(multiplexer_16_out), .Q(EXTresult_o), .clk(in_1), .clr(in_2));  // open: en
  Register #(.width(2)) register_15 (.D(multiplexer_6_out), .Q(MemToReg_o), .clk(in_1), .clr(in_2));  // open: en
  Register #(.width(2)) register_16 (.D(multiplexer_7_out), .Q(ALUop_o), .clk(in_1), .clr(in_2));  // open: en
  Register #(.width(32)) register_17 (.D(multiplexer_17_out), .Q(instr_o), .clk(in_1), .clr(in_2));  // open: en

  // Other names for the same wires on the sheet: clk = in_1; clk_prime = in_1; flush = in_12; Reset = in_2
endmodule

module EM_Reg (
  input  in_1,
  input  in_2,
  input  MemWrite_i,
  input  RegWrite_i,
  input  MemRead_i,
  input  [1:0] MemToReg_i,
  input  [31:0] aluresult_i,
  input  [31:0] writedata_i,
  input  [4:0] writereg_i,
  input  [31:0] pc_i,
  input  [31:0] pc_4_i,
  input  [31:0] pc_8_i,
  input  [31:0] instr_i,
  input  [4:0] tnew_E,
  input  [4:0] tnew_M,
  output MemWrite_o,
  output RegWrite_o,
  output MemRead_o,
  output [1:0] MemToReg_o,
  output [31:0] out_20,
  output [31:0] out_21,
  output [4:0] out_22,
  output [31:0] pc_o,
  output [31:0] pc_4_o,
  output [31:0] pc_8_o,
  output [31:0] out_26
);

  Register #(.width(1)) register_1 (.D(MemWrite_i), .Q(MemWrite_o), .clk(in_1), .clr(in_2));  // open: en
  Register #(.width(1)) register_2 (.D(RegWrite_i), .Q(RegWrite_o), .clk(in_1), .clr(in_2));  // open: en
  Register #(.width(1)) register_3 (.D(MemRead_i), .Q(MemRead_o), .clk(in_1), .clr(in_2));  // open: en
  Register #(.width(2)) register_4 (.D(MemToReg_i), .Q(MemToReg_o), .clk(in_1), .clr(in_2));  // open: en
  Register #(.width(32)) register_5 (.D(aluresult_i), .Q(out_20), .clk(in_1), .clr(in_2));  // open: en
  Register #(.width(32)) register_6 (.D(writedata_i), .Q(out_21), .clk(in_1), .clr(in_2));  // open: en
  Register #(.width(5)) register_7 (.D(writereg_i), .Q(out_22), .clk(in_1), .clr(in_2));  // open: en
  Register #(.width(32)) register_8 (.D(pc_i), .Q(pc_o), .clk(in_1), .clr(in_2));  // open: en
  Register #(.width(32)) register_9 (.D(pc_4_i), .Q(pc_4_o), .clk(in_1), .clr(in_2));  // open: en
  Register #(.width(32)) register_10 (.D(pc_8_i), .Q(pc_8_o), .clk(in_1), .clr(in_2));  // open: en
  Register #(.width(32)) register_11 (.D(instr_i), .Q(out_26), .clk(in_1), .clr(in_2));  // open: en

  // Other names for the same wires on the sheet: clk = in_1; clk_prime = in_1; Reset = in_2
endmodule

module MW_Reg (
  input  in_1,
  input  in_2,
  input  RegWrite,
  input  [1:0] MemtoReg,
  input  [31:0] aluresult_i,
  input  [31:0] writedata_i,
  input  [31:0] readdata_i,
  input  [31:0] pc_i,
  input  [31:0] pc_4_i,
  input  [31:0] pc_8_i,
  input  [31:0] instr_i,
  input  [4:0] writereg_i,
  input  [31:0] memaddr,
  input  [31:0] memdata,
  input  memwrite,
  output out_16,
  output [1:0] out_17,
  output [31:0] out_18,
  output [31:0] out_19,
  output [31:0] out_20,
  output [31:0] pc_o,
  output [31:0] pc_4_o,
  output [31:0] pc_8_o,
  output [31:0] out_24,
  output [4:0] out_25,
  output [31:0] out_26,
  output [31:0] out_27,
  output out_28
);

  Register #(.width(1)) register_1 (.D(RegWrite), .Q(out_16), .clk(in_1), .clr(in_2));  // open: en
  Register #(.width(2)) register_2 (.D(MemtoReg), .Q(out_17), .clk(in_1), .clr(in_2));  // open: en
  Register #(.width(32)) register_3 (.D(aluresult_i), .Q(out_18), .clk(in_1), .clr(in_2));  // open: en
  Register #(.width(32)) register_4 (.D(writedata_i), .Q(out_19), .clk(in_1), .clr(in_2));  // open: en
  Register #(.width(32)) register_5 (.D(readdata_i), .Q(out_20), .clk(in_1), .clr(in_2));  // open: en
  Register #(.width(32)) register_6 (.D(pc_i), .Q(pc_o), .clk(in_1), .clr(in_2));  // open: en
  Register #(.width(32)) register_7 (.D(pc_4_i), .Q(pc_4_o), .clk(in_1), .clr(in_2));  // open: en
  Register #(.width(32)) register_8 (.D(pc_8_i), .Q(pc_8_o), .clk(in_1), .clr(in_2));  // open: en
  Register #(.width(32)) register_9 (.D(instr_i), .Q(out_24), .clk(in_1), .clr(in_2));  // open: en
  Register #(.width(5)) register_10 (.D(writereg_i), .Q(out_25), .clk(in_1), .clr(in_2));  // open: en
  Register #(.width(32)) register_11 (.D(memaddr), .Q(out_26), .clk(in_1), .clr(in_2));  // open: en
  Register #(.width(32)) register_12 (.D(memdata), .Q(out_27), .clk(in_1), .clr(in_2));  // open: en
  Register #(.width(1)) register_13 (.D(memwrite), .Q(out_28), .clk(in_1), .clr(in_2));  // open: en

  // Other names for the same wires on the sheet: clk = in_1; clk_prime = in_1; Reset = in_2
endmodule
