// Logisim project CPU_pipeline_sbsh.circ as structural Verilog: 20 circuits, main circuit main
module main (
  input  in_1,
  output [31:0] Instr,
  output RegWrite,
  output [4:0] RegAddr,
  output [31:0] RegData,
  output MemWrite,
  output [4:0] MemAddr,
  output [31:0] MemData
);

  wire addu, ALUSrc, beq, branch_beq, branch_j_jal, branch_jr, clk, DE_Reg_alusrc_o, DE_Reg_memread_o,
       DE_Reg_memwrite_o, DE_Reg_regwrite_o, eql, Flush_E, forwardunit_1_frtmsel, j, jal, jr, lb, lh, lui,
       lw, Mem_MemRead, Mem_MemWrite, Mem_RegWrite, MemRead, MemWrite_t, nop, ori, RegWrite_t, sb, sh,
       Stall_D, Stall_F, subu, sw;
  wire [1:0] ALUop, DE_Reg_aluop_o, DE_Reg_memtoreg_o, DE_Reg_regdst_o, EXTop, forwardunit_1_frsdsel,
       forwardunit_1_frsesel, forwardunit_1_frtdsel, forwardunit_1_frtesel, id_1_tuse1_d, id_1_tuse2_d, Lsel,
       Mem_MemtoReg, MemtoReg, MW_Reg_out_18, RegDst, register_1_q, register_2_q, register_3_q, register_4_q,
       Ssel;
  wire [3:0] EM_Reg_tnew_m, ex_1_tnew_e, high4, MW_Reg_tnew_w;
  wire [4:0] DE_Reg_rd_o, ex_1_des_e, ex_1_s1_e, ex_1_s2_e, id_1_s1_d, id_1_s2_d, mem_1_des_m, mem_1_s2_m,
       Mem_WriteReg, multiplexer_1_out, s1_d, s1_e, s2_d, s2_e, Shamt_shift, Splitter_out_4, wb_1_des_w;
  wire [5:0] func, Op;
  wire [9:0] pc_1_instraddr;
  wire [15:0] imm16;
  wire [25:0] j_imm26;
  wire [27:0] bit_extender_1_out, jumpAddr, pc_1_pc;
  wire [31:0] adder_1_out, adder_2_out, ALU_out_5, alu_w, D_CMP_RS, D_CMP_RT, DE_Reg_extresult_o,
       DE_Reg_instr_o, DE_Reg_pc_4_o, DE_Reg_pc_8_o, DE_Reg_pc_o, dm_1_rd, dm_1_w_memdata, E_ALU_A, E_ALU_B,
       EM_Reg_out_19, EM_Reg_out_25, EM_Reg_pc_4_o, EM_Reg_pc_8_o, EM_Reg_pc_o, EtoD, EXTresult,
       fd_reg_1_instr_o, fd_reg_1_pc_4_o, fd_reg_1_pc_8_o, fd_reg_1_pc_o, instr_t, M_DM_WD, MemAddr_t, MtoD,
       multiplexer_3_out, MW_Reg_out_21, npc_1_out_10, pc_8_w, rd_1, rd_2, rs_E, rt_E, WD, WtoD;

  // Probe on npc_1_out_10
  // Probe on {high4, pc_1_pc}
  Clock clock_1 (.out(clk));
  PC pc_1 (
    .NPC(npc_1_out_10), .InstrAddr(pc_1_instraddr), .PC({high4, pc_1_pc}), .StallF(Stall_F), .CLK(clk),
    .reset(in_1));
  assign bit_extender_1_out = {{2{1'b0}}, j_imm26};  // Bit_Extender bit_extender_1
  // Mips_Probe mips_probe_1: pin names not known; wires that end beside it: instr_t
  // Probe on instr_t
  ROM #(.addrWidth(10), .dataWidth(32)) rom_1 (.addr(pc_1_instraddr), .data(instr_t));  // open: sel
  Adder #(.width(32)) adder_1 (.a({high4, pc_1_pc}), .b(32'h4), .out(adder_1_out));  // open: cin, cout
  Adder #(.width(32)) adder_2 (.a({high4, pc_1_pc}), .b(32'h8), .out(adder_2_out));  // open: cin, cout
  EXT EXT (.in_1(imm16), .out_3(EXTresult), .in_2(EXTop));
  Shifter #(.width(28)) shifter_1 (.in(bit_extender_1_out), .\dist (5'b00010), .out(jumpAddr));
  UseFunc UseFunc (
    .Op(Op), .func(func), .out_3(lw), .out_4(sw), .out_5(addu), .out_6(subu), .out_7(ori), .out_8(lui),
    .out_9(j), .out_10(jal), .out_11(jr), .out_12(beq), .out_13(nop), .out_14(lh), .out_15(sh), .out_16(lb),
    .out_17(sb));
  FD_Reg fd_reg_1 (
    .instr_i(instr_t), .pc_i({high4, pc_1_pc}), .pc_4_i(adder_1_out), .pc_8_i(adder_2_out),
    .instr_o(fd_reg_1_instr_o), .pc_o(fd_reg_1_pc_o), .pc_4_o(fd_reg_1_pc_4_o), .pc_8_o(fd_reg_1_pc_8_o),
    .in_1(clk), .in_2(in_1), .in_7(Stall_D));
  NPC npc_1 (
    .PC_4(adder_1_out), .PC({high4, pc_1_pc}), .EXTresult_imm32(EXTresult), .j_jal_Addr({high4, jumpAddr}),
    .RegData(D_CMP_RS), .out_10(npc_1_out_10), .B_beq(branch_beq), .B_j_jal(branch_j_jal), .B_jr(branch_jr),
    .equal(eql));
  // Probe on EM_Reg_out_25
  // Probe on fd_reg_1_instr_o
  // Probe on DE_Reg_instr_o
  splitter Splitter (
    .in_1(fd_reg_1_instr_o), .out_2(func), .out_3(Shamt_shift), .out_4(Splitter_out_4), .out_5(s2_d),
    .out_6(s1_d), .out_7(Op), .out_8(imm16), .out_9(j_imm26));
  Controller Controller (
    .Op(Op), .func(func), .RegDst(RegDst), .MemWrite(MemWrite_t), .branch_beq(branch_beq),
    .branch_j_jal(branch_j_jal), .branch_jr(branch_jr), .EXTop(EXTop), .RegWrite(RegWrite_t),
    .ALUSrc(ALUSrc), .MemRead(MemRead), .MemtoReg(MemtoReg), .ALUop(ALUop), .Ssel(Ssel), .Lsel(Lsel));
  // Probe on s1_d
  ID id_1 (.in_1(fd_reg_1_instr_o), .S1_D(id_1_s1_d), .S2_D(id_1_s2_d), .tuse1_D(id_1_tuse1_d), .tuse2_D(id_1_tuse2_d));
  EX ex_1 (
    .in_1(DE_Reg_instr_o), .EXTresult(DE_Reg_extresult_o), .pc_8(DE_Reg_pc_8_o), .S1_E(ex_1_s1_e),
    .S2_E(ex_1_s2_e), .des_E(ex_1_des_e), .EtoD(EtoD), .Tnew_E(ex_1_tnew_e));
  MEM mem_1 (
    .in_1(EM_Reg_out_25), .ALUresult(EM_Reg_out_19), .pc_8(EM_Reg_pc_8_o), .S2_M(mem_1_s2_m),
    .des_M(mem_1_des_m), .MtoD(MtoD));
  WB wb_1 (.in_1(Instr), .ALUresult(alu_w), .pc_8(pc_8_w), .RegData(RegData), .des_W(wb_1_des_w), .WtoD(WtoD));
  GRF grf_1 (
    .A1(s1_d), .A2(s2_d), .A3(RegAddr), .WD(RegData), .RD1(rd_1), .RD2(rd_2), .clk(clk), .reset(in_1),
    .we(RegWrite));
  StallUnit stallunit_1 (
    .s1_D(id_1_s1_d), .s2_D(id_1_s2_d), .tUse1_D(id_1_tuse1_d), .tUse2_D(id_1_tuse2_d), .des_E(ex_1_des_e),
    .tNew_E(ex_1_tnew_e), .tNew_M(EM_Reg_tnew_m), .des_M(mem_1_des_m), .Stall_F(Stall_F), .Stall_D(Stall_D),
    .flush_E(Flush_E));
  // Probe on rd_1
  // Mips_Probe mips_probe_2: pin names not known; wires that end beside it: fd_reg_1_instr_o
  Comparator #(.width(32)) comparator_1 (.a(D_CMP_RS), .b(D_CMP_RT), .eq(eql));  // open: gt, lt
  // Probe on id_1_s2_d
  // Probe on ex_1_des_e
  DE_Reg DE_Reg (
    .RegDst_i(RegDst), .MemWrite_i(MemWrite_t), .RegWrite_i(RegWrite_t), .ALUSrc_i(ALUSrc),
    .MemRead_i(MemRead), .MemToReg_i(MemtoReg), .ALUop_i(ALUop), .RD1_i(D_CMP_RS), .RD2_i(D_CMP_RT),
    .rs_i(s1_d), .rt_i(s2_d), .rd_i(Splitter_out_4), .pc_i(fd_reg_1_pc_o), .pc_4_i(fd_reg_1_pc_4_o),
    .pc_8_i(fd_reg_1_pc_8_o), .EXTresult_i(EXTresult), .instr_i(fd_reg_1_instr_o),
    .RegDst_o(DE_Reg_regdst_o), .MemWrite_o(DE_Reg_memwrite_o), .RegWrite_o(DE_Reg_regwrite_o),
    .ALUSrc_o(DE_Reg_alusrc_o), .MemRead_o(DE_Reg_memread_o), .MemToReg_o(DE_Reg_memtoreg_o),
    .ALUop_o(DE_Reg_aluop_o), .RD1_o(rs_E), .RD2_o(rt_E), .rs_o(s1_e), .rt_o(s2_e), .rd_o(DE_Reg_rd_o),
    .pc_o(DE_Reg_pc_o), .pc_4_o(DE_Reg_pc_4_o), .pc_8_o(DE_Reg_pc_8_o), .EXTresult_o(DE_Reg_extresult_o),
    .instr_o(DE_Reg_instr_o), .in_1(clk), .in_2(in_1), .in_12(Flush_E));
  Multiplexer #(.select(2), .width(5), .enable("false")) multiplexer_1 (
    .in0(s2_e), .in1(DE_Reg_rd_o), .in2({5{1'b1}}), .out(multiplexer_1_out), .sel(DE_Reg_regdst_o));  // open: in3
  Multiplexer #(.select(2), .width(32), .enable("false")) multiplexer_2 (
    .in0(rd_1), .in1(EtoD), .in2(MtoD), .in3({32{1'b0}}), .out(D_CMP_RS), .sel(forwardunit_1_frsdsel));
  // Probe on D_CMP_RS
  // Probe on E_ALU_A
  Multiplexer #(.width(32), .enable("false")) multiplexer_3 (
    .in0(E_ALU_B), .in1(DE_Reg_extresult_o), .out(multiplexer_3_out), .sel(DE_Reg_alusrc_o));
  // Mips_Probe mips_probe_3: pin names not known; wires that end beside it: DE_Reg_instr_o
  ALU ALU (.in_1(E_ALU_A), .in_2(multiplexer_3_out), .out_5(ALU_out_5), .ALUOP(DE_Reg_aluop_o));  // open: Zero
  forwardUnit forwardunit_1 (
    .s1_D(id_1_s1_d), .s2_D(id_1_s2_d), .s1_E(ex_1_s1_e), .s2_E(ex_1_s2_e), .des_E(ex_1_des_e),
    .tNew_E(ex_1_tnew_e), .s2_M(mem_1_s2_m), .tNew_M(EM_Reg_tnew_m), .des_M(mem_1_des_m),
    .tNew_W(MW_Reg_tnew_w), .des_W(wb_1_des_w), .fRsDsel(forwardunit_1_frsdsel),
    .fRtDsel(forwardunit_1_frtdsel), .fRsEsel(forwardunit_1_frsesel), .fRtEsel(forwardunit_1_frtesel),
    .fRtMsel(forwardunit_1_frtmsel));
  // Probe on ALU_out_5
  Multiplexer #(.select(2), .width(32), .enable("false")) multiplexer_4 (
    .in0(rd_2), .in1(EtoD), .in2(MtoD), .in3({32{1'b0}}), .out(D_CMP_RT), .sel(forwardunit_1_frtdsel));
  // Probe on D_CMP_RT
  // Probe on ex_1_tnew_e
  EM_Reg EM_Reg (
    .MemWrite_i(DE_Reg_memwrite_o), .RegWrite_i(DE_Reg_regwrite_o), .MemRead_i(DE_Reg_memread_o),
    .MemToReg_i(DE_Reg_memtoreg_o), .aluresult_i(ALU_out_5), .writedata_i(E_ALU_B),
    .writereg_i(multiplexer_1_out), .pc_i(DE_Reg_pc_o), .pc_4_i(DE_Reg_pc_4_o), .pc_8_i(DE_Reg_pc_8_o),
    .instr_i(DE_Reg_instr_o), .MemWrite_o(Mem_MemWrite), .RegWrite_o(Mem_RegWrite), .MemRead_o(Mem_MemRead),
    .MemToReg_o(Mem_MemtoReg), .out_19(EM_Reg_out_19), .out_20(WD), .out_21(Mem_WriteReg),
    .pc_o(EM_Reg_pc_o), .pc_4_o(EM_Reg_pc_4_o), .pc_8_o(EM_Reg_pc_8_o), .out_25(EM_Reg_out_25), .in_1(clk),
    .in_2(in_1), .tnew_E(ex_1_tnew_e), .tnew_M(EM_Reg_tnew_m));
  // Probe on EM_Reg_tnew_m
  Multiplexer #(.select(2), .width(32), .enable("false")) multiplexer_5 (
    .in0(rs_E), .in1(MtoD), .in2(WtoD), .in3({32{1'b0}}), .out(E_ALU_A), .sel(forwardunit_1_frsesel));
  // Mips_Probe mips_probe_4: pin names not known; wires that end beside it: EM_Reg_out_25, Mem_MemRead
  Register #(.width(2)) register_1 (.D(register_2_q), .Q(register_1_q), .clk(clk), .clr(in_1));  // open: en
  Register #(.width(2)) register_2 (.D(Lsel), .Q(register_2_q), .clk(clk), .clr(in_1));  // open: en
  Multiplexer #(.select(2), .width(32), .enable("false")) multiplexer_6 (
    .in0(rt_E), .in1(MtoD), .in2(WtoD), .in3({32{1'b0}}), .out(E_ALU_B), .sel(forwardunit_1_frtesel));
  // Probe on E_ALU_B
  Register #(.width(2)) register_3 (.D(Ssel), .Q(register_3_q), .clk(clk), .clr(in_1));  // open: en
  DM dm_1 (
    .SSel(register_4_q), .Lsel(register_1_q), .Addr(EM_Reg_out_19), .WriteData(M_DM_WD), .RD(dm_1_rd),
    .in_4(Mem_MemWrite), .in_5(clk), .in_6(in_1), .W_MemData(dm_1_w_memdata));
  // Probe on WD
  Register #(.width(2)) register_4 (.D(register_3_q), .Q(register_4_q), .clk(clk), .clr(in_1));  // open: en
  // Probe on WD
  Multiplexer #(.width(32), .enable("false")) multiplexer_7 (
    .in0(WD), .in1(WtoD), .out(M_DM_WD), .sel(forwardunit_1_frtmsel));
  MW_Reg MW_Reg (
    .aluresult_i(EM_Reg_out_19), .writedata_i(WD), .readdata_i(dm_1_rd), .pc_i(EM_Reg_pc_o),
    .pc_4_i(EM_Reg_pc_4_o), .pc_8_i(EM_Reg_pc_8_o), .instr_i(EM_Reg_out_25), .memaddr(EM_Reg_out_19),
    .memdata(dm_1_w_memdata), .memwrite(Mem_MemWrite), .out_19(alu_w), .out_21(MW_Reg_out_21),
    .pc_8_o(pc_8_w), .out_25(Instr), .out_27({MemAddr_t[31:7], MemAddr, MemAddr_t[1:0]}), .out_28(MemData),
    .out_29(MemWrite), .in_1(clk), .in_2(in_1), .writereg_i(Mem_WriteReg), .out_26(RegAddr),
    .MemtoReg(Mem_MemtoReg), .out_18(MW_Reg_out_18), .RegWrite(Mem_RegWrite), .out_17(RegWrite),
    .tnew_W(MW_Reg_tnew_w), .tnew_M(EM_Reg_tnew_m));  // open: out_20, pc_o, pc_4_o
  // Probe on MW_Reg_tnew_w
  // Probe on RegData
  Multiplexer #(.select(2), .width(32), .enable("false")) multiplexer_8 (
    .in0(alu_w), .in1(MW_Reg_out_21), .in2(pc_8_w), .out(RegData), .sel(MW_Reg_out_18));  // open: in3
  // Probe on MW_Reg_out_21
  // Mips_Probe mips_probe_5: pin names not known; wires that end beside it: Instr
  // Probe on MemData

  // Other names for the same wires on the sheet: instr_w[31:0] = Instr; jumpAddr[31:28] = high4;
  //   MemAddr_t[6:2] = MemAddr; memWriteFinal = MemWrite; regWriteFinal = RegWrite; reset = in_1

  // Notes on the sheet:
  //   contents of rom_1 (hex, n*v repeats v):
  //   36100000 36310003 36f70003 ae110000 8e120000 12f20001 36530004 ae130004
endmodule

module PC (
  input  [31:0] NPC,
  input  StallF,
  input  CLK,
  input  reset,
  output [9:0] InstrAddr,
  output [31:0] PC
);

  wire comparator_1_eq, not_1_out;
  wire [31:0] register_1_q, subtractor_1_out;

  not not_1 (not_1_out, StallF);
  Register #(.width(32)) register_1 (.D(NPC), .en(not_1_out), .Q(register_1_q), .clk(CLK), .clr(reset));
  Comparator #(.width(32)) comparator_1 (.a(register_1_q), .b({32{1'b0}}), .eq(comparator_1_eq));  // open: gt, lt
  Multiplexer #(.width(32), .enable("false")) multiplexer_1 (
    .in0(register_1_q), .in1(32'h3000), .out(PC), .sel(comparator_1_eq));
  Subtractor #(.width(32)) subtractor_1 (
    .a(PC), .b(32'h3000), .out({subtractor_1_out[31:12], InstrAddr, subtractor_1_out[1:0]}));  // open: bin, bout
endmodule

module NPC (
  input  B_beq,
  input  B_j_jal,
  input  B_jr,
  input  equal,
  input  [31:0] PC_4,
  input  [31:0] PC,
  input  [31:0] EXTresult_imm32,
  input  [31:0] j_jal_Addr,
  input  [31:0] RegData,
  output [31:0] out_10
);

  wire and_1_out;
  wire [1:0] NPCop;
  wire [31:0] adder_1_out, shifter_1_out;

  and and_1 (and_1_out, equal, B_beq);
  Shifter #(.width(32)) shifter_1 (.in(EXTresult_imm32), .\dist (5'b00010), .out(shifter_1_out));
  or or_1 (NPCop[0], and_1_out, B_jr);
  or or_2 (NPCop[1], B_j_jal, B_jr);
  Adder #(.width(32)) adder_1 (.a(PC), .b(shifter_1_out), .out(adder_1_out));  // open: cin, cout
  // Probe on NPCop
  Multiplexer #(.select(2), .width(32), .enable("false")) multiplexer_1 (
    .in0(PC_4), .in1(adder_1_out), .in2(j_jal_Addr), .in3(RegData), .out(out_10), .sel(NPCop));

  // Other names for the same wires on the sheet: eql = equal

  // Notes on the sheet:
  //   beq
endmodule

module splitter (
  input  [31:0] in_1,
  output [5:0] out_2,
  output [4:0] out_3,
  output [4:0] out_4,
  output [4:0] out_5,
  output [4:0] out_6,
  output [5:0] out_7,
  output [15:0] out_8,
  output [25:0] out_9
);


  assign out_2 = in_1[5:0];
  assign out_3 = in_1[10:6];
  assign out_4 = in_1[15:11];
  assign out_5 = in_1[20:16];
  assign out_6 = in_1[25:21];
  assign out_7 = in_1[31:26];
  assign out_8 = in_1[15:0];
  assign out_9 = in_1[25:0];

  // Notes on the sheet:
  //   Func 0-5
  //   Shamt 6-10
  //   Rt 16-20
  //   Rd 11-15
  //   Rs 21-25
  //   Op 26-31
  //   16bit Immediate
  //   26 bir address for jump
endmodule

module GRF (
  input  [4:0] A1,
  input  clk,
  input  reset,
  input  we,
  input  [4:0] A2,
  input  [4:0] A3,
  input  [31:0] WD,
  output [31:0] RD1,
  output [31:0] RD2
);

  wire and_1_out, and_2_out, comparator_1_eq, comparator_2_eq, comparator_3_eq, comparator_4_eq;
  wire [31:0] I0, I1, I2, I3, I4, I5, I6, I7, I8, I9, I10, I11, I12, I13, I14, I15, I16, I17, I18, I19, I20,
       I21, I22, I23, I24, I25, I26, I27, I28, I29, I30, I31, multiplexer_2_out, multiplexer_3_out, O0, O1,
       O2, O3, O4, O5, O6, O7, O8, O9, O10, O11, O12, O13, O14, O15, O16, O17, O18, O19, O20, O21, O22, O23,
       O24, O25, O26, O27, O28, O29, O30, O31, RD1_t, RD2_t;

  Demultiplexer #(.select(5), .width(32), .tristate("true")) demultiplexer_1 (
    .out0(I0), .out1(I1), .out2(I2), .out3(I3), .out4(I4), .out5(I5), .out6(I6), .out7(I7), .out8(I8),
    .out9(I9), .out10(I10), .out11(I11), .out12(I12), .out13(I13), .out14(I14), .out15(I15), .out16(I16),
    .out17(I17), .out18(I18), .out19(I19), .out20(I20), .out21(I21), .out22(I22), .out23(I23), .out24(I24),
    .out25(I25), .out26(I26), .out27(I27), .out28(I28), .out29(I29), .out30(I30), .out31(I31), .in(WD),
    .sel(A3));  // open: en
  Multiplexer #(.select(5), .width(32)) multiplexer_1 (
    .in0(O0), .in1(O1), .in2(O2), .in3(O3), .in4(O4), .in5(O5), .in6(O6), .in7(O7), .in8(O8), .in9(O9),
    .in10(O10), .in11(O11), .in12(O12), .in13(O13), .in14(O14), .in15(O15), .in16(O16), .in17(O17),
    .in18(O18), .in19(O19), .in20(O20), .in21(O21), .in22(O22), .in23(O23), .in24(O24), .in25(O25),
    .in26(O26), .in27(O27), .in28(O28), .in29(O29), .in30(O30), .in31(O31), .out(RD2_t), .sel(A2));  // open: en
  // Probe on A1
  Comparator #(.width(5)) comparator_1 (.a(A1), .b(A3), .eq(comparator_1_eq));  // open: gt, lt
  Comparator #(.width(5)) comparator_2 (.a(A2), .b(A3), .eq(comparator_2_eq));  // open: gt, lt
  Comparator #(.width(5)) comparator_3 (.a(A1), .b({5{1'b0}}), .eq(comparator_3_eq));  // open: gt, lt
  and and_1 (and_1_out, comparator_1_eq, we);
  Comparator #(.width(5)) comparator_4 (.a(A2), .b({5{1'b0}}), .eq(comparator_4_eq));  // open: gt, lt
  and and_2 (and_2_out, comparator_2_eq, we);
  Multiplexer #(.width(32), .enable("false")) multiplexer_2 (
    .in0(RD1_t), .in1(WD), .out(multiplexer_2_out), .sel(and_1_out));
  Multiplexer #(.width(32), .enable("false")) multiplexer_3 (
    .in0(RD2_t), .in1(WD), .out(multiplexer_3_out), .sel(and_2_out));
  Multiplexer #(.select(5), .width(32)) multiplexer_4 (
    .in0(O0), .in1(O1), .in2(O2), .in3(O3), .in4(O4), .in5(O5), .in6(O6), .in7(O7), .in8(O8), .in9(O9),
    .in10(O10), .in11(O11), .in12(O12), .in13(O13), .in14(O14), .in15(O15), .in16(O16), .in17(O17),
    .in18(O18), .in19(O19), .in20(O20), .in21(O21), .in22(O22), .in23(O23), .in24(O24), .in25(O25),
    .in26(O26), .in27(O27), .in28(O28), .in29(O29), .in30(O30), .in31(O31), .out(RD1_t), .sel(A1));  // open: en
  Multiplexer #(.width(32), .enable("false")) multiplexer_5 (
    .in0(multiplexer_2_out), .in1({32{1'b0}}), .out(RD1), .sel(comparator_3_eq));
  Multiplexer #(.width(32), .enable("false")) multiplexer_6 (
    .in0(multiplexer_3_out), .in1({32{1'b0}}), .out(RD2), .sel(comparator_4_eq));
  Register #(.width(32)) register_1 (.D({32{1'b0}}), .en(we), .Q(O0), .clk(clk), .clr(reset));
  Register #(.width(32)) register_2 (.D(I8), .en(we), .Q(O8), .clk(clk), .clr(reset));
  Register #(.width(32)) register_3 (.D(I16), .en(we), .Q(O16), .clk(clk), .clr(reset));
  Register #(.width(32)) register_4 (.D(I24), .en(we), .Q(O24), .clk(clk), .clr(reset));
  Register #(.width(32)) register_5 (.D(I1), .en(we), .Q(O1), .clk(clk), .clr(reset));
  Register #(.width(32)) register_6 (.D(I9), .en(we), .Q(O9), .clk(clk), .clr(reset));
  Register #(.width(32)) register_7 (.D(I17), .en(we), .Q(O17), .clk(clk), .clr(reset));
  Register #(.width(32)) register_8 (.D(I25), .en(we), .Q(O25), .clk(clk), .clr(reset));
  Register #(.width(32)) register_9 (.D(I2), .en(we), .Q(O2), .clk(clk), .clr(reset));
  Register #(.width(32)) register_10 (.D(I10), .en(we), .Q(O10), .clk(clk), .clr(reset));
  Register #(.width(32)) register_11 (.D(I18), .en(we), .Q(O18), .clk(clk), .clr(reset));
  Register #(.width(32)) register_12 (.D(I26), .en(we), .Q(O26), .clk(clk), .clr(reset));
  Register #(.width(32)) register_13 (.D(I3), .en(we), .Q(O3), .clk(clk), .clr(reset));
  Register #(.width(32)) register_14 (.D(I11), .en(we), .Q(O11), .clk(clk), .clr(reset));
  Register #(.width(32)) register_15 (.D(I19), .en(we), .Q(O19), .clk(clk), .clr(reset));
  Register #(.width(32)) register_16 (.D(I27), .en(we), .Q(O27), .clk(clk), .clr(reset));
  Register #(.width(32)) register_17 (.D(I4), .en(we), .Q(O4), .clk(clk), .clr(reset));
  Register #(.width(32)) register_18 (.D(I12), .en(we), .Q(O12), .clk(clk), .clr(reset));
  Register #(.width(32)) register_19 (.D(I20), .en(we), .Q(O20), .clk(clk), .clr(reset));
  Register #(.width(32)) register_20 (.D(I28), .en(we), .Q(O28), .clk(clk), .clr(reset));
  Register #(.width(32)) register_21 (.D(I5), .en(we), .Q(O5), .clk(clk), .clr(reset));
  Register #(.width(32)) register_22 (.D(I13), .en(we), .Q(O13), .clk(clk), .clr(reset));
  Register #(.width(32)) register_23 (.D(I21), .en(we), .Q(O21), .clk(clk), .clr(reset));
  Register #(.width(32)) register_24 (.D(I29), .en(we), .Q(O29), .clk(clk), .clr(reset));
  Register #(.width(32)) register_25 (.D(I6), .en(we), .Q(O6), .clk(clk), .clr(reset));
  Register #(.width(32)) register_26 (.D(I14), .en(we), .Q(O14), .clk(clk), .clr(reset));
  Register #(.width(32)) register_27 (.D(I22), .en(we), .Q(O22), .clk(clk), .clr(reset));
  Register #(.width(32)) register_28 (.D(I30), .en(we), .Q(O30), .clk(clk), .clr(reset));
  Register #(.width(32)) register_29 (.D(I7), .en(we), .Q(O7), .clk(clk), .clr(reset));
  Register #(.width(32)) register_30 (.D(I15), .en(we), .Q(O15), .clk(clk), .clr(reset));
  Register #(.width(32)) register_31 (.D(I23), .en(we), .Q(O23), .clk(clk), .clr(reset));
  Register #(.width(32)) register_32 (.D(I31), .en(we), .Q(O31), .clk(clk), .clr(reset));
endmodule

module Controller (
  input  [5:0] Op,
  input  [5:0] func,
  output [1:0] RegDst,
  output MemWrite,
  output branch_beq,
  output branch_j_jal,
  output branch_jr,
  output [1:0] EXTop,
  output RegWrite,
  output ALUSrc,
  output MemRead,
  output [1:0] MemtoReg,
  output [1:0] ALUop,
  output [1:0] Ssel,
  output [1:0] Lsel
);

  wire addu, beq, j, jal, jr, lb, lh, lui, lw, nop, not_1_out, not_2_out, not_3_out, not_4_out, not_5_out,
       not_6_out, not_7_out, not_8_out, not_9_out, not_10_out, not_11_out, not_12_out, ori, r, sb, sh, subu,
       sw;

  not not_1 (not_1_out, Op[5]);
  not not_2 (not_2_out, Op[3]);
  not not_3 (not_3_out, Op[4]);
  not not_4 (not_4_out, Op[1]);
  not not_5 (not_5_out, Op[2]);
  not not_6 (not_6_out, Op[0]);
  and u_LW (lw, Op[5], not_3_out, not_2_out, not_5_out, Op[1], Op[0]);
  and u_SW (sw, Op[5], not_3_out, Op[3], not_5_out, Op[1], Op[0]);
  and u_R (r, not_1_out, not_3_out, not_2_out, not_5_out, not_4_out, not_6_out);
  and u_ORI (ori, not_1_out, not_3_out, Op[3], Op[2], not_4_out, Op[0]);
  and u_J (j, not_1_out, not_3_out, not_2_out, not_5_out, Op[1], not_6_out);
  and u_JAL (jal, not_1_out, not_3_out, not_2_out, not_5_out, Op[1], Op[0]);
  and u_BEQ (beq, not_1_out, not_3_out, not_2_out, Op[2], not_4_out, not_6_out);
  and u_LUI (lui, not_1_out, not_3_out, Op[3], Op[2], Op[1], Op[0]);
  and u_LH (lh, Op[5], not_3_out, not_2_out, not_5_out, not_4_out, Op[0]);
  and u_SH (sh, Op[5], not_3_out, Op[3], not_5_out, not_4_out, Op[0]);
  and u_LB (lb, Op[5], not_3_out, not_2_out, not_5_out, not_4_out, not_6_out);
  and u_SB (sb, Op[5], not_3_out, Op[3], not_5_out, not_4_out, not_6_out);
  not not_7 (not_7_out, func[5]);
  not not_8 (not_8_out, func[4]);
  not not_9 (not_9_out, func[3]);
  not not_10 (not_10_out, func[1]);
  not not_11 (not_11_out, func[2]);
  not not_12 (not_12_out, func[0]);
  and u_ADDU (addu, r, func[5], not_8_out, not_9_out, not_11_out, not_10_out, func[0]);
  and u_SUBU (subu, r, func[5], not_8_out, not_9_out, not_11_out, func[1], func[0]);
  and u_JR (jr, r, not_7_out, not_8_out, func[3], not_11_out, not_10_out, not_12_out);
  and u_NOP (nop, r, not_7_out, not_8_out, not_9_out, not_11_out, not_10_out, not_12_out);
  buf or_1 (RegDst[0], r);  // OR_Gate
  buf or_2 (RegDst[1], jal);  // OR_Gate
  or or_3 (MemWrite, sw, sh, sb);
  buf or_4 (branch_beq, beq);  // OR_Gate
  or or_5 (branch_j_jal, j, jal);
  buf or_6 (branch_jr, jr);  // OR_Gate
  or or_7 (EXTop[0], lw, sw, lh, sh, lb, sb);
  buf or_8 (EXTop[1], lui);  // OR_Gate
  or or_9 (RegWrite, lb, lh, jal, lui, ori, r, lw);
  or or_10 (ALUSrc, lw, sw, ori, lui, lh, sh, lb, sb);
  or or_11 (MemRead, lw, lh, lb);
  or or_12 (MemtoReg[0], lw, lh, lb);
  buf or_13 (MemtoReg[1], jal);  // OR_Gate
  buf or_14 (ALUop[0], subu);  // OR_Gate
  buf or_15 (ALUop[1], ori);  // OR_Gate
  or or_16 (Ssel[0], sb, lb);
  or or_17 (Ssel[1], sh, lh);
  or or_18 (Lsel[0], lb, sb);
  or or_19 (Lsel[1], sh, lh);

  // Notes on the sheet:
  //   有EXT就为1
endmodule

module UseFunc (
  input  [5:0] Op,
  input  [5:0] func,
  output out_3,
  output out_4,
  output out_5,
  output out_6,
  output out_7,
  output out_8,
  output out_9,
  output out_10,
  output out_11,
  output out_12,
  output out_13,
  output out_14,
  output out_15,
  output out_16,
  output out_17
);

  wire not_1_out, not_2_out, not_3_out, not_4_out, not_5_out, not_6_out, not_7_out, not_8_out, not_9_out,
       not_10_out, not_11_out, not_12_out, r;

  not not_1 (not_1_out, Op[5]);
  not not_2 (not_2_out, Op[4]);
  not not_3 (not_3_out, Op[3]);
  not not_4 (not_4_out, Op[2]);
  not not_5 (not_5_out, Op[1]);
  not not_6 (not_6_out, Op[0]);
  and LW (out_3, Op[5], not_2_out, not_3_out, not_4_out, Op[1], Op[0]);
  and SW (out_4, Op[5], not_2_out, Op[3], not_4_out, Op[1], Op[0]);
  and u_R (r, not_1_out, not_2_out, not_3_out, not_4_out, not_5_out, not_6_out);
  and ORI (out_7, not_1_out, not_2_out, Op[3], Op[2], not_5_out, Op[0]);
  and J (out_9, not_1_out, not_2_out, not_3_out, not_4_out, Op[1], not_6_out);
  and JAL (out_10, not_1_out, not_2_out, not_3_out, not_4_out, Op[1], Op[0]);
  and BEQ (out_12, not_1_out, not_2_out, not_3_out, Op[2], not_5_out, not_6_out);
  and LUI (out_8, not_1_out, not_2_out, Op[3], Op[2], Op[1], Op[0]);
  and LH (out_14, Op[5], not_2_out, not_3_out, not_4_out, not_5_out, Op[0]);
  and SH (out_15, Op[5], not_2_out, Op[3], not_4_out, not_5_out, Op[0]);
  and LB (out_16, Op[5], not_2_out, not_3_out, not_4_out, not_5_out, not_6_out);
  and SB (out_17, Op[5], not_2_out, Op[3], not_4_out, not_5_out, not_6_out);
  not not_7 (not_7_out, func[5]);
  not not_8 (not_8_out, func[3]);
  not not_9 (not_9_out, func[4]);
  not not_10 (not_10_out, func[2]);
  not not_11 (not_11_out, func[1]);
  not not_12 (not_12_out, func[0]);
  and ADDU (out_5, r, func[5], not_9_out, not_8_out, not_10_out, not_11_out, func[0]);
  and SUBU (out_6, r, func[5], not_9_out, not_8_out, not_10_out, func[1], func[0]);
  and JR (out_11, r, not_7_out, not_9_out, func[3], not_10_out, not_11_out, not_12_out);
  and NOP (out_13, r, not_7_out, not_9_out, not_8_out, not_10_out, not_11_out, not_12_out);

  // Other names for the same wires on the sheet: addu = out_5; beq = out_12; j = out_9; jal = out_10; jr = out_11;
  //   lb = out_16; lh = out_14; lui = out_8; lw = out_3; nop = out_13; ori = out_7; sb = out_17; sh = out_15;
  //   subu = out_6; sw = out_4
endmodule

module EXT (
  input  [15:0] in_1,
  input  [1:0] in_2,
  output [31:0] out_3
);

  wire [31:0] bit_extender_1_out, bit_extender_2_out;

  assign bit_extender_1_out = {{16{1'b0}}, in_1};  // Bit_Extender bit_extender_1
  assign bit_extender_2_out = {{16{in_1[15]}}, in_1};  // Bit_Extender bit_extender_2
  Multiplexer #(.select(2), .width(32), .enable("false")) multiplexer_1 (
    .in0(bit_extender_1_out), .in1(bit_extender_2_out), .in2({in_1, {16{1'b0}}}), .out(out_3), .sel(in_2));  // open: in3
endmodule

module ALU (
  input  [31:0] in_1,
  input  [31:0] in_2,
  input  [1:0] ALUOP,
  output Zero,
  output [31:0] out_5
);

  wire comparator_1_eq;
  wire [31:0] adder_1_out, bit_extender_1_out, or_1_out, subtractor_1_out;

  Adder #(.width(32)) adder_1 (.a(in_1), .b(in_2), .out(adder_1_out));  // open: cin, cout
  Subtractor #(.width(32)) subtractor_1 (.a(in_1), .b(in_2), .out(subtractor_1_out));  // open: bin, bout
  assign or_1_out = in_1 | in_2;  // OR_Gate or_1, 32 bits wide
  Multiplexer #(.select(2), .width(32), .enable("false")) multiplexer_1 (
    .in0(adder_1_out), .in1(subtractor_1_out), .in2(or_1_out), .in3(bit_extender_1_out), .out(out_5),
    .sel(ALUOP));
  Comparator #(.width(32)) comparator_1 (.a(in_1), .b(in_2), .eq(comparator_1_eq));  // open: gt, lt
  assign bit_extender_1_out = {{31{1'b0}}, comparator_1_eq};  // Bit_Extender bit_extender_1
  Comparator #(.width(32)) comparator_2 (.a(out_5), .b({32{1'b0}}), .eq(Zero));  // open: gt, lt
endmodule

module DM (
  input  [1:0] SSel,
  input  [1:0] Lsel,
  input  [31:0] Addr,
  input  in_4,
  input  in_5,
  input  in_6,
  input  [31:0] WriteData,
  output [31:0] RD,
  output [31:0] W_MemData
);

  wire decoder_1_out0, decoder_1_out1, decoder_1_out2, decoder_1_out3, decoder_2_out0, decoder_2_out1;
  wire [7:0] _7_0, _15_8, _23_16, _24_31, multiplexer_1_out, multiplexer_2_out, multiplexer_3_out,
       multiplexer_4_out, multiplexer_8_out;
  wire [15:0] multiplexer_5_out, multiplexer_6_out, multiplexer_9_out;
  wire [31:0] bit_extender_1_out, bit_extender_2_out;

  Decoder #(.select(2)) decoder_1 (
    .out0(decoder_1_out0), .out1(decoder_1_out1), .out2(decoder_1_out2), .out3(decoder_1_out3),
    .sel(Addr[1:0]));  // open: en
  Decoder decoder_2 (.out0(decoder_2_out0), .out1(decoder_2_out1), .sel(Addr[1]));  // open: en
  Multiplexer #(.width(8), .enable("false")) multiplexer_1 (
    .in0(_7_0), .in1(WriteData[7:0]), .out(multiplexer_1_out), .sel(decoder_1_out0));
  Multiplexer #(.width(8), .enable("false")) multiplexer_2 (
    .in0(_15_8), .in1(WriteData[7:0]), .out(multiplexer_2_out), .sel(decoder_1_out1));
  Multiplexer #(.width(8), .enable("false")) multiplexer_3 (
    .in0(_23_16), .in1(WriteData[7:0]), .out(multiplexer_3_out), .sel(decoder_1_out2));
  Multiplexer #(.width(8), .enable("false")) multiplexer_4 (
    .in0(_24_31), .in1(WriteData[7:0]), .out(multiplexer_4_out), .sel(decoder_1_out3));
  Multiplexer #(.width(16), .enable("false")) multiplexer_5 (
    .in0({_15_8, _7_0}), .in1(WriteData[15:0]), .out(multiplexer_5_out), .sel(decoder_2_out0));
  Multiplexer #(.width(16), .enable("false")) multiplexer_6 (
    .in0({_24_31, _23_16}), .in1(WriteData[15:0]), .out(multiplexer_6_out), .sel(decoder_2_out1));
  Multiplexer #(.select(2), .width(32), .enable("false")) multiplexer_7 (
    .in0(WriteData), .in1({multiplexer_4_out, multiplexer_3_out, multiplexer_2_out, multiplexer_1_out}),
    .in2({multiplexer_6_out, multiplexer_5_out}), .out(W_MemData), .sel(SSel));  // open: in3
  RAM #(.addrWidth(5), .dataWidth(32), .bus("separate")) ram_1 (
    .addr(Addr[6:2]), .din(W_MemData), .data({_24_31, _23_16, _15_8, _7_0}), .str(in_4), .clk(in_5),
    .ld(1'b1), .clr(in_6));  // open: sel
  Multiplexer #(.select(2), .width(8), .enable("false")) multiplexer_8 (
    .in0(_7_0), .in1(_15_8), .in2(_23_16), .in3(_24_31), .out(multiplexer_8_out), .sel(Addr[1:0]));
  Multiplexer #(.width(16), .enable("false")) multiplexer_9 (
    .in0({_15_8, _7_0}), .in1({_24_31, _23_16}), .out(multiplexer_9_out), .sel(Addr[1]));
  assign bit_extender_1_out = {{24{multiplexer_8_out[7]}}, multiplexer_8_out};  // Bit_Extender bit_extender_1
  assign bit_extender_2_out = {{16{multiplexer_9_out[15]}}, multiplexer_9_out};  // Bit_Extender bit_extender_2
  Multiplexer #(.select(2), .width(32), .enable("false")) multiplexer_10 (
    .in0({_24_31, _23_16, _15_8, _7_0}), .in1(bit_extender_1_out), .in2(bit_extender_2_out), .out(RD),
    .sel(Lsel));  // open: in3
endmodule

module FD_Reg (
  input  in_1,
  input  in_2,
  input  [31:0] instr_i,
  input  [31:0] pc_i,
  input  [31:0] pc_4_i,
  input  [31:0] pc_8_i,
  input  in_7,
  output [31:0] instr_o,
  output [31:0] pc_o,
  output [31:0] pc_4_o,
  output [31:0] pc_8_o
);

  wire clk_prime, not_1_out, not_2_out, not_3_out, not_4_out;

  buf and_1 (clk_prime, in_1);  // AND_Gate
  not not_1 (not_1_out, in_7);
  not not_2 (not_2_out, in_7);
  not not_3 (not_3_out, in_7);
  not not_4 (not_4_out, in_7);
  Register #(.width(32)) register_1 (.D(instr_i), .en(not_1_out), .Q(instr_o), .clk(clk_prime), .clr(in_2));
  Register #(.width(32)) register_2 (.D(pc_i), .en(not_2_out), .Q(pc_o), .clk(clk_prime), .clr(in_2));
  Register #(.width(32)) register_3 (.D(pc_4_i), .en(not_3_out), .Q(pc_4_o), .clk(clk_prime), .clr(in_2));
  Register #(.width(32)) register_4 (.D(pc_8_i), .en(not_4_out), .Q(pc_8_o), .clk(clk_prime), .clr(in_2));

  // Other names for the same wires on the sheet: clk = in_1; F_D_stall = in_7; reset = in_2
endmodule

module DE_Reg (
  input  in_1,
  input  in_2,
  input  [1:0] RegDst_i,
  input  MemWrite_i,
  input  RegWrite_i,
  input  ALUSrc_i,
  input  MemRead_i,
  input  [1:0] MemToReg_i,
  input  [1:0] ALUop_i,
  input  [31:0] RD1_i,
  input  [31:0] RD2_i,
  input  in_12,
  input  [4:0] rs_i,
  input  [4:0] rt_i,
  input  [4:0] rd_i,
  input  [31:0] pc_i,
  input  [31:0] pc_4_i,
  input  [31:0] pc_8_i,
  input  [31:0] EXTresult_i,
  input  [31:0] instr_i,
  output [1:0] RegDst_o,
  output MemWrite_o,
  output RegWrite_o,
  output ALUSrc_o,
  output MemRead_o,
  output [1:0] MemToReg_o,
  output [1:0] ALUop_o,
  output [31:0] RD1_o,
  output [31:0] RD2_o,
  output [4:0] rs_o,
  output [4:0] rt_o,
  output [4:0] rd_o,
  output [31:0] pc_o,
  output [31:0] pc_4_o,
  output [31:0] pc_8_o,
  output [31:0] EXTresult_o,
  output [31:0] instr_o
);

  wire multiplexer_2_out, multiplexer_3_out, multiplexer_4_out, multiplexer_5_out;
  wire [1:0] multiplexer_1_out, multiplexer_6_out, multiplexer_7_out;
  wire [4:0] multiplexer_10_out, multiplexer_11_out, multiplexer_12_out;
  wire [31:0] multiplexer_8_out, multiplexer_9_out, multiplexer_13_out, multiplexer_14_out,
       multiplexer_15_out, multiplexer_16_out, multiplexer_17_out;

  Multiplexer #(.width(2), .enable("false")) multiplexer_1 (
    .in0(RegDst_i), .in1(2'b00), .out(multiplexer_1_out), .sel(in_12));
  Multiplexer #(.enable("false")) multiplexer_2 (.in0(MemWrite_i), .in1(1'b0), .out(multiplexer_2_out), .sel(in_12));
  Multiplexer #(.enable("false")) multiplexer_3 (.in0(RegWrite_i), .in1(1'b0), .out(multiplexer_3_out), .sel(in_12));
  Multiplexer #(.enable("false")) multiplexer_4 (.in0(ALUSrc_i), .in1(1'b0), .out(multiplexer_4_out), .sel(in_12));
  Multiplexer #(.enable("false")) multiplexer_5 (.in0(MemRead_i), .in1(1'b0), .out(multiplexer_5_out), .sel(in_12));
  Multiplexer #(.width(2), .enable("false")) multiplexer_6 (
    .in0(MemToReg_i), .in1(2'b00), .out(multiplexer_6_out), .sel(in_12));
  Multiplexer #(.width(2), .enable("false")) multiplexer_7 (
    .in0(ALUop_i), .in1(2'b00), .out(multiplexer_7_out), .sel(in_12));
  Multiplexer #(.width(32), .enable("false")) multiplexer_8 (
    .in0(RD1_i), .in1({32{1'b0}}), .out(multiplexer_8_out), .sel(in_12));
  Multiplexer #(.width(32), .enable("false")) multiplexer_9 (
    .in0(RD2_i), .in1({32{1'b0}}), .out(multiplexer_9_out), .sel(in_12));
  Multiplexer #(.width(5), .enable("false")) multiplexer_10 (
    .in0(rs_i), .in1({5{1'b0}}), .out(multiplexer_10_out), .sel(in_12));
  Multiplexer #(.width(5), .enable("false")) multiplexer_11 (
    .in0(rt_i), .in1({5{1'b0}}), .out(multiplexer_11_out), .sel(in_12));
  Multiplexer #(.width(5), .enable("false")) multiplexer_12 (
    .in0(rd_i), .in1({5{1'b0}}), .out(multiplexer_12_out), .sel(in_12));
  Multiplexer #(.width(32), .enable("false")) multiplexer_13 (
    .in0(pc_i), .in1({32{1'b0}}), .out(multiplexer_13_out), .sel(in_12));
  Multiplexer #(.width(32), .enable("false")) multiplexer_14 (
    .in0(pc_4_i), .in1({32{1'b0}}), .out(multiplexer_14_out), .sel(in_12));
  Multiplexer #(.width(32), .enable("false")) multiplexer_15 (
    .in0(pc_8_i), .in1({32{1'b0}}), .out(multiplexer_15_out), .sel(in_12));
  Multiplexer #(.width(32), .enable("false")) multiplexer_16 (
    .in0(EXTresult_i), .in1({32{1'b0}}), .out(multiplexer_16_out), .sel(in_12));
  Multiplexer #(.width(32), .enable("false")) multiplexer_17 (
    .in0(instr_i), .in1({32{1'b0}}), .out(multiplexer_17_out), .sel(in_12));
  Register #(.width(2)) register_1 (.D(multiplexer_1_out), .Q(RegDst_o), .clk(in_1), .clr(in_2));  // open: en
  Register #(.width(1)) register_2 (.D(multiplexer_2_out), .Q(MemWrite_o), .clk(in_1), .clr(in_2));  // open: en
  Register #(.width(1)) register_3 (.D(multiplexer_3_out), .Q(RegWrite_o), .clk(in_1), .clr(in_2));  // open: en
  Register #(.width(1)) register_4 (.D(multiplexer_4_out), .Q(ALUSrc_o), .clk(in_1), .clr(in_2));  // open: en
  Register #(.width(1)) register_5 (.D(multiplexer_5_out), .Q(MemRead_o), .clk(in_1), .clr(in_2));  // open: en
  Register #(.width(32)) register_6 (.D(multiplexer_8_out), .Q(RD1_o), .clk(in_1), .clr(in_2));  // open: en
  Register #(.width(32)) register_7 (.D(multiplexer_9_out), .Q(RD2_o), .clk(in_1), .clr(in_2));  // open: en
  Register #(.width(5)) register_8 (.D(multiplexer_10_out), .Q(rs_o), .clk(in_1), .clr(in_2));  // open: en
  Register #(.width(5)) register_9 (.D(multiplexer_11_out), .Q(rt_o), .clk(in_1), .clr(in_2));  // open: en
  Register #(.width(5)) register_10 (.D(multiplexer_12_out), .Q(rd_o), .clk(in_1), .clr(in_2));  // open: en
  Register #(.width(32)) register_11 (.D(multiplexer_13_out), .Q(pc_o), .clk(in_1), .clr(in_2));  // open: en
  Register #(.width(32)) register_12 (.D(multiplexer_14_out), .Q(pc_4_o), .clk(in_1), .clr(in_2));  // open: en
  Register #(.width(32)) register_13 (.D(multiplexer_15_out), .Q(pc_8_o), .clk(in_1), .clr(in_2));  // open: en
  Register #(.width(32)) register_14 (.D(multiplexer_16_out), .Q(EXTresult_o), .clk(in_1), .clr(in_2));  // open: en
  Register #(.width(2)) register_15 (.D(multiplexer_6_out), .Q(MemToReg_o), .clk(in_1), .clr(in_2));  // open: en
  Register #(.width(2)) register_16 (.D(multiplexer_7_out), .Q(ALUop_o), .clk(in_1), .clr(in_2));  // open: en
  Register #(.width(32)) register_17 (.D(multiplexer_17_out), .Q(instr_o), .clk(in_1), .clr(in_2));  // open: en

  // Other names for the same wires on the sheet: clk = in_1; clk_prime = in_1; flush = in_12; Reset = in_2
endmodule

module EM_Reg (
  input  in_1,
  input  in_2,
  input  MemWrite_i,
  input  RegWrite_i,
  input  MemRead_i,
  input  [1:0] MemToReg_i,
  input  [31:0] aluresult_i,
  input  [31:0] writedata_i,
  input  [4:0] writereg_i,
  input  [31:0] pc_i,
  input  [31:0] pc_4_i,
  input  [31:0] pc_8_i,
  input  [31:0] instr_i,
  input  [3:0] tnew_E,
  output MemWrite_o,
  output RegWrite_o,
  output MemRead_o,
  output [1:0] MemToReg_o,
  output [31:0] out_19,
  output [31:0] out_20,
  output [4:0] out_21,
  output [31:0] pc_o,
  output [31:0] pc_4_o,
  output [31:0] pc_8_o,
  output [31:0] out_25,
  output [3:0] tnew_M
);

  wire comparator_1_lt;
  wire [3:0] multiplexer_1_out, subtractor_1_out;

  Subtractor #(.width(4)) subtractor_1 (.a(tnew_E), .b(4'b0001), .out(subtractor_1_out));  // open: bin, bout
  Register #(.width(1)) register_1 (.D(MemWrite_i), .Q(MemWrite_o), .clk(in_1), .clr(in_2));  // open: en
  Register #(.width(1)) register_2 (.D(RegWrite_i), .Q(RegWrite_o), .clk(in_1), .clr(in_2));  // open: en
  Register #(.width(1)) register_3 (.D(MemRead_i), .Q(MemRead_o), .clk(in_1), .clr(in_2));  // open: en
  Register #(.width(2)) register_4 (.D(MemToReg_i), .Q(MemToReg_o), .clk(in_1), .clr(in_2));  // open: en
  Register #(.width(32)) register_5 (.D(aluresult_i), .Q(out_19), .clk(in_1), .clr(in_2));  // open: en
  Register #(.width(32)) register_6 (.D(writedata_i), .Q(out_20), .clk(in_1), .clr(in_2));  // open: en
  Register #(.width(5)) register_7 (.D(writereg_i), .Q(out_21), .clk(in_1), .clr(in_2));  // open: en
  Register #(.width(32)) register_8 (.D(pc_i), .Q(pc_o), .clk(in_1), .clr(in_2));  // open: en
  Register #(.width(32)) register_9 (.D(pc_4_i), .Q(pc_4_o), .clk(in_1), .clr(in_2));  // open: en
  Register #(.width(32)) register_10 (.D(pc_8_i), .Q(pc_8_o), .clk(in_1), .clr(in_2));  // open: en
  Register #(.width(32)) register_11 (.D(instr_i), .Q(out_25), .clk(in_1), .clr(in_2));  // open: en
  Comparator #(.width(4)) comparator_1 (.a(subtractor_1_out), .b(4'b0000), .lt(comparator_1_lt));  // open: gt, eq
  Multiplexer #(.width(4), .enable("false")) multiplexer_1 (
    .in0(subtractor_1_out), .in1(4'b0000), .out(multiplexer_1_out), .sel(comparator_1_lt));
  Register #(.width(4)) register_12 (.D(multiplexer_1_out), .Q(tnew_M), .clk(in_1), .clr(in_2));  // open: en

  // Other names for the same wires on the sheet: clk = in_1; clk_prime = in_1; Reset = in_2
endmodule

module MW_Reg (
  input  in_1,
  input  in_2,
  input  RegWrite,
  input  [1:0] MemtoReg,
  input  [31:0] aluresult_i,
  input  [31:0] writedata_i,
  input  [31:0] readdata_i,
  input  [31:0] pc_i,
  input  [31:0] pc_4_i,
  input  [31:0] pc_8_i,
  input  [31:0] instr_i,
  input  [4:0] writereg_i,
  input  [31:0] memaddr,
  input  [31:0] memdata,
  input  memwrite,
  input  [3:0] tnew_M,
  output out_17,
  output [1:0] out_18,
  output [31:0] out_19,
  output [31:0] out_20,
  output [31:0] out_21,
  output [31:0] pc_o,
  output [31:0] pc_4_o,
  output [31:0] pc_8_o,
  output [31:0] out_25,
  output [4:0] out_26,
  output [31:0] out_27,
  output [31:0] out_28,
  output out_29,
  output [3:0] tnew_W
);

  wire comparator_1_lt;
  wire [3:0] multiplexer_1_out, subtractor_1_out;

  Register #(.width(1)) register_1 (.D(RegWrite), .Q(out_17), .clk(in_1), .clr(in_2));  // open: en
  Register #(.width(2)) register_2 (.D(MemtoReg), .Q(out_18), .clk(in_1), .clr(in_2));  // open: en
  Register #(.width(32)) register_3 (.D(aluresult_i), .Q(out_19), .clk(in_1), .clr(in_2));  // open: en
  Register #(.width(32)) register_4 (.D(writedata_i), .Q(out_20), .clk(in_1), .clr(in_2));  // open: en
  Register #(.width(32)) register_5 (.D(readdata_i), .Q(out_21), .clk(in_1), .clr(in_2));  // open: en
  Register #(.width(32)) register_6 (.D(pc_i), .Q(pc_o), .clk(in_1), .clr(in_2));  // open: en
  Register #(.width(32)) register_7 (.D(pc_4_i), .Q(pc_4_o), .clk(in_1), .clr(in_2));  // open: en
  Register #(.width(32)) register_8 (.D(pc_8_i), .Q(pc_8_o), .clk(in_1), .clr(in_2));  // open: en
  Register #(.width(32)) register_9 (.D(instr_i), .Q(out_25), .clk(in_1), .clr(in_2));  // open: en
  Register #(.width(5)) register_10 (.D(writereg_i), .Q(out_26), .clk(in_1), .clr(in_2));  // open: en
  Register #(.width(32)) register_11 (.D(memaddr), .Q(out_27), .clk(in_1), .clr(in_2));  // open: en
  Register #(.width(32)) register_12 (.D(memdata), .Q(out_28), .clk(in_1), .clr(in_2));  // open: en
  Subtractor #(.width(4)) subtractor_1 (.a(tnew_M), .b(4'b0001), .out(subtractor_1_out));  // open: bin, bout
  // Probe on subtractor_1_out
  Register #(.width(1)) register_13 (.D(memwrite), .Q(out_29), .clk(in_1), .clr(in_2));  // open: en
  Comparator #(.width(4)) comparator_1 (.a(subtractor_1_out), .b(4'b0000), .lt(comparator_1_lt));  // open: gt, eq
  // Probe on multiplexer_1_out
  Multiplexer #(.width(4), .enable("false")) multiplexer_1 (
    .in0(subtractor_1_out), .in1(4'b0000), .out(multiplexer_1_out), .sel(comparator_1_lt));
  Register #(.width(4)) register_14 (.D(multiplexer_1_out), .Q(tnew_W), .clk(in_1), .clr(in_2));  // open: en

  // Other names for the same wires on the sheet: clk = in_1; clk_prime = in_1; Reset = in_2
endmodule

module forwardUnit (
  input  [4:0] s1_D,
  input  [4:0] s2_D,
  input  [4:0] s1_E,
  input  [4:0] s2_E,
  input  [4:0] des_E,
  input  [3:0] tNew_E,
  input  [4:0] s2_M,
  input  [3:0] tNew_M,
  input  [4:0] des_M,
  input  [3:0] tNew_W,
  input  [4:0] des_W,
  output [1:0] fRsDsel,
  output [1:0] fRtDsel,
  output [1:0] fRsEsel,
  output [1:0] fRtEsel,
  output fRtMsel
);

  wire and_1_out, and_2_out, and_3_out, and_4_out, and_5_out, and_6_out, and_7_out, and_8_out, and_9_out,
       comparator_1_eq, comparator_2_eq, comparator_3_eq, comparator_4_eq, comparator_5_eq, comparator_6_eq,
       comparator_7_eq, comparator_8_eq, comparator_9_eq, comparator_10_eq, comparator_11_eq,
       comparator_12_eq, comparator_13_eq, comparator_14_eq, comparator_15_eq, comparator_16_eq,
       comparator_17_eq, comparator_18_eq, comparator_19_eq, comparator_20_eq, comparator_21_eq,
       comparator_22_eq, comparator_23_eq, comparator_24_eq, comparator_25_eq, comparator_26_eq,
       comparator_27_eq, not_1_out, not_2_out, not_3_out, not_4_out, not_5_out, not_6_out, not_7_out,
       not_8_out, not_9_out;
  wire [1:0] multiplexer_1_out, multiplexer_2_out, multiplexer_5_out, multiplexer_6_out;

  not not_1 (not_1_out, comparator_1_eq);
  Comparator #(.width(5), .mode("unsigned")) comparator_1 (
    .a(s1_D), .b({5{1'b0}}), .eq(comparator_1_eq));  // open: gt, lt
  Comparator #(.width(5), .mode("unsigned")) comparator_2 (.a(s1_D), .b(des_M), .eq(comparator_2_eq));  // open: gt, lt
  Comparator #(.width(4), .mode("unsigned")) comparator_3 (
    .a(tNew_M), .b(4'b0000), .eq(comparator_3_eq));  // open: gt, lt
  not not_2 (not_2_out, comparator_4_eq);
  Comparator #(.width(5), .mode("unsigned")) comparator_4 (
    .a(s1_D), .b({5{1'b0}}), .eq(comparator_4_eq));  // open: gt, lt
  Comparator #(.width(5), .mode("unsigned")) comparator_5 (.a(s1_D), .b(des_E), .eq(comparator_5_eq));  // open: gt, lt
  Comparator #(.width(4), .mode("unsigned")) comparator_6 (
    .a(tNew_E), .b(4'b0000), .eq(comparator_6_eq));  // open: gt, lt
  Comparator #(.width(5), .mode("unsigned")) comparator_7 (
    .a(s2_D), .b({5{1'b0}}), .eq(comparator_7_eq));  // open: gt, lt
  Comparator #(.width(5), .mode("unsigned")) comparator_8 (.a(s2_D), .b(des_M), .eq(comparator_8_eq));  // open: gt, lt
  Comparator #(.width(4), .mode("unsigned")) comparator_9 (
    .a(tNew_M), .b(4'b0000), .eq(comparator_9_eq));  // open: gt, lt
  Comparator #(.width(5), .mode("unsigned")) comparator_10 (
    .a(s2_D), .b({5{1'b0}}), .eq(comparator_10_eq));  // open: gt, lt
  Comparator #(.width(5), .mode("unsigned")) comparator_11 (
    .a(s2_D), .b(des_E), .eq(comparator_11_eq));  // open: gt, lt
  Comparator #(.width(4), .mode("unsigned")) comparator_12 (
    .a(tNew_E), .b(4'b0000), .eq(comparator_12_eq));  // open: gt, lt
  and and_1 (and_1_out, not_1_out, comparator_2_eq, comparator_3_eq);
  and and_2 (and_2_out, not_2_out, comparator_5_eq, comparator_6_eq);
  not not_3 (not_3_out, comparator_7_eq);
  not not_4 (not_4_out, comparator_10_eq);
  Multiplexer #(.width(2)) multiplexer_1 (
    .in0(2'b00), .in1(2'b10), .out(multiplexer_1_out), .sel(and_1_out));  // open: en
  and and_3 (and_3_out, not_3_out, comparator_8_eq, comparator_9_eq);
  and and_4 (and_4_out, not_4_out, comparator_11_eq, comparator_12_eq);
  Multiplexer #(.width(2)) multiplexer_2 (
    .in0(2'b00), .in1(2'b10), .out(multiplexer_2_out), .sel(and_3_out));  // open: en
  Multiplexer #(.width(2)) multiplexer_3 (
    .in0(multiplexer_1_out), .in1(2'b01), .out(fRsDsel), .sel(and_2_out));  // open: en
  Multiplexer #(.width(2)) multiplexer_4 (
    .in0(multiplexer_2_out), .in1(2'b01), .out(fRtDsel), .sel(and_4_out));  // open: en
  Comparator #(.width(5), .mode("unsigned")) comparator_13 (
    .a(s1_E), .b({5{1'b0}}), .eq(comparator_13_eq));  // open: gt, lt
  Comparator #(.width(5), .mode("unsigned")) comparator_14 (
    .a(s1_E), .b(des_W), .eq(comparator_14_eq));  // open: gt, lt
  Comparator #(.width(4), .mode("unsigned")) comparator_15 (
    .a(tNew_W), .b(4'b0000), .eq(comparator_15_eq));  // open: gt, lt
  Comparator #(.width(5), .mode("unsigned")) comparator_16 (
    .a(s1_E), .b({5{1'b0}}), .eq(comparator_16_eq));  // open: gt, lt
  Comparator #(.width(5), .mode("unsigned")) comparator_17 (
    .a(s1_E), .b(des_M), .eq(comparator_17_eq));  // open: gt, lt
  Comparator #(.width(4), .mode("unsigned")) comparator_18 (
    .a(tNew_M), .b(4'b0000), .eq(comparator_18_eq));  // open: gt, lt
  Comparator #(.width(5), .mode("unsigned")) comparator_19 (
    .a(s2_E), .b({5{1'b0}}), .eq(comparator_19_eq));  // open: gt, lt
  Comparator #(.width(5), .mode("unsigned")) comparator_20 (
    .a(s2_E), .b(des_W), .eq(comparator_20_eq));  // open: gt, lt
  Comparator #(.width(4), .mode("unsigned")) comparator_21 (
    .a(tNew_W), .b(4'b0000), .eq(comparator_21_eq));  // open: gt, lt
  Comparator #(.width(5), .mode("unsigned")) comparator_22 (
    .a(s2_E), .b({5{1'b0}}), .eq(comparator_22_eq));  // open: gt, lt
  Comparator #(.width(5), .mode("unsigned")) comparator_23 (
    .a(s2_E), .b(des_M), .eq(comparator_23_eq));  // open: gt, lt
  Comparator #(.width(4), .mode("unsigned")) comparator_24 (
    .a(tNew_M), .b(4'b0000), .eq(comparator_24_eq));  // open: gt, lt
  not not_5 (not_5_out, comparator_13_eq);
  not not_6 (not_6_out, comparator_16_eq);
  not not_7 (not_7_out, comparator_19_eq);
  not not_8 (not_8_out, comparator_22_eq);
  and and_5 (and_5_out, not_5_out, comparator_14_eq, comparator_15_eq);
  and and_6 (and_6_out, not_6_out, comparator_17_eq, comparator_18_eq);
  and and_7 (and_7_out, not_7_out, comparator_20_eq, comparator_21_eq);
  and and_8 (and_8_out, not_8_out, comparator_23_eq, comparator_24_eq);
  Multiplexer #(.width(2)) multiplexer_5 (
    .in0(2'b00), .in1(2'b10), .out(multiplexer_5_out), .sel(and_5_out));  // open: en
  Multiplexer #(.width(2)) multiplexer_6 (
    .in0(2'b00), .in1(2'b10), .out(multiplexer_6_out), .sel(and_7_out));  // open: en
  Multiplexer #(.width(2)) multiplexer_7 (
    .in0(multiplexer_5_out), .in1(2'b01), .out(fRsEsel), .sel(and_6_out));  // open: en
  Multiplexer #(.width(2)) multiplexer_8 (
    .in0(multiplexer_6_out), .in1(2'b01), .out(fRtEsel), .sel(and_8_out));  // open: en
  Comparator #(.width(5), .mode("unsigned")) comparator_25 (
    .a(s2_M), .b({5{1'b0}}), .eq(comparator_25_eq));  // open: gt, lt
  not not_9 (not_9_out, comparator_25_eq);
  Comparator #(.width(5), .mode("unsigned")) comparator_26 (
    .a(s2_M), .b(des_W), .eq(comparator_26_eq));  // open: gt, lt
  Comparator #(.width(4), .mode("unsigned")) comparator_27 (
    .a(tNew_W), .b(4'b0000), .eq(comparator_27_eq));  // open: gt, lt
  and and_9 (and_9_out, not_9_out, comparator_26_eq, comparator_27_eq);
  Multiplexer multiplexer_9 (.in0(1'b0), .in1(1'b1), .out(fRtMsel), .sel(and_9_out));  // open: en
endmodule

module StallUnit (
  input  [4:0] s1_D,
  input  [4:0] s2_D,
  input  [1:0] tUse1_D,
  input  [1:0] tUse2_D,
  input  [4:0] des_E,
  input  [3:0] tNew_E,
  input  [3:0] tNew_M,
  input  [4:0] des_M,
  output Stall_F,
  output Stall_D,
  output flush_E
);

  wire and_1_out, and_2_out, and_3_out, and_4_out, comparator_1_eq, comparator_2_eq, comparator_3_lt,
       comparator_4_eq, comparator_5_eq, comparator_6_lt, comparator_7_eq, comparator_8_eq, comparator_9_lt,
       comparator_10_eq, comparator_11_eq, comparator_12_lt, not_1_out, not_2_out, not_3_out, not_4_out;
  wire [3:0] tUse1_D_t, tUse2_D_t;

  Comparator #(.width(5), .mode("unsigned")) comparator_1 (
    .a(s1_D), .b({5{1'b0}}), .eq(comparator_1_eq));  // open: gt, lt
  Comparator #(.width(5), .mode("unsigned")) comparator_2 (.a(s1_D), .b(des_E), .eq(comparator_2_eq));  // open: gt, lt
  Comparator #(.width(4), .mode("unsigned")) comparator_3 (
    .a(tUse1_D_t), .b(tNew_E), .lt(comparator_3_lt));  // open: gt, eq
  Comparator #(.width(5), .mode("unsigned")) comparator_4 (
    .a(s2_D), .b({5{1'b0}}), .eq(comparator_4_eq));  // open: gt, lt
  Comparator #(.width(5), .mode("unsigned")) comparator_5 (.a(s2_D), .b(des_E), .eq(comparator_5_eq));  // open: gt, lt
  Comparator #(.width(4), .mode("unsigned")) comparator_6 (
    .a(tUse2_D_t), .b(tNew_E), .lt(comparator_6_lt));  // open: gt, eq
  Comparator #(.width(5), .mode("unsigned")) comparator_7 (
    .a(s1_D), .b({5{1'b0}}), .eq(comparator_7_eq));  // open: gt, lt
  Comparator #(.width(5), .mode("unsigned")) comparator_8 (.a(s1_D), .b(des_M), .eq(comparator_8_eq));  // open: gt, lt
  Comparator #(.width(4), .mode("unsigned")) comparator_9 (
    .a(tUse1_D_t), .b(tNew_M), .lt(comparator_9_lt));  // open: gt, eq
  Comparator #(.width(5), .mode("unsigned")) comparator_10 (
    .a(s2_D), .b({5{1'b0}}), .eq(comparator_10_eq));  // open: gt, lt
  Comparator #(.width(5), .mode("unsigned")) comparator_11 (
    .a(s2_D), .b(des_M), .eq(comparator_11_eq));  // open: gt, lt
  Comparator #(.width(4), .mode("unsigned")) comparator_12 (
    .a(tUse2_D_t), .b(tNew_M), .lt(comparator_12_lt));  // open: gt, eq
  assign tUse1_D_t = {{2{1'b0}}, tUse1_D};  // Bit_Extender bit_extender_1
  not not_1 (not_1_out, comparator_1_eq);
  not not_2 (not_2_out, comparator_4_eq);
  not not_3 (not_3_out, comparator_7_eq);
  not not_4 (not_4_out, comparator_10_eq);
  and and_1 (and_1_out, not_1_out, comparator_2_eq, comparator_3_lt);
  and and_2 (and_2_out, not_2_out, comparator_5_eq, comparator_6_lt);
  and and_3 (and_3_out, not_3_out, comparator_8_eq, comparator_9_lt);
  and and_4 (and_4_out, not_4_out, comparator_11_eq, comparator_12_lt);
  assign tUse2_D_t = {{2{1'b0}}, tUse2_D};  // Bit_Extender bit_extender_2
  or or_1 (flush_E, and_1_out, and_2_out, and_3_out, and_4_out);

  assign Stall_D = flush_E;
  assign Stall_F = flush_E;

  // Other names for the same wires on the sheet: stall_flag = flush_E
endmodule

module ID (
  input  [31:0] in_1,
  output [4:0] S1_D,
  output [4:0] S2_D,
  output [1:0] tuse1_D,
  output [1:0] tuse2_D
);

  wire addu, beq, j, jal, jr, lb, lh, lui, lw, nop, or_1_out, or_2_out, or_3_out, or_4_out, or_5_out,
       or_6_out, or_7_out, ori, S1_D_out, S2_D_out, sb, sh, subu, sw, tuse1_D_out, tuse2_D_out;
  wire [1:0] bit_extender_1_out;
  wire [4:0] splitter_1_out_5, splitter_1_out_6;
  wire [5:0] func, Op;

  splitter splitter_1 (
    .in_1(in_1), .out_2(func), .out_5(splitter_1_out_5), .out_6(splitter_1_out_6), .out_7(Op));  // open: out_3, out_4, out_8, out_9
  or or_1 (or_1_out, addu, subu);
  or or_2 (or_2_out, lw, sw);
  buf or_3 (or_3_out, ori);  // OR_Gate
  or u_tuse1_D (tuse1_D_out, or_1_out, or_2_out, or_3_out);
  or u_tuse2_D (tuse2_D_out, addu, subu);
  UseFunc UseFunc (
    .Op(Op), .func(func), .out_3(lw), .out_4(sw), .out_5(addu), .out_6(subu), .out_7(ori), .out_8(lui),
    .out_9(j), .out_10(jal), .out_11(jr), .out_12(beq), .out_13(nop), .out_14(lh), .out_15(sh), .out_16(lb),
    .out_17(sb));
  assign bit_extender_1_out = {{1{1'b0}}, tuse2_D_out};  // Bit_Extender bit_extender_1
  Multiplexer #(.width(2), .enable("false")) multiplexer_1 (.in0(2'b00), .in1(2'b01), .out(tuse1_D), .sel(tuse1_D_out));
  Multiplexer #(.width(2), .enable("false")) multiplexer_2 (
    .in0(bit_extender_1_out), .in1(2'b10), .out(tuse2_D), .sel(sw));
  or u_S2_D (S2_D_out, addu, subu, sw, beq);
  or or_4 (or_4_out, addu, subu);
  or or_5 (or_5_out, lw, sw);
  buf or_6 (or_6_out, ori);  // OR_Gate
  buf or_7 (or_7_out, beq);  // OR_Gate
  Multiplexer #(.width(5), .enable("false")) multiplexer_3 (
    .in0({5{1'b0}}), .in1(splitter_1_out_6), .out(S1_D), .sel(S1_D_out));
  Multiplexer #(.width(5), .enable("false")) multiplexer_4 (
    .in0({5{1'b0}}), .in1(splitter_1_out_5), .out(S2_D), .sel(S2_D_out));
  or u_S1_D (S1_D_out, or_4_out, or_5_out, jr, or_6_out, or_7_out);
endmodule

module EX (
  input  [31:0] in_1,
  input  [31:0] EXTresult,
  input  [31:0] pc_8,
  output [4:0] S1_E,
  output [4:0] S2_E,
  output [3:0] Tnew_E,
  output [4:0] des_E,
  output [31:0] EtoD
);

  wire addu, beq, j, jal, jr, lb, lh, lui, lw, nop, or_3_out, or_4_out, or_5_out, or_6_out, or_7_out,
       or_8_out, or_9_out, or_10_out, or_11_out, or_14_out, or_15_out, or_16_out, ori, S1_E_out, S2_E_out,
       sb, sh, subu, sw;
  wire [1:0] multiplexer_2_out, multiplexer_3_out, multiplexer_4_out, multiplexer_5_out, multiplexer_6_out,
       or_1_out, or_12_out, or_13_out;
  wire [4:0] rd, rt, splitter_1_out_6;
  wire [5:0] func, Op;

  splitter splitter_1 (
    .in_1(in_1), .out_2(func), .out_4(rd), .out_5(rt), .out_6(splitter_1_out_6), .out_7(Op));  // open: out_3, out_8, out_9
  buf or_1 (or_1_out[0], lui);  // OR_Gate
  buf or_2 (or_1_out[1], jal);  // OR_Gate
  Multiplexer #(.select(2), .width(32), .enable("false")) multiplexer_1 (
    .in0({32{1'b0}}), .in1(EXTresult), .in2(pc_8), .out(EtoD), .sel(or_1_out));  // open: in3
  or or_3 (or_3_out, addu, subu);
  buf or_4 (or_4_out, ori);  // OR_Gate
  or or_5 (or_5_out, lui, ori, lw);
  or or_6 (or_6_out, addu, subu);
  buf or_7 (or_7_out, jal);  // OR_Gate
  UseFunc UseFunc (
    .Op(Op), .func(func), .out_3(lw), .out_4(sw), .out_5(addu), .out_6(subu), .out_7(ori), .out_8(lui),
    .out_9(j), .out_10(jal), .out_11(jr), .out_12(beq), .out_13(nop), .out_14(lh), .out_15(sh), .out_16(lb),
    .out_17(sb));
  or or_8 (or_8_out, or_3_out, or_4_out);
  buf or_9 (or_9_out, lw);  // OR_Gate
  Multiplexer #(.width(2), .enable("false")) multiplexer_2 (
    .in0(2'b00), .in1(2'b01), .out(multiplexer_2_out), .sel(or_5_out));
  Multiplexer #(.width(2), .enable("false")) multiplexer_3 (
    .in0(2'b00), .in1(2'b10), .out(multiplexer_3_out), .sel(or_6_out));
  Multiplexer #(.width(2), .enable("false")) multiplexer_4 (
    .in0(2'b00), .in1(2'b11), .out(multiplexer_4_out), .sel(or_7_out));
  or or_10 (or_10_out, addu, subu);
  buf or_11 (or_11_out, sw);  // OR_Gate
  or u_S2_E (S2_E_out, or_10_out, or_11_out);
  Multiplexer #(.width(2), .enable("false")) multiplexer_5 (
    .in0(2'b00), .in1(2'b01), .out(multiplexer_5_out), .sel(or_8_out));
  Multiplexer #(.width(2), .enable("false")) multiplexer_6 (
    .in0(2'b00), .in1(2'b10), .out(multiplexer_6_out), .sel(or_9_out));
  assign or_12_out = multiplexer_2_out | multiplexer_3_out | multiplexer_4_out;  // OR_Gate or_12, 2 bits wide
  Multiplexer #(.width(5), .enable("false")) multiplexer_7 (
    .in0({5{1'b0}}), .in1(splitter_1_out_6), .out(S1_E), .sel(S1_E_out));
  Multiplexer #(.width(5), .enable("false")) multiplexer_8 (.in0({5{1'b0}}), .in1(rt), .out(S2_E), .sel(S2_E_out));
  assign or_13_out = multiplexer_5_out | multiplexer_6_out;  // OR_Gate or_13, 2 bits wide
  Multiplexer #(.select(2), .width(5), .enable("false")) multiplexer_9 (
    .in0({5{1'b0}}), .in1(rt), .in2(rd), .in3({5{1'b1}}), .out(des_E), .sel(or_12_out));
  or or_14 (or_14_out, addu, subu);
  or or_15 (or_15_out, lw, sw);
  buf or_16 (or_16_out, ori);  // OR_Gate
  assign Tnew_E = {{2{1'b0}}, or_13_out};  // Bit_Extender bit_extender_1
  or u_S1_E (S1_E_out, or_14_out, or_15_out, or_16_out);
endmodule

module MEM (
  input  [31:0] in_1,
  input  [31:0] ALUresult,
  input  [31:0] pc_8,
  output [4:0] S2_M,
  output [4:0] des_M,
  output [31:0] MtoD
);

  wire addu, beq, j, jal, jr, lb, lh, lui, lw, nop, or_1_out, or_2_out, or_3_out, or_4_out, or_5_out, ori,
       S2_E_out, sb, sh, subu, sw;
  wire [1:0] multiplexer_1_out, multiplexer_2_out, multiplexer_3_out, or_6_out, or_8_out;
  wire [4:0] rd, rt;
  wire [5:0] func, Op;

  splitter splitter_1 (
    .in_1(in_1), .out_2(func), .out_4(rd), .out_5(rt), .out_7(Op));  // open: out_3, out_6, out_8, out_9
  or or_1 (or_1_out, lui, ori, lw);
  or or_2 (or_2_out, addu, subu);
  buf or_3 (or_3_out, jal);  // OR_Gate
  or or_4 (or_4_out, addu, subu);
  Multiplexer #(.width(2), .enable("false")) multiplexer_1 (
    .in0(2'b00), .in1(2'b01), .out(multiplexer_1_out), .sel(or_1_out));
  Multiplexer #(.width(2), .enable("false")) multiplexer_2 (
    .in0(2'b00), .in1(2'b10), .out(multiplexer_2_out), .sel(or_2_out));
  Multiplexer #(.width(2), .enable("false")) multiplexer_3 (
    .in0(2'b00), .in1(2'b11), .out(multiplexer_3_out), .sel(or_3_out));
  UseFunc UseFunc (
    .Op(Op), .func(func), .out_3(lw), .out_4(sw), .out_5(addu), .out_6(subu), .out_7(ori), .out_8(lui),
    .out_9(j), .out_10(jal), .out_11(jr), .out_12(beq), .out_13(nop), .out_14(lh), .out_15(sh), .out_16(lb),
    .out_17(sb));
  buf or_5 (or_5_out, sw);  // OR_Gate
  Multiplexer #(.select(2), .width(32), .enable("false")) multiplexer_4 (
    .in0({32{1'b0}}), .in1(ALUresult), .in2(pc_8), .out(MtoD), .sel(or_6_out));  // open: in3
  or or_6 (or_6_out[0], lui, ori, or_4_out);
  buf or_7 (or_6_out[1], jal);  // OR_Gate
  assign or_8_out = multiplexer_1_out | multiplexer_2_out | multiplexer_3_out;  // OR_Gate or_8, 2 bits wide
  Multiplexer #(.width(5), .enable("false")) multiplexer_5 (.in0({5{1'b0}}), .in1(rt), .out(S2_M), .sel(S2_E_out));
  buf S2_E (S2_E_out, or_5_out);  // OR_Gate
  Multiplexer #(.select(2), .width(5), .enable("false")) multiplexer_6 (
    .in0({5{1'b0}}), .in1(rt), .in2(rd), .in3({5{1'b1}}), .out(des_M), .sel(or_8_out));
endmodule

module WB (
  input  [31:0] in_1,
  input  [31:0] ALUresult,
  input  [31:0] pc_8,
  input  [31:0] RegData,
  output [4:0] des_W,
  output [31:0] WtoD
);

  wire addu, beq, j, jal, jr, lb, lh, lui, lw, nop, or_1_out, or_2_out, or_3_out, or_4_out, or_5_out, ori,
       sb, sh, subu, sw;
  wire [1:0] multiplexer_1_out, multiplexer_2_out, multiplexer_3_out, or_6_out, or_8_out;
  wire [4:0] rd, rt;
  wire [5:0] func, Op;

  or or_1 (or_1_out, lui, ori, lw);
  or or_2 (or_2_out, addu, subu);
  buf or_3 (or_3_out, jal);  // OR_Gate
  or or_4 (or_4_out, lui, ori);
  or or_5 (or_5_out, addu, subu);
  Multiplexer #(.width(2), .enable("false")) multiplexer_1 (
    .in0(2'b00), .in1(2'b01), .out(multiplexer_1_out), .sel(or_1_out));
  Multiplexer #(.width(2), .enable("false")) multiplexer_2 (
    .in0(2'b00), .in1(2'b10), .out(multiplexer_2_out), .sel(or_2_out));
  Multiplexer #(.width(2), .enable("false")) multiplexer_3 (
    .in0(2'b00), .in1(2'b11), .out(multiplexer_3_out), .sel(or_3_out));
  or or_6 (or_6_out[0], or_4_out, lw, or_5_out);
  or or_7 (or_6_out[1], jal, lw);
  UseFunc UseFunc (
    .Op(Op), .func(func), .out_3(lw), .out_4(sw), .out_5(addu), .out_6(subu), .out_7(ori), .out_8(lui),
    .out_9(j), .out_10(jal), .out_11(jr), .out_12(beq), .out_13(nop), .out_14(lh), .out_15(sh), .out_16(lb),
    .out_17(sb));
  Multiplexer #(.select(2), .width(32), .enable("false")) multiplexer_4 (
    .in0({32{1'b0}}), .in1(ALUresult), .in2(pc_8), .in3(RegData), .out(WtoD), .sel(or_6_out));
  splitter splitter_1 (
    .in_1(in_1), .out_2(func), .out_4(rd), .out_5(rt), .out_7(Op));  // open: out_3, out_6, out_8, out_9
  assign or_8_out = multiplexer_1_out | multiplexer_2_out | multiplexer_3_out;  // OR_Gate or_8, 2 bits wide
  Multiplexer #(.select(2), .width(5), .enable("false")) multiplexer_5 (
    .in0({5{1'b0}}), .in1(rt), .in2(rd), .in3({5{1'b1}}), .out(des_W), .sel(or_8_out));
endmodule
