// Logisim project stallUnit.circ as structural Verilog: 1 circuit, main circuit StallUnit
module StallUnit (
  input  [4:0] s1_D,
  input  [4:0] s2_D,
  input  [1:0] tUse1_D,
  input  [1:0] tUse2_D,
  input  [4:0] des_E,
  input  [3:0] tNew_E,
  input  [3:0] tNew_M,
  input  [4:0] des_M,
  output Stall_F,
  output Stall_D,
  output flush_E
);

  wire and_1_out, and_2_out, and_3_out, and_4_out, comparator_1_eq, comparator_2_eq, comparator_3_lt,
       comparator_4_eq, comparator_5_eq, comparator_6_lt, comparator_7_eq, comparator_8_eq, comparator_9_lt,
       comparator_10_eq, comparator_11_eq, comparator_12_lt, not_1_out, not_2_out, not_3_out, not_4_out;
  wire [3:0] tUse1_D_t, tUse2_D_t;

  Comparator #(.width(5), .mode("unsigned")) comparator_1 (
    .a(s1_D), .b({5{1'b0}}), .eq(comparator_1_eq));  // open: gt, lt
  Comparator #(.width(5), .mode("unsigned")) comparator_2 (.a(s1_D), .b(des_E), .eq(comparator_2_eq));  // open: gt, lt
  Comparator #(.width(4), .mode("unsigned")) comparator_3 (
    .a(tUse1_D_t), .b(tNew_E), .lt(comparator_3_lt));  // open: gt, eq
  Comparator #(.width(5), .mode("unsigned")) comparator_4 (
    .a(s2_D), .b({5{1'b0}}), .eq(comparator_4_eq));  // open: gt, lt
  Comparator #(.width(5), .mode("unsigned")) comparator_5 (.a(s2_D), .b(des_E), .eq(comparator_5_eq));  // open: gt, lt
  Comparator #(.width(4), .mode("unsigned")) comparator_6 (
    .a(tUse2_D_t), .b(tNew_E), .lt(comparator_6_lt));  // open: gt, eq
  Comparator #(.width(5), .mode("unsigned")) comparator_7 (
    .a(s1_D), .b({5{1'b0}}), .eq(comparator_7_eq));  // open: gt, lt
  Comparator #(.width(5), .mode("unsigned")) comparator_8 (.a(s1_D), .b(des_M), .eq(comparator_8_eq));  // open: gt, lt
  Comparator #(.width(4), .mode("unsigned")) comparator_9 (
    .a(tUse1_D_t), .b(tNew_M), .lt(comparator_9_lt));  // open: gt, eq
  Comparator #(.width(5), .mode("unsigned")) comparator_10 (
    .a(s2_D), .b({5{1'b0}}), .eq(comparator_10_eq));  // open: gt, lt
  Comparator #(.width(5), .mode("unsigned")) comparator_11 (
    .a(s2_D), .b(des_M), .eq(comparator_11_eq));  // open: gt, lt
  Comparator #(.width(4), .mode("unsigned")) comparator_12 (
    .a(tUse2_D_t), .b(tNew_M), .lt(comparator_12_lt));  // open: gt, eq
  assign tUse1_D_t = {{2{1'b0}}, tUse1_D};  // Bit_Extender bit_extender_1
  not not_1 (not_1_out, comparator_1_eq);
  not not_2 (not_2_out, comparator_4_eq);
  not not_3 (not_3_out, comparator_7_eq);
  not not_4 (not_4_out, comparator_10_eq);
  and and_1 (and_1_out, not_1_out, comparator_2_eq, comparator_3_lt);
  and and_2 (and_2_out, not_2_out, comparator_5_eq, comparator_6_lt);
  and and_3 (and_3_out, not_3_out, comparator_8_eq, comparator_9_lt);
  and and_4 (and_4_out, not_4_out, comparator_11_eq, comparator_12_lt);
  assign tUse2_D_t = {{2{1'b0}}, tUse2_D};  // Bit_Extender bit_extender_2
  or or_1 (flush_E, and_1_out, and_2_out, and_3_out, and_4_out);

  assign Stall_D = flush_E;
  assign Stall_F = flush_E;

  // Other names for the same wires on the sheet: stall_flag = flush_E
endmodule
