// Logisim project cpu -cache -流水线寄存器M-W.circ as structural Verilog: 1 circuit, main circuit M_W_reg
module M_W_reg (
  input  in_1,
  input  in_2,
  input  [4:0] writereg_i,
  input  [31:0] aluresult_i,
  input  [31:0] writedata_i,
  input  [31:0] readdata_i,
  input  [31:0] pc_i,
  input  [31:0] pc_4_i,
  input  [31:0] pc_8_i,
  input  [31:0] instr_i,
  input  [31:0] memaddr,
  input  [31:0] memdata,
  input  memwrite,
  output [4:0] out_14,
  output [31:0] out_15,
  output [31:0] out_16,
  output [31:0] out_17,
  output [31:0] pc_o,
  output [31:0] pc_4_o,
  output [31:0] pc_8_o,
  output [31:0] out_21,
  output [31:0] out_22,
  output [31:0] out_23,
  output out_24
);

  Register #(.width(5)) register_1 (.D(writereg_i), .Q(out_14), .clk(in_1), .clr(in_2));  // open: en
  Register #(.width(32)) register_2 (.D(aluresult_i), .Q(out_15), .clk(in_1), .clr(in_2));  // open: en
  Register #(.width(32)) register_3 (.D(writedata_i), .Q(out_16), .clk(in_1), .clr(in_2));  // open: en
  Register #(.width(32)) register_4 (.D(readdata_i), .Q(out_17), .clk(in_1), .clr(in_2));  // open: en
  Register #(.width(32)) register_5 (.D(pc_i), .Q(pc_o), .clk(in_1), .clr(in_2));  // open: en
  Register #(.width(32)) register_6 (.D(pc_4_i), .Q(pc_4_o), .clk(in_1), .clr(in_2));  // open: en
  Register #(.width(32)) register_7 (.D(pc_8_i), .Q(pc_8_o), .clk(in_1), .clr(in_2));  // open: en
  Register #(.width(32)) register_8 (.D(instr_i), .Q(out_21), .clk(in_1), .clr(in_2));  // open: en
  Register #(.width(32)) register_9 (.D(memaddr), .Q(out_22), .clk(in_1), .clr(in_2));  // open: en
  Register #(.width(32)) register_10 (.D(memdata), .Q(out_23), .clk(in_1), .clr(in_2));  // open: en
  Register #(.width(1)) register_11 (.D(memwrite), .Q(out_24), .clk(in_1), .clr(in_2));  // open: en

  // Other names for the same wires on the sheet: clk = in_1; clk_prime = in_1; Reset = in_2
endmodule
