// Logisim project Cache_1.circ as structural Verilog
module Cache (
  input  [31:0] Address,
  input  [31:0] Data,
  input  in_3,
  input  in_4,
  input  in_5,
  input  in_6,
  output [15:0] out_7,
  output [15:0] out_8,
  output out_9,
  output [31:0] D
);

  wire and_1_out, and_3_out, B1, B2, B3, B4, decoder_2_out0, decoder_2_out1, decoder_2_out2, decoder_2_out3,
       en1, en2, en3, en4, Hit, Hit1, Hit2, Hit3, Hit4, or_1_out, or_3_out;
  wire [1:0] multiplexer_1_out, multiplexer_2_out;
  wire [31:0] _1d1, _1d2, _1d3, _1d4, _2d1, _2d2, _2d3, _2d4, _3d1, _3d2, _3d3, _3d4, _4d1, _4d2, _4d3, _4d4,
       D1, D2, D3, D4, multiplexer_4_out, multiplexer_5_out, multiplexer_6_out, multiplexer_7_out,
       multiplexer_8_out, multiplexer_9_out, multiplexer_10_out;

  Clock clock_1 ();  // open: out
  RAM ram_1 (
    .MuxBlock(Address[3:2]), .MemWrite(in_4), .MemRead(in_3), .Hit(Hit), .Tag(Address[11:6]),
    .MuxGroup(Address[5:4]), .MemData(Data), .Clk(in_6), .Reset(in_5), ._4(D4), ._3(D3), ._2(D2),
    .out_13(out_9), ._1(D1));
  Decoder #(.select(2), .enable("false")) decoder_1 (.out0(B1), .out1(B2), .out2(B3), .out3(B4), .sel(Address[3:2]));
  Decoder #(.select(2), .enable("false")) decoder_2 (
    .out0(decoder_2_out0), .out1(decoder_2_out1), .out2(decoder_2_out2), .out3(decoder_2_out3),
    .sel(Address[5:4]));
  or or_1 (or_1_out, in_3, in_4);
  and and_1 (and_1_out, in_3, ~out_9);  // AND_Gate
  and and_2 (en4, decoder_2_out3, or_1_out);
  Counter_part #(.width(16), .max('hffff)) counter_1 (
    .count(and_1_out), .Q(out_7), .clk(in_6), .clr(in_5));  // open: load, D, carry
  Counter_part #(.width(16), .max('hffff)) counter_2 (
    .count(and_3_out), .Q(out_8), .clk(in_6), .clr(in_5));  // open: load, D, carry
  and and_3 (and_3_out, in_3, Hit, ~out_9);  // AND_Gate
  and and_4 (en2, decoder_2_out1, or_1_out);
  and and_5 (en3, decoder_2_out2, or_1_out);
  and and_6 (en1, decoder_2_out0, or_1_out);
  or or_2 (Hit, Hit1, Hit2, Hit3, Hit4);
  Group group_1 (
    .Data1(D1), .Data2(D2), .Data3(D3), .Data4(D4), .tag(Address[11:6]), .clk(in_6), .reset(in_5),
    .enable(en1), .stop(out_9), .MemRead(in_3), .MemWrite(in_4), .Hit(Hit1), .out_13(_1d1), .out_14(_1d2),
    .out_15(_1d3), .out_16(_1d4));
  Group group_2 (
    .Data1(D1), .Data2(D2), .Data3(D3), .Data4(D4), .tag(Address[11:6]), .clk(in_6), .reset(in_5),
    .enable(en2), .stop(out_9), .MemRead(in_3), .MemWrite(in_4), .Hit(Hit2), .out_13(_2d1), .out_14(_2d2),
    .out_15(_2d3), .out_16(_2d4));
  Group group_3 (
    .Data1(D1), .Data2(D2), .Data3(D3), .Data4(D4), .tag(Address[11:6]), .clk(in_6), .reset(in_5),
    .enable(en3), .stop(out_9), .MemRead(in_3), .MemWrite(in_4), .Hit(Hit3), .out_13(_3d1), .out_14(_3d2),
    .out_15(_3d3), .out_16(_3d4));
  Group group_4 (
    .Data1(D1), .Data2(D2), .Data3(D3), .Data4(D4), .tag(Address[11:6]), .clk(in_6), .reset(in_5),
    .enable(en4), .stop(out_9), .MemRead(in_3), .MemWrite(in_4), .Hit(Hit4), .out_13(_4d1), .out_14(_4d2),
    .out_15(_4d3), .out_16(_4d4));
  Multiplexer #(.width(2), .enable("false")) multiplexer_1 (
    .in0(2'b00), .in1(2'b01), .out(multiplexer_1_out), .sel(en2));
  Multiplexer #(.width(2), .enable("false")) multiplexer_2 (
    .in0(multiplexer_1_out), .in1(2'b10), .out(multiplexer_2_out), .sel(en3));
  Multiplexer #(.width(2), .enable("false")) multiplexer_3 (
    .in0(multiplexer_2_out), .in1(2'b11), .sel(en4));  // open: out
  Multiplexer #(.select(2), .width(32)) multiplexer_4 (
    .in0(_1d1), .in1(_2d1), .in2(_3d1), .in3(_4d1), .out(multiplexer_4_out), .sel(Address[5:4]));  // open: en
  Multiplexer #(.select(2), .width(32)) multiplexer_5 (
    .in0(_1d2), .in1(_2d2), .in2(_3d2), .in3(_4d2), .out(multiplexer_5_out), .sel(Address[5:4]));  // open: en
  Multiplexer #(.select(2), .width(32)) multiplexer_6 (
    .in0(_1d3), .in1(_2d3), .in2(_3d3), .in3(_4d3), .out(multiplexer_6_out), .sel(Address[5:4]));  // open: en
  Multiplexer #(.select(2), .width(32)) multiplexer_7 (
    .in0(_1d4), .in1(_2d4), .in2(_3d4), .in3(_4d4), .out(multiplexer_7_out), .sel(Address[5:4]));  // open: en
  Multiplexer #(.select(2), .width(32)) multiplexer_8 (
    .in0(multiplexer_4_out), .in1(multiplexer_5_out), .in2(multiplexer_6_out), .in3(multiplexer_7_out),
    .out(multiplexer_8_out), .sel(Address[3:2]));  // open: en
  Multiplexer #(.select(2), .width(32)) multiplexer_9 (
    .in0(D1), .in1(D2), .in2(D3), .in3(D4), .out(multiplexer_9_out), .sel(Address[3:2]));  // open: en
  Multiplexer #(.width(32)) multiplexer_10 (
    .in0(multiplexer_9_out), .in1(multiplexer_8_out), .out(multiplexer_10_out), .sel(Hit));  // open: en
  Multiplexer #(.width(32)) multiplexer_11 (
    .in0(multiplexer_10_out), .in1({32{1'b0}}), .out(D), .sel(or_3_out));  // open: en
  or or_3 (or_3_out, in_4, out_9);

  // Other names for the same wires on the sheet: MuxBlock[1:0] = Address[3:2]; MuxGroup[1:0] = Address[5:4];
  //   Tag[5:0] = Address[11:6]; clk = in_6; HitTimes[15:0] = out_8; MemRead = in_3; MemWrite = in_4;
  //   ReadTimes[15:0] = out_7; reset = in_5; stop = out_9
endmodule

module RAM (
  input  [1:0] MuxBlock,
  input  MemWrite,
  input  MemRead,
  input  Hit,
  input  [5:0] Tag,
  input  [1:0] MuxGroup,
  input  [31:0] MemData,
  input  Clk,
  input  Reset,
  output [31:0] _4,
  output [31:0] _3,
  output [31:0] _2,
  output out_13,
  output [31:0] _1
);

  wire _1_t, _2_t, _3_t, _4_t, and_1_out, and_2_out, counter_1_carry, not_1_out, not_2_out;
  wire [9:0] adder_1_out, adder_2_out, adder_3_out, adder_4_out, multiplexer_1_out;
  wire [31:0] ram_1_data, ram_2_data, ram_3_data, ram_4_data;

  and and_1 (and_1_out, MemRead, not_1_out);
  not not_1 (not_1_out, Hit);
  Counter_part #(.width(3), .max('h5)) counter_1 (
    .count(and_1_out), .carry(counter_1_carry), .clk(Clk), .clr(Reset));  // open: load, D, Q
  and and_2 (and_2_out, MemRead, Hit);
  and and_3 (out_13, and_1_out, not_2_out);
  not not_2 (not_2_out, counter_1_carry);
  Demultiplexer #(.select(2)) demultiplexer_1 (
    .out0(_1_t), .out1(_2_t), .out2(_3_t), .out3(_4_t), .in(MemWrite), .sel(MuxBlock));  // open: en
  Multiplexer #(.width(10), .enable("false")) multiplexer_1 (
    .in0({Tag, MuxGroup, 2'b00}), .in1({10{1'b0}}), .out(multiplexer_1_out), .sel(and_2_out));
  Adder #(.width(10)) adder_1 (.a(10'h3), .b(multiplexer_1_out), .out(adder_1_out));  // open: cin, cout
  Adder #(.width(10)) adder_2 (.a(10'h2), .b(multiplexer_1_out), .out(adder_2_out));  // open: cin, cout
  Adder #(.width(10)) adder_3 (.a(10'h1), .b(multiplexer_1_out), .out(adder_3_out));  // open: cin, cout
  Adder #(.width(10)) adder_4 (.a({10{1'b0}}), .b(multiplexer_1_out), .out(adder_4_out));  // open: cin, cout
  RAM_part #(.addrWidth(10), .dataWidth(32), .bus("separate")) ram_1 (
    .addr(adder_1_out), .din(MemData), .data(ram_1_data), .str(_4_t), .clk(Clk), .clr(Reset));  // open: sel, ld
  RAM_part #(.addrWidth(10), .dataWidth(32), .bus("separate")) ram_2 (
    .addr(adder_2_out), .din(MemData), .data(ram_2_data), .str(_3_t), .clk(Clk), .clr(Reset));  // open: sel, ld
  RAM_part #(.addrWidth(10), .dataWidth(32), .bus("separate")) ram_3 (
    .addr(adder_3_out), .din(MemData), .data(ram_3_data), .str(_2_t), .clk(Clk), .clr(Reset));  // open: sel, ld
  RAM_part #(.addrWidth(10), .dataWidth(32), .bus("separate")) ram_4 (
    .addr(adder_4_out), .din(MemData), .data(ram_4_data), .str(_1_t), .clk(Clk), .clr(Reset));  // open: sel, ld
  Multiplexer #(.width(32), .enable("false")) multiplexer_2 (.in0(ram_1_data), .in1(MemData), .out(_4), .sel(_4_t));
  Multiplexer #(.width(32), .enable("false")) multiplexer_3 (.in0(ram_2_data), .in1(MemData), .out(_3), .sel(_3_t));
  Multiplexer #(.width(32), .enable("false")) multiplexer_4 (.in0(ram_3_data), .in1(MemData), .out(_2), .sel(_2_t));
  Multiplexer #(.width(32), .enable("false")) multiplexer_5 (.in0(ram_4_data), .in1(MemData), .out(_1), .sel(_1_t));

  // Other names for the same wires on the sheet: Data[31:0] = MemData
endmodule

module CacheBlock (
  input  reset,
  input  [5:0] tag,
  input  clk,
  input  enable,
  input  [31:0] in_5,
  input  [31:0] in_6,
  input  [31:0] in_7,
  input  [31:0] in_8,
  output out_9,
  output [5:0] out_10,
  output [31:0] out_11,
  output [31:0] out_12,
  output [31:0] out_13,
  output [31:0] out_14
);

  Register #(.width(1)) register_1 (.D(1'b1), .en(enable), .Q(out_9), .clk(clk), .clr(reset));
  Register #(.width(32)) register_2 (.D(in_5), .en(enable), .Q(out_11), .clk(clk), .clr(reset));
  Register #(.width(32)) register_3 (.D(in_6), .en(enable), .Q(out_12), .clk(clk), .clr(reset));
  Register #(.width(32)) register_4 (.D(in_7), .en(enable), .Q(out_13), .clk(clk), .clr(reset));
  Register #(.width(32)) register_5 (.D(in_8), .en(enable), .Q(out_14), .clk(clk), .clr(reset));
  Register #(.width(6)) register_6 (.D(tag), .en(enable), .Q(out_10), .clk(clk), .clr(reset));

  // Other names for the same wires on the sheet: data1[31:0] = out_11; data2[31:0] = out_12; data3[31:0] = out_13;
  //   data4[31:0] = out_14; en = enable; tag_t[5:0] = out_10; V = out_9
endmodule

module LRU (
  input  [15:0] count1,
  input  [15:0] count2,
  input  [15:0] count3,
  input  [15:0] count4,
  input  hit1,
  input  hit2,
  input  hit3,
  input  hit4,
  input  MemRead,
  input  MemWrite,
  input  Enable,
  output Write1,
  output Write1_2,
  output Write3,
  output Write4
);

  wire and_2_out, and_3_out, and_4_out, and_5_out, comparator_1_lt, comparator_2_lt, comparator_3_lt,
       decoder_1_out0, decoder_1_out1, decoder_1_out2, decoder_1_out3, multiplexer_6_out, multiplexer_7_out,
       multiplexer_8_out, multiplexer_9_out, NhNw, nor_1_out, not_1_out, or_1_out, or_2_out, or_3_out,
       or_4_out;
  wire [1:0] cmp, cmp1, cmp2;
  wire [15:0] multiplexer_3_out, multiplexer_4_out;

  Comparator #(.width(16)) comparator_1 (.a(count1), .b(count2), .lt(comparator_1_lt));  // open: gt, eq
  Comparator #(.width(16)) comparator_2 (.a(count3), .b(count4), .lt(comparator_2_lt));  // open: gt, eq
  Multiplexer #(.width(2), .enable("false")) multiplexer_1 (
    .in0(2'b00), .in1(2'b01), .out(cmp1), .sel(comparator_1_lt));
  Multiplexer #(.width(2), .enable("false")) multiplexer_2 (
    .in0(2'b10), .in1(2'b11), .out(cmp2), .sel(comparator_2_lt));
  nor nor_1 (nor_1_out, hit1, hit2, hit3, hit4);
  not not_1 (not_1_out, MemWrite);
  and and_1 (NhNw, nor_1_out, not_1_out);
  and and_2 (and_2_out, hit1, MemWrite);
  and and_3 (and_3_out, hit2, MemWrite);
  and and_4 (and_4_out, hit3, MemWrite);
  and and_5 (and_5_out, hit4, MemWrite);
  Multiplexer #(.select(2), .width(16), .enable("false")) multiplexer_3 (
    .in0(count1), .in1(count2), .in2({16{1'b0}}), .in3({16{1'b0}}), .out(multiplexer_3_out), .sel(cmp1));
  Multiplexer #(.select(2), .width(16), .enable("false")) multiplexer_4 (
    .in0({16{1'b0}}), .in1({16{1'b0}}), .in2(count3), .in3(count4), .out(multiplexer_4_out), .sel(cmp2));
  Decoder #(.select(2)) decoder_1 (
    .out0(decoder_1_out0), .out1(decoder_1_out1), .out2(decoder_1_out2), .out3(decoder_1_out3), .sel(cmp));  // open: en
  Comparator #(.width(16)) comparator_3 (
    .a(multiplexer_3_out), .b(multiplexer_4_out), .lt(comparator_3_lt));  // open: gt, eq
  Multiplexer #(.width(2), .enable("false")) multiplexer_5 (.in0(cmp1), .in1(cmp2), .out(cmp), .sel(comparator_3_lt));
  Multiplexer #(.enable("false")) multiplexer_6 (.in0(1'b0), .in1(decoder_1_out0), .out(multiplexer_6_out), .sel(NhNw));
  Multiplexer #(.enable("false")) multiplexer_7 (.in0(1'b0), .in1(decoder_1_out1), .out(multiplexer_7_out), .sel(NhNw));
  Multiplexer #(.enable("false")) multiplexer_8 (.in0(1'b0), .in1(decoder_1_out2), .out(multiplexer_8_out), .sel(NhNw));
  Multiplexer #(.enable("false")) multiplexer_9 (.in0(1'b0), .in1(decoder_1_out3), .out(multiplexer_9_out), .sel(NhNw));
  or or_1 (or_1_out, multiplexer_6_out, 1'b0, and_2_out);
  or or_2 (or_2_out, multiplexer_7_out, 1'b0, and_3_out);
  or or_3 (or_3_out, multiplexer_8_out, 1'b0, and_4_out);
  or or_4 (or_4_out, multiplexer_9_out, 1'b0, and_5_out);
  and and_6 (Write1, Enable, or_1_out);
  and and_7 (Write1_2, Enable, or_2_out);
  and and_8 (Write3, Enable, or_3_out);
  and and_9 (Write4, Enable, or_4_out);

  // Other names for the same wires on the sheet: cnt1[15:0] = count1; cnt2[15:0] = count2; cnt3[15:0] = count3;
  //   cnt4[15:0] = count4; en = Enable

  // Notes on the sheet:
  //   决定Cacheblock是否更新
endmodule

module Counter (
  input  clk,
  input  reset,
  input  MemRead,
  input  hit,
  input  B_Enable,
  input  G_Enable,
  output [15:0] out_7
);

  wire add, and_2_out, and_3_out, clear, count, load, not_1_out, not_2_out, or_1_out, or_2_out;

  buf or_1 (or_1_out, clear);  // OR_Gate
  buf or_2 (or_2_out, add);  // OR_Gate
  Multiplexer #(.enable("false")) multiplexer_1 (.in0(1'b0), .in1(1'b1), .out(load), .sel(or_1_out));
  Multiplexer #(.enable("false")) multiplexer_2 (.in0(1'b0), .in1(1'b1), .out(count), .sel(or_2_out));
  and and_1 (add, G_Enable, not_1_out, MemRead);
  not not_1 (not_1_out, clear);
  Counter_part #(.width(16), .max('hffff)) counter_1 (
    .load(load), .D({16{1'b0}}), .count(count), .Q(out_7), .clk(clk), .clr(reset));  // open: carry
  or or_3 (clear, and_2_out, and_3_out);
  and and_2 (and_2_out, hit, MemRead);
  not not_2 (not_2_out, hit);
  and and_3 (and_3_out, not_2_out, MemRead, B_Enable);
  // Probe on out_7

  // Other names for the same wires on the sheet: B_en = B_Enable; G_en = G_Enable

  // Notes on the sheet:
  //   击中且读入
  //   未命中替换data
endmodule

module Group (
  input  [31:0] Data1,
  input  [31:0] Data2,
  input  [31:0] Data3,
  input  [31:0] Data4,
  input  [5:0] tag,
  input  clk,
  input  reset,
  input  enable,
  input  stop,
  input  MemRead,
  input  MemWrite,
  output Hit,
  output [31:0] out_13,
  output [31:0] out_14,
  output [31:0] out_15,
  output [31:0] out_16
);

  wire comparator_1_eq, comparator_2_eq, comparator_3_eq, comparator_4_eq, en1, en2, en3, en4, Enable_t,
       hit1, hit2, hit3, hit4, not_1_out, or_1_out, v1, v2, v3, v4;
  wire [1:0] multiplexer_1_out, multiplexer_2_out, multiplexer_3_out;
  wire [5:0] tag1, tag2, tag3, tag4;
  wire [15:0] count1, count2, count3, count4;
  wire [31:0] _1d1, _1d2, _1d3, _1d4, _2d1, _2d2, _2d3, _2d4, _3d1, _3d2, _3d3, _3d4, _4d1, _4d2, _4d3, _4d4;

  not not_1 (not_1_out, stop);
  and and_1 (Enable_t, enable, not_1_out);
  CacheBlock cacheblock_1 (
    .reset(reset), .tag(tag), .clk(clk), .enable(en1), .in_5(Data1), .in_6(Data2), .in_7(Data3),
    .in_8(Data4), .out_9(v1), .out_10(tag1), .out_11(_1d1), .out_12(_1d2), .out_13(_1d3), .out_14(_1d4));
  CacheBlock cacheblock_2 (
    .reset(reset), .tag(tag), .clk(clk), .enable(en2), .in_5(Data1), .in_6(Data2), .in_7(Data3),
    .in_8(Data4), .out_9(v2), .out_10(tag2), .out_11(_2d1), .out_12(_2d2), .out_13(_2d3), .out_14(_2d4));
  CacheBlock cacheblock_3 (
    .reset(reset), .tag(tag), .clk(clk), .enable(en3), .in_5(Data1), .in_6(Data2), .in_7(Data3),
    .in_8(Data4), .out_9(v3), .out_10(tag3), .out_11(_3d1), .out_12(_3d2), .out_13(_3d3), .out_14(_3d4));
  CacheBlock cacheblock_4 (
    .reset(reset), .tag(tag), .clk(clk), .enable(en4), .in_5(Data1), .in_6(Data2), .in_7(Data3),
    .in_8(Data4), .out_9(v4), .out_10(tag4), .out_11(_4d1), .out_12(_4d2), .out_13(_4d3), .out_14(_4d4));
  LRU lru_1 (
    .count1(count1), .count2(count2), .count3(count3), .count4(count4), .hit1(hit1), .hit2(hit2),
    .hit3(hit3), .hit4(hit4), .MemRead(MemRead), .MemWrite(MemWrite), .Enable(Enable_t), .Write1(en1),
    .Write1_2(en2), .Write3(en3), .Write4(en4));
  Comparator #(.width(6)) comparator_1 (.a(tag1), .b(tag), .eq(comparator_1_eq));  // open: gt, lt
  Comparator #(.width(6)) comparator_2 (.a(tag2), .b(tag), .eq(comparator_2_eq));  // open: gt, lt
  Comparator #(.width(6)) comparator_3 (.a(tag3), .b(tag), .eq(comparator_3_eq));  // open: gt, lt
  Comparator #(.width(6)) comparator_4 (.a(tag4), .b(tag), .eq(comparator_4_eq));  // open: gt, lt
  and and_2 (hit1, v1, enable, comparator_1_eq);
  and and_3 (hit2, v2, enable, comparator_2_eq);
  and and_4 (hit3, v3, enable, comparator_3_eq);
  and and_5 (hit4, v4, enable, comparator_4_eq);
  Multiplexer #(.width(2), .enable("false")) multiplexer_1 (
    .in0(2'b00), .in1(2'b01), .out(multiplexer_1_out), .sel(hit2));
  Multiplexer #(.width(2), .enable("false")) multiplexer_2 (
    .in0(multiplexer_1_out), .in1(2'b10), .out(multiplexer_2_out), .sel(hit3));
  Multiplexer #(.width(2), .enable("false")) multiplexer_3 (
    .in0(multiplexer_2_out), .in1(2'b11), .out(multiplexer_3_out), .sel(hit4));
  Counter counter_1 (
    .clk(clk), .reset(reset), .MemRead(MemRead), .hit(hit1), .B_Enable(en1), .G_Enable(Enable_t),
    .out_7(count1));
  Counter counter_2 (
    .clk(clk), .reset(reset), .MemRead(MemRead), .hit(hit2), .B_Enable(en2), .G_Enable(Enable_t),
    .out_7(count2));
  Counter counter_3 (
    .clk(clk), .reset(reset), .MemRead(MemRead), .hit(hit3), .B_Enable(en3), .G_Enable(Enable_t),
    .out_7(count3));
  Counter counter_4 (
    .clk(clk), .reset(reset), .MemRead(MemRead), .hit(hit4), .B_Enable(en4), .G_Enable(Enable_t),
    .out_7(count4));
  or or_1 (or_1_out, hit1, hit2, hit3, hit4);
  and and_6 (Hit, or_1_out, enable);
  Multiplexer #(.select(2), .width(32)) multiplexer_4 (
    .in0(_1d1), .in1(_2d1), .in2(_3d1), .in3(_4d1), .out(out_13), .sel(multiplexer_3_out));  // open: en
  Multiplexer #(.select(2), .width(32)) multiplexer_5 (
    .in0(_1d2), .in1(_2d2), .in2(_3d2), .in3(_4d2), .out(out_14), .sel(multiplexer_3_out));  // open: en
  Multiplexer #(.select(2), .width(32)) multiplexer_6 (
    .in0(_1d3), .in1(_2d3), .in2(_3d3), .in3(_4d3), .out(out_15), .sel(multiplexer_3_out));  // open: en
  Multiplexer #(.select(2), .width(32)) multiplexer_7 (
    .in0(_1d4), .in1(_2d4), .in2(_3d4), .in3(_4d4), .out(out_16), .sel(multiplexer_3_out));  // open: en

  // Other names for the same wires on the sheet: en = enable

  // Notes on the sheet:
  //   MuxForBlock
endmodule
