// Logisim project LRU_test1.circ as structural Verilog: 1 circuit, main circuit LRU
module LRU (
  input  [15:0] count1,
  input  [15:0] count2,
  input  [15:0] count3,
  input  [15:0] count4,
  input  hit1,
  input  hit2,
  input  hit3,
  input  hit4,
  input  MemRead,
  input  MemWrite,
  input  Enable,
  output Write1,
  output Write1_2,
  output Write3,
  output Write4
);

  wire and_2_out, and_3_out, and_4_out, and_5_out, comparator_1_lt, comparator_2_lt, comparator_3_lt,
       decoder_1_out0, decoder_1_out1, decoder_1_out2, decoder_1_out3, multiplexer_6_out, multiplexer_7_out,
       multiplexer_8_out, multiplexer_9_out, NhNw, nor_1_out, not_1_out, or_1_out, or_2_out, or_3_out,
       or_4_out;
  wire [1:0] cmp, cmp1, cmp2;
  wire [15:0] multiplexer_3_out, multiplexer_4_out;

  Comparator #(.width(16)) comparator_1 (.a(count1), .b(count2), .lt(comparator_1_lt));  // open: gt, eq
  Comparator #(.width(16)) comparator_2 (.a(count3), .b(count4), .lt(comparator_2_lt));  // open: gt, eq
  Multiplexer #(.width(2), .enable("false")) multiplexer_1 (
    .in0(2'b00), .in1(2'b01), .out(cmp1), .sel(comparator_1_lt));
  Multiplexer #(.width(2), .enable("false")) multiplexer_2 (
    .in0(2'b10), .in1(2'b11), .out(cmp2), .sel(comparator_2_lt));
  nor nor_1 (nor_1_out, hit1, hit2, hit3, hit4);
  not not_1 (not_1_out, MemWrite);
  and and_1 (NhNw, nor_1_out, not_1_out);
  and and_2 (and_2_out, hit1, MemWrite);
  and and_3 (and_3_out, hit2, MemWrite);
  and and_4 (and_4_out, hit3, MemWrite);
  and and_5 (and_5_out, hit4, MemWrite);
  Multiplexer #(.select(2), .width(16), .enable("false")) multiplexer_3 (
    .in0(count1), .in1(count2), .in2({16{1'b0}}), .in3({16{1'b0}}), .out(multiplexer_3_out), .sel(cmp1));
  Multiplexer #(.select(2), .width(16), .enable("false")) multiplexer_4 (
    .in0({16{1'b0}}), .in1({16{1'b0}}), .in2(count3), .in3(count4), .out(multiplexer_4_out), .sel(cmp2));
  Decoder #(.select(2)) decoder_1 (
    .out0(decoder_1_out0), .out1(decoder_1_out1), .out2(decoder_1_out2), .out3(decoder_1_out3), .sel(cmp));  // open: en
  Comparator #(.width(16)) comparator_3 (
    .a(multiplexer_3_out), .b(multiplexer_4_out), .lt(comparator_3_lt));  // open: gt, eq
  Multiplexer #(.width(2), .enable("false")) multiplexer_5 (.in0(cmp1), .in1(cmp2), .out(cmp), .sel(comparator_3_lt));
  Multiplexer #(.enable("false")) multiplexer_6 (.in0(1'b0), .in1(decoder_1_out0), .out(multiplexer_6_out), .sel(NhNw));
  Multiplexer #(.enable("false")) multiplexer_7 (.in0(1'b0), .in1(decoder_1_out1), .out(multiplexer_7_out), .sel(NhNw));
  Multiplexer #(.enable("false")) multiplexer_8 (.in0(1'b0), .in1(decoder_1_out2), .out(multiplexer_8_out), .sel(NhNw));
  Multiplexer #(.enable("false")) multiplexer_9 (.in0(1'b0), .in1(decoder_1_out3), .out(multiplexer_9_out), .sel(NhNw));
  or or_1 (or_1_out, multiplexer_6_out, 1'b0, and_2_out);
  or or_2 (or_2_out, multiplexer_7_out, 1'b0, and_3_out);
  or or_3 (or_3_out, multiplexer_8_out, 1'b0, and_4_out);
  or or_4 (or_4_out, multiplexer_9_out, 1'b0, and_5_out);
  and and_6 (Write1, Enable, or_1_out);
  and and_7 (Write1_2, Enable, or_2_out);
  and and_8 (Write3, Enable, or_3_out);
  and and_9 (Write4, Enable, or_4_out);

  // Other names for the same wires on the sheet: cnt1[15:0] = count1; cnt2[15:0] = count2; cnt3[15:0] = count3;
  //   cnt4[15:0] = count4; en = Enable
endmodule
